// Logisim project MCU.circ as structural Verilog: 10 circuits, main circuit MCU
module local_test (
  input  in_1,
  input  [1:0] in_2,
  input  in_3,
  input  [1:0] in_4,
  input  in_5,
  input  [5:0] in_6,
  input  in_7,
  input  in_8,
  input  [1:0] in_9,
  input  [3:0] in_10,
  input  [10:0] in_11
);

  wire and_1_out, and_2_out, basic_controller_1_call_cdm, basic_controller_1_check_speciality,
       basic_controller_1_enter, basic_controller_1_error, basic_controller_1_merge,
       basic_controller_1_pc_active, basic_controller_1_pc_allow_nearby, basic_controller_1_pc_free_mode,
       basic_controller_1_req_kbd, basic_controller_1_req_kbd_num, clock_1_out, clock_2_out,
       demultiplexer_1_out0, demultiplexer_1_out1, demultiplexer_1_out2, demultiplexer_1_out3,
       field_cahce_1_p31, input_controller_1_active_led, input_controller_1_data_ready,
       input_controller_1_error_led, input_controller_1_kbd_clear, input_controller_1_kbd_clock,
       input_controller_1_kbd_en, input_controller_1_user_action_led, keyboard_1_avail,
       move_checker_1_is_wrong, not_1_out, not_2_out, not_3_out, not_4_out, not_5_out, or_1_out, or_2_out,
       pointer_controller_1_err, pointer_controller_1_ready, position_checker_1_out, pull_resistor_1_node,
       spi_module_cell_1_input_transanction_end, spi_module_cell_1_is_selected, spi_module_cell_1_move_end_1,
       spi_module_cell_1_move_end_2, spi_module_cell_1_output_transanction_end, spi_module_cell_1_task_conf,
       spi_module_master_1_clk, spi_module_master_1_communication_end,
       spi_module_master_1_input_transanction_end, spi_module_master_1_mosi,
       spi_module_master_1_output_transanction_end;
  wire [1:0] input_controller_1_cursor_position, multiplexer_1_out, spi_module_cell_1_is_task,
       spi_module_cell_1_player_select_out, spi_module_cell_1_type_select_out;
  wire [3:0] input_shifter_1_buffer_ptr, input_shifter_2_buffer_ptr;
  wire [4:0] spi_module_cell_1_command;
  wire [6:0] input_controller_1_input_buffer_2, input_controller_1_input_buffer_3, keyboard_1_data;
  wire [7:0] basic_controller_1_spi_control, field_cahce_1_p20, field_cahce_1_p21, field_cahce_1_p22,
       field_cahce_1_p23, field_cahce_1_p24, field_cahce_1_p25, field_cahce_1_p26, field_cahce_1_p27,
       pointer_controller_1_csc, pointer_controller_1_csr;
  wire [8:0] field_cahce_1_p12, field_cahce_1_p13, field_cahce_1_p14, field_cahce_1_p15, field_cahce_1_p16,
       field_cahce_1_p17, field_cahce_1_p18, field_cahce_1_p19;
  wire [9:0] field_cahce_1_p3, field_cahce_1_p4, field_cahce_1_p5, field_cahce_1_p6, field_cahce_1_p7,
       field_cahce_1_p8, field_cahce_1_p9, field_cahce_1_p10;
  wire [10:0] spi_module_cell_1_energy_out;
  wire [13:0] input_controller_1_input_buffer;
  wire [15:0] controlled_buffer_1_out, input_controller_1_command_parsed_from_user_input,
       input_shifter_1_data_out, input_shifter_2_data_out, or_3_out, register_1_q,
       spi_module_master_1_recv_data;
  wire [31:0] field_cahce_1_p29, field_cahce_1_p30;

  assign controlled_buffer_1_out = not_1_out ? input_controller_1_command_parsed_from_user_input : 16'bz;  // Controlled_Buffer controlled_buffer_1
  not not_1 (not_1_out, basic_controller_1_merge);
  assign controlled_buffer_1_out = basic_controller_1_merge ? or_3_out : 16'bz;  // Controlled_Buffer controlled_buffer_2
  or or_1 (or_1_out, spi_module_master_1_input_transanction_end, in_3);
  or or_2 (or_2_out, and_1_out, and_2_out);
  assign or_3_out = register_1_q | input_controller_1_command_parsed_from_user_input;  // OR_Gate or_3, 16 bits wide
  Register #(.width(16), .trigger("falling")) register_1 (
    .D(controlled_buffer_1_out), .en(1'b1), .Q(register_1_q), .clk(or_2_out), .clr(or_1_out));
  // Probe on register_1_q[4:0]
  // Probe on basic_controller_1_spi_control
  Clock clock_1 (.out(clock_1_out));
  LED led_1 (.in(spi_module_master_1_input_transanction_end));
  LED led_2 (.in(spi_module_master_1_output_transanction_end));
  and and_1 (and_1_out, basic_controller_1_req_kbd, not_3_out);
  and and_2 (and_2_out, basic_controller_1_merge, not_2_out);
  not not_2 (not_2_out, basic_controller_1_merge);
  Clock clock_2 (.out(clock_2_out));
  // Probe on register_1_q[15:5]
  // Probe on spi_module_master_1_recv_data
  SPI_module__master spi_module_master_1 (
    .In_clock(clock_1_out), .MISO(pull_resistor_1_node), .CLK(spi_module_master_1_clk),
    .MOSI(spi_module_master_1_mosi), .Output_transanction_end(spi_module_master_1_output_transanction_end),
    .Input_transanction_end(spi_module_master_1_input_transanction_end),
    .Control_command(basic_controller_1_spi_control), .Send_command(register_1_q[4:0]),
    .Send_energy(register_1_q[15:5]), .Recv_data(spi_module_master_1_recv_data),
    .Communication_end(spi_module_master_1_communication_end));
  Pull_Resistor pull_resistor_1 (.node(pull_resistor_1_node));
  LED led_3 (.in(spi_module_master_1_communication_end));
  LED led_4 (.in(basic_controller_1_req_kbd));
  not not_3 (not_3_out, basic_controller_1_req_kbd_num);
  LED led_5 (.in(basic_controller_1_enter));
  LED led_6 (.in(basic_controller_1_call_cdm));
  not not_4 (not_4_out, in_7);
  input_shifter input_shifter_1 (
    .MOSI(pull_resistor_1_node), .CLK(spi_module_master_1_clk), .Reset(not_5_out),
    .Data_out(input_shifter_1_data_out), .buffer_ptr(input_shifter_1_buffer_ptr));
  not not_5 (not_5_out, in_7);
  Keyboard #(.buflen(5)) keyboard_1 (
    .clk(input_controller_1_kbd_clock), .re(input_controller_1_kbd_en), .clr(input_controller_1_kbd_clear),
    .avail(keyboard_1_avail), .data(keyboard_1_data));
  input_controller input_controller_1 (
    .Signed_number_parsed_from_user_input(input_controller_1_command_parsed_from_user_input[15:5]),
    .Command_parsed_from_user_input(input_controller_1_command_parsed_from_user_input[4:0]),
    .KBD_clock(input_controller_1_kbd_clock), .KBD_clear(input_controller_1_kbd_clear),
    .KBD_available(keyboard_1_avail), .KBD_buffer(keyboard_1_data), .KBD_en(input_controller_1_kbd_en),
    .Enabled__clears_buffer_on_rising_edge(basic_controller_1_req_kbd),
    .Active_LED(input_controller_1_active_led), .Request_number(basic_controller_1_req_kbd_num),
    .User_action_LED(input_controller_1_user_action_led), .Error_LED(input_controller_1_error_led),
    .Data_ready(input_controller_1_data_ready),
    .input_buffer({input_controller_1_input_buffer_3, input_controller_1_input_buffer_2, input_controller_1_input_buffer}),
    .Cursor_position(input_controller_1_cursor_position), .CLK(clock_2_out));
  LED led_7 (.in(input_controller_1_user_action_led));
  LED led_8 (.in(input_controller_1_active_led));
  LED led_9 (.in(basic_controller_1_req_kbd_num));
  LED led_10 (.in(basic_controller_1_merge));
  basic_controller basic_controller_1 (
    .Merge(basic_controller_1_merge), .PC_ready(pointer_controller_1_ready), .Active(in_1),
    .Is_special(position_checker_1_out), .Call_CDM(basic_controller_1_call_cdm), .Mode(in_2),
    .Wrong_move(move_checker_1_is_wrong), .CLK(clock_2_out), .SPI_error(spi_module_master_1_recv_data[0]),
    .PC_active(basic_controller_1_pc_active), .Check_speciality(basic_controller_1_check_speciality),
    .PC_free_mode(basic_controller_1_pc_free_mode), .PC_allow_nearby(basic_controller_1_pc_allow_nearby),
    .SPI_done(spi_module_master_1_communication_end), .SPI_control(basic_controller_1_spi_control),
    .Enter(basic_controller_1_enter), .Req_KBD(basic_controller_1_req_kbd),
    .Req_KBD_num(basic_controller_1_req_kbd_num),
    .KBD_command(input_controller_1_command_parsed_from_user_input[4:0]),
    .KBD_ready(input_controller_1_data_ready), .Error(basic_controller_1_error));
  LED led_11 (.in(basic_controller_1_error));
  // Probe on input_shifter_2_buffer_ptr
  input_shifter input_shifter_2 (
    .MOSI(spi_module_master_1_mosi), .CLK(spi_module_master_1_clk), .Reset(not_4_out),
    .Data_out(input_shifter_2_data_out), .buffer_ptr(input_shifter_2_buffer_ptr));
  // Probe on input_shifter_2_data_out
  // Probe on input_shifter_1_data_out
  // Probe on input_shifter_1_buffer_ptr
  LED led_12 (.in(demultiplexer_1_out3));
  // Probe on input_controller_1_input_buffer_3
  LED led_13 (.in(input_controller_1_error_led));
  DotMatrix #(.inputtype("row"), .matrixcols(9), .matrixrows(8)) dotmatrix_1 (
    .row0(field_cahce_1_p12), .row1(field_cahce_1_p13), .row2(field_cahce_1_p14), .row3(field_cahce_1_p15),
    .row4(field_cahce_1_p16), .row5(field_cahce_1_p17), .row6(field_cahce_1_p18), .row7(field_cahce_1_p19));
  DotMatrix #(.inputtype("row"), .matrixcols(10), .matrixrows(8), .dotshape("circle")) dotmatrix_2 (
    .row0(field_cahce_1_p3), .row1(field_cahce_1_p4), .row2(field_cahce_1_p5), .row3(field_cahce_1_p6),
    .row4(field_cahce_1_p7), .row5(field_cahce_1_p8), .row6(field_cahce_1_p9), .row7(field_cahce_1_p10));
  LED led_14 (.in(spi_module_cell_1_output_transanction_end));
  // Probe on spi_module_cell_1_player_select_out
  LED led_15 (.in(demultiplexer_1_out2));
  // Probe on input_controller_1_input_buffer_2
  Multiplexer #(.width(2), .disabled(0), .enable("false")) multiplexer_1 (
    .in0(in_4), .in1(2'b11), .out(multiplexer_1_out), .sel(basic_controller_1_check_speciality));
  // Field_cahce field_cahce_1: pin names not known; wires that end beside it: in_3, in_5, field_cahce_1_p3, field_cahce_1_p4, field_cahce_1_p5, field_cahce_1_p6, field_cahce_1_p7, field_cahce_1_p8, field_cahce_1_p9, field_cahce_1_p10, in_6, field_cahce_1_p12, field_cahce_1_p13, field_cahce_1_p14, field_cahce_1_p15, field_cahce_1_p16, field_cahce_1_p17, field_cahce_1_p18, field_cahce_1_p19, field_cahce_1_p20, field_cahce_1_p21, field_cahce_1_p22, field_cahce_1_p23, field_cahce_1_p24, field_cahce_1_p25, field_cahce_1_p26, field_cahce_1_p27, multiplexer_1_out, field_cahce_1_p29, field_cahce_1_p30, field_cahce_1_p31
  DotMatrix #(.inputtype("row"), .matrixcols(8), .matrixrows(8)) dotmatrix_3 (
    .row0(field_cahce_1_p20), .row1(field_cahce_1_p21), .row2(field_cahce_1_p22), .row3(field_cahce_1_p23),
    .row4(field_cahce_1_p24), .row5(field_cahce_1_p25), .row6(field_cahce_1_p26), .row7(field_cahce_1_p27));
  SPI_module__cell spi_module_cell_1 (
    .CS(in_7), .CLK(spi_module_master_1_clk), .MOSI(spi_module_master_1_mosi), .err(in_8), .energy_in(in_11),
    .type_select_in(in_10), .player_select_in(in_9), .clk_out(field_cahce_1_p31),
    .is_selected(spi_module_cell_1_is_selected), .move_end_1(spi_module_cell_1_move_end_1),
    .move_end_2(spi_module_cell_1_move_end_2), .is_task(spi_module_cell_1_is_task),
    .task_conf(spi_module_cell_1_task_conf), .command(spi_module_cell_1_command),
    .energy_out(spi_module_cell_1_energy_out),
    .input_transanction_end(spi_module_cell_1_input_transanction_end),
    .type_select_out(spi_module_cell_1_type_select_out),
    .player_select_out(spi_module_cell_1_player_select_out), .MISO(pull_resistor_1_node),
    .output_transanction_end(spi_module_cell_1_output_transanction_end));
  LED led_16 (.in(spi_module_cell_1_input_transanction_end));
  // Probe on spi_module_cell_1_command
  // Probe on spi_module_cell_1_type_select_out
  // Probe on spi_module_cell_1_energy_out
  Demultiplexer #(.select(2), .enable("false")) demultiplexer_1 (
    .out0(demultiplexer_1_out0), .out1(demultiplexer_1_out1), .out2(demultiplexer_1_out2),
    .out3(demultiplexer_1_out3), .in(1'b1), .sel(input_controller_1_cursor_position));
  LED led_17 (.in(demultiplexer_1_out1));
  // Probe on input_controller_1_input_buffer[13:7]
  pointer_controller pointer_controller_1 (
    .Active(basic_controller_1_pc_active), .CLK(clock_2_out), .RST(in_3), .Field_state_1(field_cahce_1_p29),
    .Field_state_2(field_cahce_1_p30), .Free_mode(basic_controller_1_pc_free_mode),
    .CSC(pointer_controller_1_csc), .CSR(pointer_controller_1_csr), .Err(pointer_controller_1_err),
    .Ready(pointer_controller_1_ready), .KBD_command(input_controller_1_command_parsed_from_user_input[4:0]),
    .Allow_nearby(basic_controller_1_pc_allow_nearby));
  LED led_18 (.in(pointer_controller_1_err));
  LED led_19 (.in(spi_module_cell_1_is_selected));
  LED led_20 (.in(spi_module_cell_1_move_end_1));
  LED led_21 (.in(spi_module_cell_1_move_end_2));
  LED led_22 (.in(spi_module_cell_1_task_conf));
  LED led_23 (.in(demultiplexer_1_out0));
  // Probe on input_controller_1_input_buffer[6:0]
  // Probe on pointer_controller_1_csc
  LED led_24 (.in(pointer_controller_1_ready));
  position_checker position_checker_1 (
    .CSc(pointer_controller_1_csc), .CSR(pointer_controller_1_csr), .Field_input_1(field_cahce_1_p29),
    .Field_input_2(field_cahce_1_p30), .Out(position_checker_1_out));
  // Probe on spi_module_cell_1_is_task
  move_checker move_checker_1 (
    .CSC(pointer_controller_1_csc), .CSR(pointer_controller_1_csr), .Is_wrong(move_checker_1_is_wrong),
    .KBD_command(input_controller_1_command_parsed_from_user_input[4:0]));
  // Probe on pointer_controller_1_csr
  // DotMatrix #(.inputtype("select"), .matrixcols(8), .matrixrows(8)) dotmatrix_4: pin names not known; wires that end beside it: pointer_controller_1_csc
endmodule

module MCU (
  input  [4:0] KBD_command,
  input  [10:0] KBD_energy_increment,
  input  KBD_Ready,
  input  Reset,
  input  CLK,
  input  MISO,
  input  SPI_busy,
  output Request_KBD,
  output Request_KBD_energy,
  output [7:0] Cell_CSC,
  output [7:0] Cell_CSR,
  output [2:0] Table_CSC,
  output [5:0] Table_CSR,
  output Task_CS,
  output SPI_clock,
  output MOSI,
  output [7:0] Debug_out,
  output Waiting_IO,
  output SPI_communication_in_progress
);

  wire and_1_out, and_2_out, and_3_out, and_4_out, and_5_out, and_6_out, and_7_out, and_8_out, and_10_out,
       and_11_out, cdm_8_1_data_code_prime, cdm_8_1_load_st_prime, cdm_8_1_mem, d_ff_1_q, Data,
       decoder_1_out0, io_dmx_1_bc_control, io_dmx_1_cell_csr, io_dmx_1_debug_output,
       io_dmx_1_spi_kbd_control, io_dmx_1_table__csc__csr____task_cs, io_dmx_1_universal_io_1,
       io_dmx_1_universal_io_2, not_1_out, or_1_out, or_2_out, or_3_out, or_5_out,
       spi_module_master_1_communication_end, spi_module_master_1_input_transanction_end,
       spi_module_master_1_output_transanction_end;
  wire [6:0] demultiplexer_2_out0, demultiplexer_2_out1, register_4_q;
  wire [6:3] register_3_q;
  wire [7:0] cdm_8_1_addr, cdm_8_1_data_out, cdm_8_1_pc, cdm_8_1_ps, cdm_8_1_r0, cdm_8_1_r1, cdm_8_1_r2,
       cdm_8_1_r3, cdm_8_1_sp, controlled_buffer_1_out, controlled_buffer_2_out, controlled_buffer_4_out,
       controlled_buffer_6_out, register_5_q, register_6_q;
  wire [15:0] spi_module_master_1_recv_data;

  // Probe on cdm_8_1_r0
  // Probe on cdm_8_1_r0
  // Probe on cdm_8_1_r0
  // Probe on cdm_8_1_ps[7]
  // Probe on cdm_8_1_ps[6:4]
  // Probe on cdm_8_1_pc
  // Probe on cdm_8_1_r1
  // Probe on cdm_8_1_r0
  // Probe on cdm_8_1_ps[3]
  // Probe on cdm_8_1_ps[2]
  // Probe on cdm_8_1_r1
  // Probe on cdm_8_1_r1
  // Probe on cdm_8_1_r1
  // Probe on cdm_8_1_ps[1]
  // Probe on cdm_8_1_ps[0]
  // Probe on cdm_8_1_r2
  // Probe on cdm_8_1_r2
  // Probe on cdm_8_1_r2
  // Probe on cdm_8_1_r2
  // Probe on cdm_8_1_sp
  // Probe on cdm_8_1_r3
  // Probe on cdm_8_1_r3
  and and_1 (and_1_out, CLK, ~Waiting_IO);  // AND_Gate
  // Probe on cdm_8_1_r3
  // Probe on cdm_8_1_r3
  CdM_8 cdm_8_1 (
    .data_code_prime(cdm_8_1_data_code_prime), .R0(cdm_8_1_r0), .R1(cdm_8_1_r1), .mem(cdm_8_1_mem),
    .R2(cdm_8_1_r2), .load_st_prime(cdm_8_1_load_st_prime), .R3(cdm_8_1_r3), .addr(cdm_8_1_addr),
    .PC(cdm_8_1_pc), .SP(cdm_8_1_sp), .data_out(cdm_8_1_data_out), .data_in(controlled_buffer_2_out),
    .PS(cdm_8_1_ps), .clk(and_1_out), .rset(Reset));  // open: page, IAck, IRQ, vector, shadow
  Decoder #(.disabled(0)) decoder_1 (
    .out0(decoder_1_out0), .out1(Data), .sel(cdm_8_1_data_code_prime), .en(cdm_8_1_mem));
  assign controlled_buffer_1_out = not_1_out ? cdm_8_1_data_out : 8'bz;  // Controlled_Buffer controlled_buffer_1
  not not_1 (not_1_out, cdm_8_1_load_st_prime);
  assign controlled_buffer_2_out = cdm_8_1_load_st_prime ? controlled_buffer_1_out : 8'bz;  // Controlled_Buffer controlled_buffer_2
  and and_2 (and_2_out, ~controlled_buffer_1_out[0], Data);  // AND_Gate
  IO_dmx io_dmx_1 (
    .Address(cdm_8_1_addr), .Is_IO(controlled_buffer_1_out[0]), .Cell_CSC(controlled_buffer_1_out[0]),
    .Cell_CSR(io_dmx_1_cell_csr), .Table__CSC__CSR____Task_CS(io_dmx_1_table__csc__csr____task_cs),
    .SPI_KBD_control(io_dmx_1_spi_kbd_control), .Universal_IO_1(io_dmx_1_universal_io_1),
    .Universal_IO_2(io_dmx_1_universal_io_2), .Debug_output(io_dmx_1_debug_output), .Selected(Data),
    .BC_control(io_dmx_1_bc_control));
  ROM rom_1 (.addr(cdm_8_1_addr), .data(controlled_buffer_1_out), .sel(decoder_1_out0));
  RAM ram_1 (
    .addr(cdm_8_1_addr), .data(controlled_buffer_1_out), .sel(and_2_out), .clk(CLK),
    .ld(cdm_8_1_load_st_prime), .clr(Reset));
  and and_3 (and_3_out, controlled_buffer_1_out[0], ~cdm_8_1_load_st_prime, io_dmx_1_universal_io_1);  // AND_Gate
  or or_1 (or_1_out, io_dmx_1_universal_io_1, spi_module_master_1_communication_end, and_11_out);
  and and_4 (and_4_out, controlled_buffer_1_out[0], ~cdm_8_1_load_st_prime, io_dmx_1_universal_io_2);  // AND_Gate
  or or_2 (or_2_out, io_dmx_1_universal_io_2, spi_module_master_1_communication_end, and_11_out);
  Register #(.trigger("falling")) register_1 (
    .D(controlled_buffer_1_out), .en(io_dmx_1_cell_csr), .Q(Cell_CSC), .clk(CLK), .clr(Reset));
  Register #(.trigger("falling")) register_2 (
    .D(controlled_buffer_1_out), .en(io_dmx_1_table__csc__csr____task_cs), .Q(Cell_CSR), .clk(CLK),
    .clr(Reset));
  Register #(.trigger("falling")) register_3 (
    .D(controlled_buffer_1_out), .en(io_dmx_1_bc_control), .Q({Task_CS, register_3_q, Table_CSC}), .clk(CLK),
    .clr(Reset));
  Register #(.trigger("falling")) register_4 (
    .D(controlled_buffer_1_out), .en(io_dmx_1_spi_kbd_control), .Q({Request_KBD, register_4_q}), .clk(CLK),
    .clr(or_3_out));
  and and_5 (and_5_out, controlled_buffer_1_out[0], cdm_8_1_load_st_prime, io_dmx_1_universal_io_1);
  assign controlled_buffer_1_out = and_5_out ? register_5_q : 8'bz;  // Controlled_Buffer controlled_buffer_3
  Register #(.trigger("falling")) register_5 (
    .D(controlled_buffer_4_out), .en(or_1_out), .Q(register_5_q), .clk(CLK), .clr(Reset));
  assign controlled_buffer_4_out = and_3_out ? controlled_buffer_1_out : 8'bz;  // Controlled_Buffer controlled_buffer_4
  and and_6 (and_6_out, controlled_buffer_1_out[0], io_dmx_1_universal_io_2, cdm_8_1_load_st_prime);
  assign controlled_buffer_1_out = and_6_out ? register_6_q : 8'bz;  // Controlled_Buffer controlled_buffer_5
  assign controlled_buffer_6_out = and_4_out ? controlled_buffer_1_out : 8'bz;  // Controlled_Buffer controlled_buffer_6
  Register #(.trigger("falling")) register_6 (
    .D(controlled_buffer_6_out), .en(or_2_out), .Q(register_6_q), .clk(CLK), .clr(Reset));
  Register #(.trigger("falling")) register_7 (
    .D(controlled_buffer_1_out), .en(io_dmx_1_debug_output), .Q(Debug_out), .clk(CLK), .clr(Reset));
  Demultiplexer #(.width(3), .disabled(0), .enable("false")) demultiplexer_1 (
    .out0(Table_CSR[2:0]), .out1(Table_CSR[5:3]), .in(register_3_q[5:3]), .sel(register_3_q[6]));
  Demultiplexer #(.width(7), .disabled(0), .enable("false")) demultiplexer_2 (
    .out0(demultiplexer_2_out0), .out1(demultiplexer_2_out1), .in(register_4_q), .sel(Request_KBD));
  or or_3 (or_3_out, and_7_out, Reset);
  and and_7 (and_7_out, Waiting_IO, or_5_out, and_8_out);
  D_Flip_Flop d_ff_1 (.clk(CLK), .D(CLK), .Q(d_ff_1_q), .reset(and_8_out));  // open: Qn, preset, en
  or or_4 (Waiting_IO, Request_KBD, SPI_communication_in_progress);
  or or_5 (or_5_out, and_11_out, spi_module_master_1_communication_end);
  and and_8 (and_8_out, ~CLK, d_ff_1_q);  // AND_Gate
  or or_6 (SPI_communication_in_progress, demultiplexer_2_out0[6], demultiplexer_2_out0[5], demultiplexer_2_out0[4], demultiplexer_2_out0[3], demultiplexer_2_out0[2], demultiplexer_2_out0[1], demultiplexer_2_out0[0]);
  and and_9 (Request_KBD_energy, demultiplexer_2_out1[0], Request_KBD);
  Pull_Resistor pull_resistor_1 (.node(SPI_busy));
  assign {controlled_buffer_6_out, controlled_buffer_4_out} = and_11_out ? {KBD_energy_increment, KBD_command} : 16'bz;  // Controlled_Buffer controlled_buffer_7
  assign {controlled_buffer_6_out, controlled_buffer_4_out} = spi_module_master_1_communication_end ? spi_module_master_1_recv_data : 16'bz;  // Controlled_Buffer controlled_buffer_8
  and and_10 (and_10_out, CLK, SPI_communication_in_progress, ~SPI_busy);  // AND_Gate
  LED led_1 (.in(spi_module_master_1_input_transanction_end));
  SPI_module__master spi_module_master_1 (
    .In_clock(and_10_out), .MISO(MISO), .CLK(SPI_clock), .MOSI(MOSI),
    .Output_transanction_end(spi_module_master_1_output_transanction_end),
    .Input_transanction_end(spi_module_master_1_input_transanction_end),
    .Control_command({Request_KBD, register_4_q}), .Send_command(register_5_q[4:0]),
    .Send_energy({register_6_q, register_5_q[7:5]}), .Recv_data(spi_module_master_1_recv_data),
    .Communication_end(spi_module_master_1_communication_end));
  LED led_2 (.in(spi_module_master_1_output_transanction_end));
  LED led_3 (.in(spi_module_master_1_communication_end));
  and and_11 (and_11_out, Request_KBD, KBD_Ready);
  Pull_Resistor pull_resistor_2 (.node(MISO));
  // Pins of 1 and 8 bits meet at controlled_buffer_1_out

  // Other names for the same wires on the sheet: wait_KBD = Request_KBD; wait_IO = Waiting_IO;
  //   wait_SPI = SPI_communication_in_progress

  // Notes on the sheet:
  //   contents of rom_1 (hex, n*v repeats v):
  //   d0 f9 d1 ff a1 d0 ff d1 ff a1 88 a1 d0 fc d1 2e a1 d0 fb d1 10 a1 d0 fc d1 c a1 d0 f9 d1 0 a1 d0 ff
  //   d1 0 a1 88 a1 d0 ea d1 1 a1 d2 ff a9 88 a1 8a a9 d0 fc d1 26 a1 d0 fc d1 80 a1 d0 fb b1 d0 10 71 e1
  //   55 0 d0 f9 d1 18 a1 d0 e9 b1 9d a1 d0 fe a1 ee 33 d0 11 71 e1 6a 0 d0 f9 d1 3 a1 d0 ea b1 9d a1 d0
  //   ff a1 ee 33 d0 12 71 e1 82 0 d0 f9 d1 c0 a1 d0 ea b1 91 e3 7c 91 a1 d0 ff a1 ee 33 d0 13 71 e1 9a 0
  //   d0 f9 d1 24 a1 d0 e9 b1 91 e3 94 91 a1 d0 fe a1 ee 33 d0 8 71 e1 d7 d0 ff d1 0 a1 d2 ea b9 a1 d0 fc
  //   d1 2e a1 d0 f9 d1 42 a1 d0 fc d1 81 a1 d0 fb b1 d2 8 56 a2 d0 fc d1 4 a1 d0 fb b1 d0 f9 d2 d0 56 a2
  //   d0 ff d1 0 a1 d2 ea b9 a1 ee 33 d0 f9 d1 c3 a1 d1 0 d0 ff a1 d0 ea b1 d0 ff a1 ee 33
endmodule

module IO_dmx (
  input  [7:0] Address,
  input  Selected,
  output Is_IO,
  output Cell_CSC,
  output Cell_CSR,
  output Table__CSC__CSR____Task_CS,
  output SPI_KBD_control,
  output Universal_IO_1,
  output Universal_IO_2,
  output Debug_output,
  output BC_control
);

  wire [7:0] controlled_buffer_1_out;

  assign controlled_buffer_1_out = Selected ? Address : 8'bz;  // Controlled_Buffer controlled_buffer_1
  Pull_Resistor pull_resistor_1 (.node(controlled_buffer_1_out));
  Comparator comparator_1 (.a(controlled_buffer_1_out), .b({8{1'b1}}), .eq(Cell_CSC));  // open: gt, lt
  Comparator comparator_2 (.a(controlled_buffer_1_out), .b(8'hfe), .eq(Cell_CSR));  // open: gt, lt
  Comparator comparator_3 (.a(controlled_buffer_1_out), .b(8'hfd), .eq(Table__CSC__CSR____Task_CS));  // open: gt, lt
  Comparator comparator_4 (.a(controlled_buffer_1_out), .b(8'hfc), .eq(SPI_KBD_control));  // open: gt, lt
  Comparator comparator_5 (.a(controlled_buffer_1_out), .b(8'hfb), .eq(Universal_IO_1));  // open: gt, lt
  Comparator comparator_6 (.a(controlled_buffer_1_out), .b(8'hfa), .eq(Universal_IO_2));  // open: gt, lt
  Comparator comparator_7 (.a(controlled_buffer_1_out), .b(8'hf9), .eq(Debug_output));  // open: gt, lt
  Comparator comparator_8 (.a(controlled_buffer_1_out), .b(8'hf8), .eq(BC_control));  // open: gt, lt
  or or_1 (Is_IO, Cell_CSC, Cell_CSR, Table__CSC__CSR____Task_CS, SPI_KBD_control, Universal_IO_1, Universal_IO_2, Debug_output, BC_control);
endmodule

module Field_cahce (
  input  wr,
  input  [7:0] CSC,
  input  [7:0] CSR,
  input  RST,
  input  [1:0] p_sel,
  output [9:0] Task_row_1,
  output [8:0] p2_row_1,
  output [9:0] Task_row_2,
  output [8:0] p2_row_2,
  output [7:0] p1_row_1,
  output [31:0] DataO_1,
  output [31:0] DataO_2,
  output [7:0] p1_row_2,
  output [7:0] p1_row_3,
  output [8:0] p2_row_3,
  output [9:0] Task_row_3,
  output [7:0] p1_row_4,
  output [8:0] p2_row_4,
  output [9:0] Task_row_4,
  output [9:0] Task_row_5,
  output [8:0] p2_row_5,
  output [9:0] Task_row_6,
  output [7:0] p1_row_5,
  output [8:0] p2_row_6,
  output [7:0] p1_row_6,
  output [7:0] p1_row_7,
  output [7:0] p1_row_8,
  output [8:0] p2_row_7,
  output [9:0] Task_row_7,
  output [8:0] p2_row_8,
  output [9:0] Task_row_8
);

  wire decoder_1_out0, decoder_1_out1, decoder_1_out2, decoder_1_out3, or_3_out, or_4_out, or_5_out,
       or_8_out, or_9_out, or_12_out;
  wire [7:0] controlled_buffer_1_out, controlled_buffer_2_out, controlled_buffer_3_out,
       controlled_buffer_4_out, controlled_buffer_5_out, controlled_buffer_6_out, controlled_buffer_7_out,
       controlled_buffer_8_out;
  wire [31:0] and_1_out, and_2_out, and_3_out, and_4_out, and_5_out, and_6_out, multiplexer_1_out,
       multiplexer_2_out, multiplexer_3_out, multiplexer_4_out, multiplexer_5_out, multiplexer_6_out,
       or_1_out, or_2_out, or_6_out, or_7_out, or_10_out, or_11_out;

  assign controlled_buffer_1_out = CSR[0] ? CSC : 8'bz;  // Controlled_Buffer controlled_buffer_1
  assign controlled_buffer_2_out = CSR[1] ? CSC : 8'bz;  // Controlled_Buffer controlled_buffer_2
  assign controlled_buffer_3_out = CSR[2] ? CSC : 8'bz;  // Controlled_Buffer controlled_buffer_3
  assign controlled_buffer_4_out = CSR[3] ? CSC : 8'bz;  // Controlled_Buffer controlled_buffer_4
  assign controlled_buffer_5_out = CSR[4] ? CSC : 8'bz;  // Controlled_Buffer controlled_buffer_5
  assign controlled_buffer_6_out = CSR[5] ? CSC : 8'bz;  // Controlled_Buffer controlled_buffer_6
  assign controlled_buffer_7_out = CSR[6] ? CSC : 8'bz;  // Controlled_Buffer controlled_buffer_7
  assign controlled_buffer_8_out = CSR[7] ? CSC : 8'bz;  // Controlled_Buffer controlled_buffer_8
  Pull_Resistor pull_resistor_1 (.node(p_sel));
  Decoder #(.select(2), .disabled(0), .enable("false")) decoder_1 (
    .out0(decoder_1_out0), .out1(decoder_1_out1), .out2(decoder_1_out2), .out3(decoder_1_out3), .sel(p_sel));
  Multiplexer #(.width(32), .enable("false")) multiplexer_1 (
    .in0(or_1_out), .in1(and_1_out), .out(multiplexer_1_out), .sel(decoder_1_out0));
  Pull_Resistor pull_resistor_2 (.node({controlled_buffer_4_out, controlled_buffer_3_out, controlled_buffer_2_out, controlled_buffer_1_out}));
  assign or_1_out = {controlled_buffer_4_out, controlled_buffer_3_out, controlled_buffer_2_out, controlled_buffer_1_out} | {p1_row_4[0], p1_row_4[1], p1_row_4[2], p1_row_4[3], p1_row_4[4], p1_row_4[5], p1_row_4[6], p1_row_4[7], p1_row_3[0], p1_row_3[1], p1_row_3[2], p1_row_3[3], p1_row_3[4], p1_row_3[5], p1_row_3[6], p1_row_3[7], p1_row_2[0], p1_row_2[1], p1_row_2[2], p1_row_2[3], p1_row_2[4], p1_row_2[5], p1_row_2[6], p1_row_2[7], p1_row_1[0], p1_row_1[1], p1_row_1[2], p1_row_1[3], p1_row_1[4], p1_row_1[5], p1_row_1[6], p1_row_1[7]};  // OR_Gate or_1, 32 bits wide
  Pull_Resistor pull_resistor_3 (.node({controlled_buffer_8_out, controlled_buffer_7_out, controlled_buffer_6_out, controlled_buffer_5_out}));
  assign or_2_out = {controlled_buffer_8_out, controlled_buffer_7_out, controlled_buffer_6_out, controlled_buffer_5_out} | {p1_row_8[0], p1_row_8[1], p1_row_8[2], p1_row_8[3], p1_row_8[4], p1_row_8[5], p1_row_8[6], p1_row_8[7], p1_row_7[0], p1_row_7[1], p1_row_7[2], p1_row_7[3], p1_row_7[4], p1_row_7[5], p1_row_7[6], p1_row_7[7], p1_row_6[0], p1_row_6[1], p1_row_6[2], p1_row_6[3], p1_row_6[4], p1_row_6[5], p1_row_6[6], p1_row_6[7], p1_row_5[0], p1_row_5[1], p1_row_5[2], p1_row_5[3], p1_row_5[4], p1_row_5[5], p1_row_5[6], p1_row_5[7]};  // OR_Gate or_2, 32 bits wide
  assign DataO_1 = decoder_1_out1 ? {p1_row_4[0], p1_row_4[1], p1_row_4[2], p1_row_4[3], p1_row_4[4], p1_row_4[5], p1_row_4[6], p1_row_4[7], p1_row_3[0], p1_row_3[1], p1_row_3[2], p1_row_3[3], p1_row_3[4], p1_row_3[5], p1_row_3[6], p1_row_3[7], p1_row_2[0], p1_row_2[1], p1_row_2[2], p1_row_2[3], p1_row_2[4], p1_row_2[5], p1_row_2[6], p1_row_2[7], p1_row_1[0], p1_row_1[1], p1_row_1[2], p1_row_1[3], p1_row_1[4], p1_row_1[5], p1_row_1[6], p1_row_1[7]} : 32'bz;  // Controlled_Buffer controlled_buffer_9
  Register #(.width(32)) register_1 (
    .D(multiplexer_1_out), .en(or_3_out),
    .Q({p1_row_4[0], p1_row_4[1], p1_row_4[2], p1_row_4[3], p1_row_4[4], p1_row_4[5], p1_row_4[6], p1_row_4[7], p1_row_3[0], p1_row_3[1], p1_row_3[2], p1_row_3[3], p1_row_3[4], p1_row_3[5], p1_row_3[6], p1_row_3[7], p1_row_2[0], p1_row_2[1], p1_row_2[2], p1_row_2[3], p1_row_2[4], p1_row_2[5], p1_row_2[6], p1_row_2[7], p1_row_1[0], p1_row_1[1], p1_row_1[2], p1_row_1[3], p1_row_1[4], p1_row_1[5], p1_row_1[6], p1_row_1[7]}),
    .clk(wr), .clr(RST));
  or or_3 (or_3_out, decoder_1_out0, decoder_1_out1);
  assign and_1_out = ~{controlled_buffer_4_out, controlled_buffer_3_out, controlled_buffer_2_out, controlled_buffer_1_out} & {p1_row_4[0], p1_row_4[1], p1_row_4[2], p1_row_4[3], p1_row_4[4], p1_row_4[5], p1_row_4[6], p1_row_4[7], p1_row_3[0], p1_row_3[1], p1_row_3[2], p1_row_3[3], p1_row_3[4], p1_row_3[5], p1_row_3[6], p1_row_3[7], p1_row_2[0], p1_row_2[1], p1_row_2[2], p1_row_2[3], p1_row_2[4], p1_row_2[5], p1_row_2[6], p1_row_2[7], p1_row_1[0], p1_row_1[1], p1_row_1[2], p1_row_1[3], p1_row_1[4], p1_row_1[5], p1_row_1[6], p1_row_1[7]};  // AND_Gate and_1, 32 bits wide
  assign and_2_out = ~{controlled_buffer_8_out, controlled_buffer_7_out, controlled_buffer_6_out, controlled_buffer_5_out} & {p1_row_8[0], p1_row_8[1], p1_row_8[2], p1_row_8[3], p1_row_8[4], p1_row_8[5], p1_row_8[6], p1_row_8[7], p1_row_7[0], p1_row_7[1], p1_row_7[2], p1_row_7[3], p1_row_7[4], p1_row_7[5], p1_row_7[6], p1_row_7[7], p1_row_6[0], p1_row_6[1], p1_row_6[2], p1_row_6[3], p1_row_6[4], p1_row_6[5], p1_row_6[6], p1_row_6[7], p1_row_5[0], p1_row_5[1], p1_row_5[2], p1_row_5[3], p1_row_5[4], p1_row_5[5], p1_row_5[6], p1_row_5[7]};  // AND_Gate and_2, 32 bits wide
  Multiplexer #(.width(32), .enable("false")) multiplexer_2 (
    .in0(or_2_out), .in1(and_2_out), .out(multiplexer_2_out), .sel(decoder_1_out0));
  Register #(.width(32)) register_2 (
    .D(multiplexer_2_out), .en(or_4_out),
    .Q({p1_row_8[0], p1_row_8[1], p1_row_8[2], p1_row_8[3], p1_row_8[4], p1_row_8[5], p1_row_8[6], p1_row_8[7], p1_row_7[0], p1_row_7[1], p1_row_7[2], p1_row_7[3], p1_row_7[4], p1_row_7[5], p1_row_7[6], p1_row_7[7], p1_row_6[0], p1_row_6[1], p1_row_6[2], p1_row_6[3], p1_row_6[4], p1_row_6[5], p1_row_6[6], p1_row_6[7], p1_row_5[0], p1_row_5[1], p1_row_5[2], p1_row_5[3], p1_row_5[4], p1_row_5[5], p1_row_5[6], p1_row_5[7]}),
    .clk(wr), .clr(RST));
  or or_4 (or_4_out, decoder_1_out0, decoder_1_out1);
  assign DataO_2 = decoder_1_out1 ? {p1_row_8[0], p1_row_8[1], p1_row_8[2], p1_row_8[3], p1_row_8[4], p1_row_8[5], p1_row_8[6], p1_row_8[7], p1_row_7[0], p1_row_7[1], p1_row_7[2], p1_row_7[3], p1_row_7[4], p1_row_7[5], p1_row_7[6], p1_row_7[7], p1_row_6[0], p1_row_6[1], p1_row_6[2], p1_row_6[3], p1_row_6[4], p1_row_6[5], p1_row_6[6], p1_row_6[7], p1_row_5[0], p1_row_5[1], p1_row_5[2], p1_row_5[3], p1_row_5[4], p1_row_5[5], p1_row_5[6], p1_row_5[7]} : 32'bz;  // Controlled_Buffer controlled_buffer_10
  Register #(.width(32)) register_3 (
    .D(multiplexer_3_out), .en(or_5_out),
    .Q({p2_row_4[0], p2_row_4[1], p2_row_4[2], p2_row_4[3], p2_row_4[4], p2_row_4[5], p2_row_4[6], p2_row_4[7], p2_row_3[0], p2_row_3[1], p2_row_3[2], p2_row_3[3], p2_row_3[4], p2_row_3[5], p2_row_3[6], p2_row_3[7], p2_row_2[0], p2_row_2[1], p2_row_2[2], p2_row_2[3], p2_row_2[4], p2_row_2[5], p2_row_2[6], p2_row_2[7], p2_row_1[0], p2_row_1[1], p2_row_1[2], p2_row_1[3], p2_row_1[4], p2_row_1[5], p2_row_1[6], p2_row_1[7]}),
    .clk(wr), .clr(RST));
  or or_5 (or_5_out, decoder_1_out0, decoder_1_out2);
  Multiplexer #(.width(32), .enable("false")) multiplexer_3 (
    .in0(or_6_out), .in1(and_3_out), .out(multiplexer_3_out), .sel(decoder_1_out0));
  assign and_3_out = ~{controlled_buffer_4_out, controlled_buffer_3_out, controlled_buffer_2_out, controlled_buffer_1_out} & {p2_row_4[0], p2_row_4[1], p2_row_4[2], p2_row_4[3], p2_row_4[4], p2_row_4[5], p2_row_4[6], p2_row_4[7], p2_row_3[0], p2_row_3[1], p2_row_3[2], p2_row_3[3], p2_row_3[4], p2_row_3[5], p2_row_3[6], p2_row_3[7], p2_row_2[0], p2_row_2[1], p2_row_2[2], p2_row_2[3], p2_row_2[4], p2_row_2[5], p2_row_2[6], p2_row_2[7], p2_row_1[0], p2_row_1[1], p2_row_1[2], p2_row_1[3], p2_row_1[4], p2_row_1[5], p2_row_1[6], p2_row_1[7]};  // AND_Gate and_3, 32 bits wide
  assign or_6_out = {controlled_buffer_4_out, controlled_buffer_3_out, controlled_buffer_2_out, controlled_buffer_1_out} | {p2_row_4[0], p2_row_4[1], p2_row_4[2], p2_row_4[3], p2_row_4[4], p2_row_4[5], p2_row_4[6], p2_row_4[7], p2_row_3[0], p2_row_3[1], p2_row_3[2], p2_row_3[3], p2_row_3[4], p2_row_3[5], p2_row_3[6], p2_row_3[7], p2_row_2[0], p2_row_2[1], p2_row_2[2], p2_row_2[3], p2_row_2[4], p2_row_2[5], p2_row_2[6], p2_row_2[7], p2_row_1[0], p2_row_1[1], p2_row_1[2], p2_row_1[3], p2_row_1[4], p2_row_1[5], p2_row_1[6], p2_row_1[7]};  // OR_Gate or_6, 32 bits wide
  assign and_4_out = ~{controlled_buffer_8_out, controlled_buffer_7_out, controlled_buffer_6_out, controlled_buffer_5_out} & {p2_row_8[0], p2_row_8[1], p2_row_8[2], p2_row_8[3], p2_row_8[4], p2_row_8[5], p2_row_8[6], p2_row_8[7], p2_row_7[0], p2_row_7[1], p2_row_7[2], p2_row_7[3], p2_row_7[4], p2_row_7[5], p2_row_7[6], p2_row_7[7], p2_row_6[0], p2_row_6[1], p2_row_6[2], p2_row_6[3], p2_row_6[4], p2_row_6[5], p2_row_6[6], p2_row_6[7], p2_row_5[0], p2_row_5[1], p2_row_5[2], p2_row_5[3], p2_row_5[4], p2_row_5[5], p2_row_5[6], p2_row_5[7]};  // AND_Gate and_4, 32 bits wide
  assign or_7_out = {controlled_buffer_8_out, controlled_buffer_7_out, controlled_buffer_6_out, controlled_buffer_5_out} | {p2_row_8[0], p2_row_8[1], p2_row_8[2], p2_row_8[3], p2_row_8[4], p2_row_8[5], p2_row_8[6], p2_row_8[7], p2_row_7[0], p2_row_7[1], p2_row_7[2], p2_row_7[3], p2_row_7[4], p2_row_7[5], p2_row_7[6], p2_row_7[7], p2_row_6[0], p2_row_6[1], p2_row_6[2], p2_row_6[3], p2_row_6[4], p2_row_6[5], p2_row_6[6], p2_row_6[7], p2_row_5[0], p2_row_5[1], p2_row_5[2], p2_row_5[3], p2_row_5[4], p2_row_5[5], p2_row_5[6], p2_row_5[7]};  // OR_Gate or_7, 32 bits wide
  Multiplexer #(.width(32), .enable("false")) multiplexer_4 (
    .in0(or_7_out), .in1(and_4_out), .out(multiplexer_4_out), .sel(decoder_1_out0));
  Register #(.width(32)) register_4 (
    .D(multiplexer_4_out), .en(or_8_out),
    .Q({p2_row_8[0], p2_row_8[1], p2_row_8[2], p2_row_8[3], p2_row_8[4], p2_row_8[5], p2_row_8[6], p2_row_8[7], p2_row_7[0], p2_row_7[1], p2_row_7[2], p2_row_7[3], p2_row_7[4], p2_row_7[5], p2_row_7[6], p2_row_7[7], p2_row_6[0], p2_row_6[1], p2_row_6[2], p2_row_6[3], p2_row_6[4], p2_row_6[5], p2_row_6[6], p2_row_6[7], p2_row_5[0], p2_row_5[1], p2_row_5[2], p2_row_5[3], p2_row_5[4], p2_row_5[5], p2_row_5[6], p2_row_5[7]}),
    .clk(wr), .clr(RST));
  or or_8 (or_8_out, decoder_1_out0, decoder_1_out2);
  assign DataO_1 = decoder_1_out2 ? {p2_row_4[0], p2_row_4[1], p2_row_4[2], p2_row_4[3], p2_row_4[4], p2_row_4[5], p2_row_4[6], p2_row_4[7], p2_row_3[0], p2_row_3[1], p2_row_3[2], p2_row_3[3], p2_row_3[4], p2_row_3[5], p2_row_3[6], p2_row_3[7], p2_row_2[0], p2_row_2[1], p2_row_2[2], p2_row_2[3], p2_row_2[4], p2_row_2[5], p2_row_2[6], p2_row_2[7], p2_row_1[0], p2_row_1[1], p2_row_1[2], p2_row_1[3], p2_row_1[4], p2_row_1[5], p2_row_1[6], p2_row_1[7]} : 32'bz;  // Controlled_Buffer controlled_buffer_11
  or or_9 (or_9_out, decoder_1_out0, decoder_1_out3);
  Multiplexer #(.width(32), .enable("false")) multiplexer_5 (
    .in0(or_10_out), .in1(and_5_out), .out(multiplexer_5_out), .sel(decoder_1_out0));
  assign or_10_out = {controlled_buffer_4_out, controlled_buffer_3_out, controlled_buffer_2_out, controlled_buffer_1_out} | {Task_row_4[0], Task_row_4[1], Task_row_4[2], Task_row_4[3], Task_row_4[4], Task_row_4[5], Task_row_4[6], Task_row_4[7], Task_row_3[0], Task_row_3[1], Task_row_3[2], Task_row_3[3], Task_row_3[4], Task_row_3[5], Task_row_3[6], Task_row_3[7], Task_row_2[0], Task_row_2[1], Task_row_2[2], Task_row_2[3], Task_row_2[4], Task_row_2[5], Task_row_2[6], Task_row_2[7], Task_row_1[0], Task_row_1[1], Task_row_1[2], Task_row_1[3], Task_row_1[4], Task_row_1[5], Task_row_1[6], Task_row_1[7]};  // OR_Gate or_10, 32 bits wide
  assign or_11_out = {controlled_buffer_8_out, controlled_buffer_7_out, controlled_buffer_6_out, controlled_buffer_5_out} | {Task_row_8[0], Task_row_8[1], Task_row_8[2], Task_row_8[3], Task_row_8[4], Task_row_8[5], Task_row_8[6], Task_row_8[7], Task_row_7[0], Task_row_7[1], Task_row_7[2], Task_row_7[3], Task_row_7[4], Task_row_7[5], Task_row_7[6], Task_row_7[7], Task_row_6[0], Task_row_6[1], Task_row_6[2], Task_row_6[3], Task_row_6[4], Task_row_6[5], Task_row_6[6], Task_row_6[7], Task_row_5[0], Task_row_5[1], Task_row_5[2], Task_row_5[3], Task_row_5[4], Task_row_5[5], Task_row_5[6], Task_row_5[7]};  // OR_Gate or_11, 32 bits wide
  Multiplexer #(.width(32), .enable("false")) multiplexer_6 (
    .in0(or_11_out), .in1(and_6_out), .out(multiplexer_6_out), .sel(decoder_1_out0));
  or or_12 (or_12_out, decoder_1_out0, decoder_1_out3);
  assign DataO_2 = decoder_1_out2 ? {p2_row_8[0], p2_row_8[1], p2_row_8[2], p2_row_8[3], p2_row_8[4], p2_row_8[5], p2_row_8[6], p2_row_8[7], p2_row_7[0], p2_row_7[1], p2_row_7[2], p2_row_7[3], p2_row_7[4], p2_row_7[5], p2_row_7[6], p2_row_7[7], p2_row_6[0], p2_row_6[1], p2_row_6[2], p2_row_6[3], p2_row_6[4], p2_row_6[5], p2_row_6[6], p2_row_6[7], p2_row_5[0], p2_row_5[1], p2_row_5[2], p2_row_5[3], p2_row_5[4], p2_row_5[5], p2_row_5[6], p2_row_5[7]} : 32'bz;  // Controlled_Buffer controlled_buffer_12
  assign DataO_1 = decoder_1_out3 ? {Task_row_4[0], Task_row_4[1], Task_row_4[2], Task_row_4[3], Task_row_4[4], Task_row_4[5], Task_row_4[6], Task_row_4[7], Task_row_3[0], Task_row_3[1], Task_row_3[2], Task_row_3[3], Task_row_3[4], Task_row_3[5], Task_row_3[6], Task_row_3[7], Task_row_2[0], Task_row_2[1], Task_row_2[2], Task_row_2[3], Task_row_2[4], Task_row_2[5], Task_row_2[6], Task_row_2[7], Task_row_1[0], Task_row_1[1], Task_row_1[2], Task_row_1[3], Task_row_1[4], Task_row_1[5], Task_row_1[6], Task_row_1[7]} : 32'bz;  // Controlled_Buffer controlled_buffer_13
  Register #(.width(32)) register_5 (
    .D(multiplexer_5_out), .en(or_9_out),
    .Q({Task_row_4[0], Task_row_4[1], Task_row_4[2], Task_row_4[3], Task_row_4[4], Task_row_4[5], Task_row_4[6], Task_row_4[7], Task_row_3[0], Task_row_3[1], Task_row_3[2], Task_row_3[3], Task_row_3[4], Task_row_3[5], Task_row_3[6], Task_row_3[7], Task_row_2[0], Task_row_2[1], Task_row_2[2], Task_row_2[3], Task_row_2[4], Task_row_2[5], Task_row_2[6], Task_row_2[7], Task_row_1[0], Task_row_1[1], Task_row_1[2], Task_row_1[3], Task_row_1[4], Task_row_1[5], Task_row_1[6], Task_row_1[7]}),
    .clk(wr), .clr(RST));
  assign and_5_out = ~{controlled_buffer_4_out, controlled_buffer_3_out, controlled_buffer_2_out, controlled_buffer_1_out} & {Task_row_4[0], Task_row_4[1], Task_row_4[2], Task_row_4[3], Task_row_4[4], Task_row_4[5], Task_row_4[6], Task_row_4[7], Task_row_3[0], Task_row_3[1], Task_row_3[2], Task_row_3[3], Task_row_3[4], Task_row_3[5], Task_row_3[6], Task_row_3[7], Task_row_2[0], Task_row_2[1], Task_row_2[2], Task_row_2[3], Task_row_2[4], Task_row_2[5], Task_row_2[6], Task_row_2[7], Task_row_1[0], Task_row_1[1], Task_row_1[2], Task_row_1[3], Task_row_1[4], Task_row_1[5], Task_row_1[6], Task_row_1[7]};  // AND_Gate and_5, 32 bits wide
  assign and_6_out = ~{controlled_buffer_8_out, controlled_buffer_7_out, controlled_buffer_6_out, controlled_buffer_5_out} & {Task_row_8[0], Task_row_8[1], Task_row_8[2], Task_row_8[3], Task_row_8[4], Task_row_8[5], Task_row_8[6], Task_row_8[7], Task_row_7[0], Task_row_7[1], Task_row_7[2], Task_row_7[3], Task_row_7[4], Task_row_7[5], Task_row_7[6], Task_row_7[7], Task_row_6[0], Task_row_6[1], Task_row_6[2], Task_row_6[3], Task_row_6[4], Task_row_6[5], Task_row_6[6], Task_row_6[7], Task_row_5[0], Task_row_5[1], Task_row_5[2], Task_row_5[3], Task_row_5[4], Task_row_5[5], Task_row_5[6], Task_row_5[7]};  // AND_Gate and_6, 32 bits wide
  Register #(.width(32)) register_6 (
    .D(multiplexer_6_out), .en(or_12_out),
    .Q({Task_row_8[0], Task_row_8[1], Task_row_8[2], Task_row_8[3], Task_row_8[4], Task_row_8[5], Task_row_8[6], Task_row_8[7], Task_row_7[0], Task_row_7[1], Task_row_7[2], Task_row_7[3], Task_row_7[4], Task_row_7[5], Task_row_7[6], Task_row_7[7], Task_row_6[0], Task_row_6[1], Task_row_6[2], Task_row_6[3], Task_row_6[4], Task_row_6[5], Task_row_6[6], Task_row_6[7], Task_row_5[0], Task_row_5[1], Task_row_5[2], Task_row_5[3], Task_row_5[4], Task_row_5[5], Task_row_5[6], Task_row_5[7]}),
    .clk(wr), .clr(RST));
  assign DataO_2 = decoder_1_out3 ? {Task_row_8[0], Task_row_8[1], Task_row_8[2], Task_row_8[3], Task_row_8[4], Task_row_8[5], Task_row_8[6], Task_row_8[7], Task_row_7[0], Task_row_7[1], Task_row_7[2], Task_row_7[3], Task_row_7[4], Task_row_7[5], Task_row_7[6], Task_row_7[7], Task_row_6[0], Task_row_6[1], Task_row_6[2], Task_row_6[3], Task_row_6[4], Task_row_6[5], Task_row_6[6], Task_row_6[7], Task_row_5[0], Task_row_5[1], Task_row_5[2], Task_row_5[3], Task_row_5[4], Task_row_5[5], Task_row_5[6], Task_row_5[7]} : 32'bz;  // Controlled_Buffer controlled_buffer_14
  Pull_Resistor pull_resistor_4 (.node(DataO_1));
  Pull_Resistor pull_resistor_5 (.node(DataO_2));

  assign p2_row_1[8] = 1'b0;
  assign p2_row_2[8] = 1'b0;
  assign p2_row_3[8] = 1'b0;
  assign p2_row_4[8] = 1'b0;
  assign p2_row_5[8] = 1'b0;
  assign p2_row_6[8] = 1'b0;
  assign p2_row_7[8] = 1'b0;
  assign p2_row_8[8] = 1'b0;
  assign Task_row_1[9:8] = 2'b00;
  assign Task_row_2[9:8] = 2'b00;
  assign Task_row_3[9:8] = 2'b00;
  assign Task_row_4[9:8] = 2'b00;
  assign Task_row_5[9:8] = 2'b00;
  assign Task_row_6[9:8] = 2'b00;
  assign Task_row_7[9:8] = 2'b00;
  assign Task_row_8[9:8] = 2'b00;
endmodule

module pointer_mover (
  input  [4:0] KBD_command,
  input  CLK,
  input  RST,
  output [7:0] CSC,
  output [7:0] CSR
);

  wire and_1_out, and_2_out, and_3_out, and_4_out, comparator_1_eq, comparator_2_eq, comparator_3_eq,
       comparator_4_eq, not_1_out, not_2_out, or_1_out, or_2_out, or_3_out, or_4_out;
  wire [7:0] multiplexer_1_out, multiplexer_2_out, multiplexer_3_out, multiplexer_4_out;

  // Probe on KBD_command
  Comparator #(.width(5), .mode("unsigned")) comparator_1 (
    .a(KBD_command), .b(5'b10001), .eq(comparator_1_eq));  // open: gt, lt
  Comparator #(.width(5), .mode("unsigned")) comparator_2 (
    .a(KBD_command), .b(5'b10010), .eq(comparator_2_eq));  // open: gt, lt
  Comparator #(.width(5), .mode("unsigned")) comparator_3 (
    .a(KBD_command), .b(5'b10000), .eq(comparator_3_eq));  // open: gt, lt
  Comparator #(.width(5), .mode("unsigned")) comparator_4 (
    .a(KBD_command), .b(5'b10011), .eq(comparator_4_eq));  // open: gt, lt
  or or_1 (or_1_out, comparator_1_eq, comparator_2_eq);
  or or_2 (or_2_out, comparator_3_eq, comparator_4_eq);
  Multiplexer #(.width(8), .enable("false")) multiplexer_1 (
    .in0({CSC[0], CSC[7:1]}), .in1({CSC[6:0], CSC[7]}), .out(multiplexer_1_out), .sel(comparator_1_eq));
  Multiplexer #(.width(8), .enable("false")) multiplexer_2 (
    .in0({CSR[0], CSR[7:1]}), .in1({CSR[6:0], CSR[7]}), .out(multiplexer_2_out), .sel(comparator_3_eq));
  Multiplexer #(.width(8), .enable("false")) multiplexer_3 (
    .in0(multiplexer_1_out), .in1(8'h1), .out(multiplexer_3_out), .sel(RST));
  Register register_1 (.D(multiplexer_3_out), .en(1'b1), .Q(CSC), .clk(or_3_out), .clr(1'b0));
  or or_3 (or_3_out, and_3_out, and_1_out);
  and and_1 (and_1_out, CLK, or_1_out);
  Multiplexer #(.width(8), .enable("false")) multiplexer_4 (
    .in0(multiplexer_2_out), .in1(8'h1), .out(multiplexer_4_out), .sel(RST));
  Register register_2 (.D(multiplexer_4_out), .en(1'b1), .Q(CSR), .clk(or_4_out), .clr(1'b0));
  or or_4 (or_4_out, and_4_out, and_2_out);
  and and_2 (and_2_out, CLK, or_2_out);
  and and_3 (and_3_out, ~RST, ~not_1_out);  // AND_Gate
  not not_1 (not_1_out, RST);
  and and_4 (and_4_out, ~RST, ~not_2_out);  // AND_Gate
  not not_2 (not_2_out, RST);
endmodule

module position_checker (
  input  [7:0] CSc,
  input  [7:0] CSR,
  input  [31:0] Field_input_1,
  input  [31:0] Field_input_2,
  output Out
);

  wire [7:0] and_1_out, controlled_buffer_1_out;

  assign controlled_buffer_1_out = CSR[0] ? Field_input_1[7:0] : 8'bz;  // Controlled_Buffer controlled_buffer_1
  assign controlled_buffer_1_out = CSR[1] ? Field_input_1[15:8] : 8'bz;  // Controlled_Buffer controlled_buffer_2
  assign controlled_buffer_1_out = CSR[2] ? Field_input_1[23:16] : 8'bz;  // Controlled_Buffer controlled_buffer_3
  assign controlled_buffer_1_out = CSR[3] ? Field_input_1[31:24] : 8'bz;  // Controlled_Buffer controlled_buffer_4
  assign controlled_buffer_1_out = CSR[4] ? Field_input_2[7:0] : 8'bz;  // Controlled_Buffer controlled_buffer_5
  assign controlled_buffer_1_out = CSR[5] ? Field_input_2[15:8] : 8'bz;  // Controlled_Buffer controlled_buffer_6
  assign controlled_buffer_1_out = CSR[6] ? Field_input_2[23:16] : 8'bz;  // Controlled_Buffer controlled_buffer_7
  assign and_1_out = CSc & controlled_buffer_1_out;  // AND_Gate and_1, 8 bits wide
  assign controlled_buffer_1_out = CSR[7] ? Field_input_2[31:24] : 8'bz;  // Controlled_Buffer controlled_buffer_8
  or or_1 (Out, and_1_out[0], and_1_out[1], and_1_out[2], and_1_out[3], and_1_out[4], and_1_out[5], and_1_out[6], and_1_out[7], 1'b0);
endmodule

module pointer_controller (
  input  Active,
  input  [4:0] KBD_command,
  input  CLK,
  input  RST,
  input  [31:0] Field_state_1,
  input  [31:0] Field_state_2,
  input  Allow_nearby,
  input  Free_mode,
  output [7:0] CSC,
  output [7:0] CSR,
  output Err,
  output Ready
);

  wire and_2_out, and_3_out, clk_t, counter_1_carry, d_ff_1_q, not_1_out, not_2_out, or_1_out, or_2_out,
       or_3_out, or_4_out, position_checker_1_out, stop, xor_1_out;
  wire [3:0] counter_1_q;

  and and_1 (clk_t, ~stop, Active, CLK);  // AND_Gate
  pointer_mover pointer_mover_1 (.CLK(clk_t), .RST(RST), .CSC(CSC), .CSR(CSR), .KBD_command(KBD_command));
  position_checker position_checker_1 (
    .CSc(CSC), .CSR(CSR), .Field_input_1(Field_state_1), .Field_input_2(Field_state_2),
    .Out(position_checker_1_out));
  D_Flip_Flop d_ff_1 (
    .clk(Active), .D(position_checker_1_out), .Q(d_ff_1_q), .en(Allow_nearby), .reset(or_1_out));  // open: Qn, preset
  and and_2 (and_2_out, Allow_nearby, d_ff_1_q);
  or or_1 (or_1_out, RST, and_3_out);
  and and_3 (and_3_out, ~Active, ~not_1_out);  // AND_Gate
  Counter #(.width(4), .max('h8), .trigger("falling")) counter_1 (
    .load(1'b0), .count(1'b1), .Q(counter_1_q), .carry(counter_1_carry), .clk(clk_t), .clr(or_2_out));  // open: D
  or or_2 (or_2_out, RST, xor_1_out);
  not not_1 (not_1_out, Active);
  or or_3 (or_3_out, 1'b0, counter_1_q[0], counter_1_q[1], counter_1_q[2], counter_1_q[3]);
  xor xor_1 (xor_1_out, ~Active, not_2_out);  // XOR_Gate
  not not_2 (not_2_out, Active);
  or or_4 (or_4_out, and_2_out, position_checker_1_out, Free_mode);
  and and_4 (Err, counter_1_carry, ~Ready);  // AND_Gate
  or or_5 (stop, Err, Ready);
  and and_5 (Ready, or_3_out, or_4_out);
endmodule

module basic_controller (
  input  [4:0] KBD_command,
  input  KBD_ready,
  input  PC_ready,
  input  Active,
  input  Is_special,
  input  [1:0] Mode,
  input  Wrong_move,
  input  CLK,
  input  SPI_done,
  input  SPI_error,
  output Req_KBD,
  output Req_KBD_num,
  output PC_active,
  output Merge,
  output Error,
  output Check_speciality,
  output Call_CDM,
  output PC_free_mode,
  output PC_allow_nearby,
  output [7:0] SPI_control,
  output Enter
);

  wire allow_e_manip, and_2_out, and_4_out, and_5_out, and_6_out, and_7_out, and_10_out, and_11_out,
       and_13_out, and_14_out, and_15_out, and_16_out, and_17_out, and_18_out, and_19_out, and_20_out,
       and_21_out, and_22_out, and_23_out, and_24_out, clk_t, comparator_1_gt, comparator_2_lt,
       comparator_3_gt, comparator_4_lt, comparator_5_eq, counter_1_carry, d_ff_1_q, d_ff_1_qn, d_ff_2_q,
       d_ff_5_q, d_ff_6_q, decoder_2_out0, decoder_2_out1, decoder_2_out3, decoder_2_out5, decoder_2_out6,
       not_1_out, not_2_out, not_3_out, not_4_out, not_5_out, not_6_out, or_1_out, or_3_out, or_4_out,
       or_5_out, or_7_out, or_8_out, or_9_out, rst, SPI_wait, stop;
  wire [2:0] pull_resistor_1_node, register_1_q;

  or or_1 (or_1_out, SPI_wait, PC_active, Req_KBD, stop);
  Pull_Resistor pull_resistor_1 (.node(pull_resistor_1_node));
  not not_1 (not_1_out, Active);
  Decoder #(.select(2), .enable("false")) decoder_1 (
    .out0(PC_free_mode), .out1(allow_e_manip), .out2(PC_allow_nearby), .sel(Mode));  // open: out3
  and and_1 (clk_t, ~or_1_out, Active, CLK);  // AND_Gate
  Register #(.width(3), .trigger("falling")) register_1 (
    .D(pull_resistor_1_node), .en(1'b1), .Q(register_1_q), .clk(and_2_out), .clr(rst));
  // Probe on pull_resistor_1_node
  and and_2 (and_2_out, or_8_out, clk_t);
  and and_3 (rst, Active, not_1_out);
  D_Flip_Flop #(.trigger("falling")) d_ff_1 (
    .clk(SPI_done), .D(decoder_2_out6), .Q(d_ff_1_q), .Qn(d_ff_1_qn), .preset(1'b0), .en(1'b1),
    .reset(and_4_out));
  not not_2 (not_2_out, decoder_2_out6);
  and and_4 (and_4_out, not_2_out, decoder_2_out6);
  Decoder #(.select(3), .disabled(0)) decoder_2 (
    .out0(decoder_2_out0), .out1(decoder_2_out1), .out2(Merge), .out3(decoder_2_out3),
    .out4(Check_speciality), .out5(decoder_2_out5), .out6(decoder_2_out6), .out7(Error), .sel(register_1_q),
    .en(Active));
  assign SPI_control = and_5_out ? 8'h44 : 8'bz;  // Controlled_Buffer controlled_buffer_1
  and and_5 (and_5_out, decoder_2_out6, d_ff_1_q);
  and and_6 (and_6_out, d_ff_1_qn, ~SPI_done, decoder_2_out6);  // AND_Gate
  assign SPI_control = and_6_out ? 8'h2e : 8'bz;  // Controlled_Buffer controlled_buffer_2
  or or_2 (Req_KBD, Req_KBD_num, and_7_out);
  and and_7 (and_7_out, Active, or_3_out, ~d_ff_5_q);  // AND_Gate
  or or_3 (or_3_out, decoder_2_out0, decoder_2_out1);
  or or_4 (or_4_out, decoder_2_out5, decoder_2_out6);
  assign SPI_control = decoder_2_out5 ? 8'h26 : 8'bz;  // Controlled_Buffer controlled_buffer_3
  and and_8 (Req_KBD_num, Active, decoder_2_out1, ~d_ff_5_q);  // AND_Gate
  and and_9 (PC_active, decoder_2_out3, Active, ~d_ff_2_q);  // AND_Gate
  or or_5 (or_5_out, decoder_2_out5, and_5_out);
  Pull_Resistor pull_resistor_2 (.node(SPI_control));
  D_Flip_Flop d_ff_2 (.clk(CLK), .D(PC_ready), .Q(d_ff_2_q), .reset(and_13_out));  // open: Qn, preset, en
  and and_10 (and_10_out, Check_speciality, Is_special);
  D_Flip_Flop d_ff_3 (.clk(clk_t), .D(and_10_out), .Q(Call_CDM), .preset(1'b0), .en(1'b1), .reset(rst));  // open: Qn
  and and_11 (and_11_out, Check_speciality, ~Error, ~Is_special);  // AND_Gate
  and and_12 (SPI_wait, Active, or_4_out, ~SPI_done);  // AND_Gate
  Comparator #(.width(5), .mode("unsigned")) comparator_1 (
    .a(KBD_command), .b(5'b01111), .gt(comparator_1_gt));  // open: eq, lt
  Comparator #(.width(5), .mode("unsigned")) comparator_2 (
    .a(KBD_command), .b(5'b10100), .lt(comparator_2_lt));  // open: gt, eq
  not not_3 (not_3_out, decoder_2_out3);
  and and_13 (and_13_out, not_3_out, decoder_2_out3);
  Comparator #(.width(5), .mode("unsigned")) comparator_3 (
    .a(KBD_command), .b(5'b01011), .gt(comparator_3_gt));  // open: eq, lt
  Comparator #(.width(5), .mode("unsigned")) comparator_4 (
    .a(KBD_command), .b(5'b10000), .lt(comparator_4_lt));  // open: gt, eq
  Comparator #(.width(5), .mode("unsigned")) comparator_5 (
    .a(KBD_command), .b({5{1'b1}}), .eq(comparator_5_eq));  // open: gt, lt
  and and_14 (and_14_out, comparator_1_gt, decoder_2_out0, comparator_2_lt);
  and and_15 (and_15_out, comparator_3_gt, allow_e_manip, comparator_4_lt);
  not not_4 (not_4_out, Wrong_move);
  D_Flip_Flop #(.trigger("falling")) d_ff_4 (
    .clk(clk_t), .D(comparator_5_eq), .Q(Enter), .preset(1'b0), .en(1'b1), .reset(rst));  // open: Qn
  and and_16 (and_16_out, KBD_ready, decoder_2_out1);
  assign pull_resistor_1_node = and_16_out ? 3'b010 : 3'bz;  // Controlled_Buffer controlled_buffer_4
  and and_17 (and_17_out, KBD_ready, and_14_out);
  assign pull_resistor_1_node = and_17_out ? 3'b011 : 3'bz;  // Controlled_Buffer controlled_buffer_5
  assign pull_resistor_1_node = Merge ? 3'b110 : 3'bz;  // Controlled_Buffer controlled_buffer_6
  and and_18 (and_18_out, d_ff_2_q, decoder_2_out3);
  assign pull_resistor_1_node = and_18_out ? 3'b101 : 3'bz;  // Controlled_Buffer controlled_buffer_7
  and and_19 (and_19_out, KBD_ready, and_15_out, not_4_out);
  assign pull_resistor_1_node = and_19_out ? 3'b001 : 3'bz;  // Controlled_Buffer controlled_buffer_8
  and and_20 (and_20_out, KBD_ready, and_15_out, Wrong_move, ~Error);  // AND_Gate
  assign pull_resistor_1_node = and_20_out ? 3'b111 : 3'bz;  // Controlled_Buffer controlled_buffer_9
  assign pull_resistor_1_node = and_11_out ? 3'b111 : 3'bz;  // Controlled_Buffer controlled_buffer_10
  and and_21 (and_21_out, SPI_done, or_5_out, SPI_error, ~Error);  // AND_Gate
  assign pull_resistor_1_node = and_21_out ? 3'b111 : 3'bz;  // Controlled_Buffer controlled_buffer_11
  and and_22 (and_22_out, or_5_out, or_4_out, ~SPI_error);  // AND_Gate
  assign pull_resistor_1_node = and_22_out ? 3'b000 : 3'bz;  // Controlled_Buffer controlled_buffer_12
  assign pull_resistor_1_node = Error ? 3'b000 : 3'bz;  // Controlled_Buffer controlled_buffer_13
  or or_6 (stop, Enter, Call_CDM);
  and and_23 (and_23_out, decoder_2_out1, not_5_out);
  not not_5 (not_5_out, decoder_2_out1);
  not not_6 (not_6_out, decoder_2_out0);
  D_Flip_Flop d_ff_5 (.clk(CLK), .D(KBD_ready), .Q(d_ff_5_q), .preset(1'b0), .en(1'b1), .reset(or_7_out));  // open: Qn
  or or_7 (or_7_out, and_23_out, and_24_out);
  and and_24 (and_24_out, decoder_2_out0, not_6_out);
  or or_8 (or_8_out, and_16_out, and_17_out, Merge, and_18_out, and_19_out, and_20_out, and_11_out, and_21_out, and_22_out, Error, d_ff_6_q);
  Counter #(.width(2), .max('h3)) counter_1 (
    .load(1'b0), .count(1'b1), .carry(counter_1_carry), .clk(clk_t), .clr(or_9_out));  // open: D, Q
  or or_9 (or_9_out, or_8_out, rst);
  D_Flip_Flop #(.trigger("falling")) d_ff_6 (
    .clk(clk_t), .D(counter_1_carry), .Q(d_ff_6_q), .preset(1'b0), .en(1'b1), .reset(rst));  // open: Qn
  assign pull_resistor_1_node = d_ff_6_q ? 3'b111 : 3'bz;  // Controlled_Buffer controlled_buffer_14

  // Other names for the same wires on the sheet: KBD_wait = Req_KBD; PC_wait = PC_active
endmodule

module move_checker (
  input  [4:0] KBD_command,
  input  [7:0] CSC,
  input  [7:0] CSR,
  output Is_wrong
);

  wire and_1_out, and_2_out, and_3_out, and_4_out, comparator_1_eq, comparator_2_eq, comparator_3_eq,
       comparator_4_eq;

  Comparator #(.width(5), .mode("unsigned")) comparator_1 (
    .a(KBD_command), .b(5'b01110), .eq(comparator_1_eq));  // open: gt, lt
  Comparator #(.width(5), .mode("unsigned")) comparator_2 (
    .a(KBD_command), .b(5'b01101), .eq(comparator_2_eq));  // open: gt, lt
  Comparator #(.width(5), .mode("unsigned")) comparator_3 (
    .a(KBD_command), .b(5'b01111), .eq(comparator_3_eq));  // open: gt, lt
  Comparator #(.width(5), .mode("unsigned")) comparator_4 (
    .a(KBD_command), .b(5'b01100), .eq(comparator_4_eq));  // open: gt, lt
  and and_1 (and_1_out, comparator_1_eq, CSC[0]);
  and and_2 (and_2_out, comparator_2_eq, CSC[7]);
  and and_3 (and_3_out, comparator_3_eq, CSR[0]);
  and and_4 (and_4_out, comparator_4_eq, CSR[7]);
  or or_1 (Is_wrong, and_1_out, and_2_out, and_3_out, and_4_out);
endmodule

module MCU_v2 (
  input  [4:0] KBD_command,
  input  [10:0] KBD_energy_increment,
  input  KBD_Ready,
  input  [31:0] Field_cache_Datai_1,
  input  [31:0] Field_cache_DataI_2,
  input  Reset,
  input  CLK,
  input  MISO,
  input  SPI_busy,
  output Request_KBD,
  output Request_KBD_energy,
  output [7:0] Cell_CSC,
  output [7:0] Cell_CSR,
  output [1:0] Field_cache_select,
  output [2:0] Table_CSC,
  output [5:0] Table_CSR,
  output Task_CS,
  output Field_cache_wr,
  output SPI_clock,
  output MOSI,
  output [7:0] Debug_out,
  output Waiting_IO,
  output SPI_communication_in_progress
);

  wire and_1_out, and_2_out, and_3_out, and_4_out, and_5_out, and_6_out, and_7_out, and_8_out, and_9_out,
       and_10_out, and_11_out, basic_controller_1_call_cdm, basic_controller_1_check_speciality,
       basic_controller_1_enter, basic_controller_1_pc_active, basic_controller_1_pc_allow_nearby,
       basic_controller_1_pc_free_mode, basic_controller_1_req_kbd, basic_controller_1_req_kbd_num, BC_err,
       cdm_8_1_data_code_prime, cdm_8_1_load_st_prime, cdm_8_1_mem, d_ff_1_q, Data, decoder_1_out0,
       io_dmx_1_bc_control, io_dmx_1_cell_csc, io_dmx_1_cell_csr, io_dmx_1_debug_output, io_dmx_1_is_io,
       io_dmx_1_spi_kbd_control, io_dmx_1_table__csc__csr____task_cs, io_dmx_1_universal_io_1,
       io_dmx_1_universal_io_2, merge, move_checker_1_is_wrong, not_1_out, not_2_out, not_3_out, or_1_out,
       or_2_out, or_3_out, or_4_out, or_6_out, or_9_out, PC_err, pointer_controller_1_ready,
       position_checker_1_out, spi_module_master_1_communication_end,
       spi_module_master_1_input_transanction_end, spi_module_master_1_output_transanction_end, wait_BC,
       wait_KBD;
  wire [6:0] demultiplexer_2_out0, demultiplexer_2_out1, register_6_q;
  wire [6:3] register_1_q;
  wire [7:0] basic_controller_1_spi_control, cdm_8_1_addr, cdm_8_1_data_out, cdm_8_1_pc, cdm_8_1_ps,
       cdm_8_1_r0, cdm_8_1_r1, cdm_8_1_r2, cdm_8_1_r3, cdm_8_1_sp, controlled_buffer_1_out,
       controlled_buffer_2_out, controlled_buffer_3_out, controlled_buffer_4_out, controlled_buffer_7_out,
       controlled_buffer_9_out, controlled_buffer_18_out, or_5_out, pointer_controller_1_csc,
       pointer_controller_1_csr, register_3_q, register_4_q, register_5_q, register_7_q, register_8_q;
  wire [15:0] spi_module_master_1_recv_data;

  // Probe on cdm_8_1_r0
  // Probe on cdm_8_1_r0
  // Probe on cdm_8_1_r0
  // Probe on cdm_8_1_ps[6:4]
  // Probe on cdm_8_1_ps[7]
  // Probe on cdm_8_1_pc
  // Probe on cdm_8_1_r1
  // Probe on cdm_8_1_r0
  // Probe on cdm_8_1_ps[3]
  // Probe on cdm_8_1_ps[2]
  // Probe on cdm_8_1_r1
  // Probe on cdm_8_1_r1
  // Probe on cdm_8_1_r1
  // Probe on cdm_8_1_ps[0]
  // Probe on cdm_8_1_ps[1]
  // Probe on cdm_8_1_r2
  // Probe on cdm_8_1_r2
  // Probe on cdm_8_1_r2
  // Probe on cdm_8_1_r2
  // Probe on cdm_8_1_sp
  // Probe on cdm_8_1_r3
  // Probe on cdm_8_1_r3
  and and_1 (and_1_out, CLK, ~wait_BC, ~Waiting_IO);  // AND_Gate
  // Probe on cdm_8_1_r3
  // Probe on cdm_8_1_r3
  CdM_8 cdm_8_1 (
    .data_code_prime(cdm_8_1_data_code_prime), .R0(cdm_8_1_r0), .R1(cdm_8_1_r1), .mem(cdm_8_1_mem),
    .R2(cdm_8_1_r2), .load_st_prime(cdm_8_1_load_st_prime), .R3(cdm_8_1_r3), .addr(cdm_8_1_addr),
    .PC(cdm_8_1_pc), .SP(cdm_8_1_sp), .data_out(cdm_8_1_data_out), .data_in(controlled_buffer_2_out),
    .PS(cdm_8_1_ps), .clk(and_1_out), .rset(Reset));  // open: page, IAck, IRQ, vector, shadow
  Decoder #(.disabled(0)) decoder_1 (
    .out0(decoder_1_out0), .out1(Data), .sel(cdm_8_1_data_code_prime), .en(cdm_8_1_mem));
  assign controlled_buffer_1_out = not_1_out ? cdm_8_1_data_out : 8'bz;  // Controlled_Buffer controlled_buffer_1
  not not_1 (not_1_out, cdm_8_1_load_st_prime);
  assign controlled_buffer_2_out = cdm_8_1_load_st_prime ? controlled_buffer_1_out : 8'bz;  // Controlled_Buffer controlled_buffer_2
  and and_2 (and_2_out, ~io_dmx_1_is_io, Data);  // AND_Gate
  IO_dmx io_dmx_1 (
    .Address(cdm_8_1_addr), .Is_IO(io_dmx_1_is_io), .Cell_CSC(io_dmx_1_cell_csc),
    .Cell_CSR(io_dmx_1_cell_csr), .Table__CSC__CSR____Task_CS(io_dmx_1_table__csc__csr____task_cs),
    .SPI_KBD_control(io_dmx_1_spi_kbd_control), .Universal_IO_1(io_dmx_1_universal_io_1),
    .Universal_IO_2(io_dmx_1_universal_io_2), .Debug_output(io_dmx_1_debug_output), .Selected(Data),
    .BC_control(io_dmx_1_bc_control));
  ROM rom_1 (.addr(cdm_8_1_addr), .data(controlled_buffer_1_out), .sel(decoder_1_out0));
  RAM ram_1 (
    .addr(cdm_8_1_addr), .data(controlled_buffer_1_out), .sel(and_2_out), .clk(CLK),
    .ld(cdm_8_1_load_st_prime), .clr(Reset));
  Register #(.trigger("falling")) register_1 (
    .D(controlled_buffer_1_out), .en(io_dmx_1_table__csc__csr____task_cs),
    .Q({Task_CS, register_1_q, Table_CSC}), .clk(CLK), .clr(Reset));
  Register #(.trigger("falling")) register_2 (
    .D(controlled_buffer_1_out), .en(io_dmx_1_debug_output), .Q(Debug_out), .clk(CLK), .clr(Reset));
  Demultiplexer #(.width(3), .disabled(0), .enable("false")) demultiplexer_1 (
    .out0(Table_CSR[2:0]), .out1(Table_CSR[5:3]), .in(register_1_q[5:3]), .sel(register_1_q[6]));
  Register #(.trigger("falling")) register_3 (
    .D(controlled_buffer_1_out), .en(io_dmx_1_cell_csc), .Q(register_3_q), .clk(CLK), .clr(Reset));
  Register #(.trigger("falling")) register_4 (
    .D(controlled_buffer_1_out), .en(io_dmx_1_cell_csr), .Q(register_4_q), .clk(CLK), .clr(Reset));
  assign controlled_buffer_3_out = io_dmx_1_bc_control ? controlled_buffer_1_out : 8'bz;  // Controlled_Buffer controlled_buffer_3
  or or_1 (or_1_out, basic_controller_1_enter, basic_controller_1_call_cdm, io_dmx_1_bc_control);
  assign controlled_buffer_4_out = wait_BC ? basic_controller_1_spi_control : 8'bz;  // Controlled_Buffer controlled_buffer_4
  assign controlled_buffer_4_out = io_dmx_1_spi_kbd_control ? controlled_buffer_1_out : 8'bz;  // Controlled_Buffer controlled_buffer_5
  or or_2 (or_2_out, io_dmx_1_spi_kbd_control, wait_BC);
  and and_3 (and_3_out, io_dmx_1_is_io, cdm_8_1_load_st_prime, io_dmx_1_universal_io_1);
  assign controlled_buffer_1_out = and_3_out ? register_7_q : 8'bz;  // Controlled_Buffer controlled_buffer_6
  and and_4 (and_4_out, io_dmx_1_is_io, ~cdm_8_1_load_st_prime, io_dmx_1_universal_io_1);  // AND_Gate
  assign controlled_buffer_7_out = and_4_out ? controlled_buffer_1_out : 8'bz;  // Controlled_Buffer controlled_buffer_7
  or or_3 (or_3_out, io_dmx_1_universal_io_1, spi_module_master_1_communication_end, and_11_out);
  and and_5 (and_5_out, io_dmx_1_is_io, io_dmx_1_universal_io_2, cdm_8_1_load_st_prime);
  assign controlled_buffer_1_out = and_5_out ? register_8_q : 8'bz;  // Controlled_Buffer controlled_buffer_8
  and and_6 (and_6_out, io_dmx_1_is_io, ~cdm_8_1_load_st_prime, io_dmx_1_universal_io_2);  // AND_Gate
  assign controlled_buffer_9_out = and_6_out ? controlled_buffer_1_out : 8'bz;  // Controlled_Buffer controlled_buffer_9
  or or_4 (or_4_out, io_dmx_1_universal_io_2, spi_module_master_1_communication_end, and_11_out);
  Register #(.trigger("falling")) register_5 (
    .D(controlled_buffer_3_out), .en(or_1_out),
    .Q({register_5_q[7], Field_cache_wr, register_5_q[5:3], wait_BC, register_5_q[1:0]}), .clk(CLK),
    .clr(Reset));
  Register #(.trigger("falling")) register_6 (
    .D(controlled_buffer_4_out), .en(or_2_out), .Q({wait_KBD, register_6_q}), .clk(CLK), .clr(or_6_out));
  Register #(.trigger("falling")) register_7 (
    .D(controlled_buffer_7_out), .en(or_3_out), .Q(register_7_q), .clk(CLK), .clr(Reset));
  Register #(.trigger("falling")) register_8 (
    .D(controlled_buffer_9_out), .en(or_4_out), .Q(register_8_q), .clk(CLK), .clr(Reset));
  assign controlled_buffer_3_out = basic_controller_1_call_cdm ? {register_5_q[7], Field_cache_wr, register_5_q[5:4], 4'b0001} : 8'bz;  // Controlled_Buffer controlled_buffer_10
  assign or_5_out = register_8_q | controlled_buffer_18_out;  // OR_Gate or_5, 8 bits wide
  assign controlled_buffer_7_out = merge ? or_5_out : 8'bz;  // Controlled_Buffer controlled_buffer_11
  not not_2 (not_2_out, merge);
  assign controlled_buffer_7_out = not_2_out ? controlled_buffer_18_out : 8'bz;  // Controlled_Buffer controlled_buffer_12
  assign controlled_buffer_3_out = basic_controller_1_enter ? {register_5_q[7], Field_cache_wr, register_5_q[5:4], 4'b0000} : 8'bz;  // Controlled_Buffer controlled_buffer_13
  basic_controller basic_controller_1 (
    .Merge(merge), .PC_ready(pointer_controller_1_ready), .Active(wait_BC),
    .Is_special(position_checker_1_out), .Call_CDM(basic_controller_1_call_cdm), .Mode(register_5_q[1:0]),
    .Wrong_move(move_checker_1_is_wrong), .CLK(CLK), .SPI_error(controlled_buffer_18_out[0]),
    .PC_active(basic_controller_1_pc_active), .Check_speciality(basic_controller_1_check_speciality),
    .PC_free_mode(basic_controller_1_pc_free_mode), .PC_allow_nearby(basic_controller_1_pc_allow_nearby),
    .SPI_done(spi_module_master_1_communication_end), .SPI_control(basic_controller_1_spi_control),
    .Enter(basic_controller_1_enter), .Req_KBD(basic_controller_1_req_kbd),
    .Req_KBD_num(basic_controller_1_req_kbd_num), .KBD_command(KBD_command), .KBD_ready(KBD_Ready),
    .Error(BC_err));
  Multiplexer #(.width(2), .disabled(0), .enable("false")) multiplexer_1 (
    .in0(register_5_q[5:4]), .in1(2'b11), .out(Field_cache_select), .sel(basic_controller_1_check_speciality));
  pointer_controller pointer_controller_1 (
    .Active(basic_controller_1_pc_active), .CLK(CLK), .RST(Reset), .Field_state_1(Field_cache_Datai_1),
    .Field_state_2(Field_cache_DataI_2), .Free_mode(basic_controller_1_pc_free_mode),
    .CSC(pointer_controller_1_csc), .CSR(pointer_controller_1_csr), .Err(PC_err),
    .Ready(pointer_controller_1_ready), .KBD_command(KBD_command),
    .Allow_nearby(basic_controller_1_pc_allow_nearby));
  assign Cell_CSR = register_5_q[3] ? register_3_q : 8'bz;  // Controlled_Buffer controlled_buffer_14
  assign Cell_CSC = register_5_q[3] ? register_4_q : 8'bz;  // Controlled_Buffer controlled_buffer_15
  not not_3 (not_3_out, register_5_q[3]);
  assign Cell_CSC = not_3_out ? pointer_controller_1_csc : 8'bz;  // Controlled_Buffer controlled_buffer_16
  assign Cell_CSR = not_3_out ? pointer_controller_1_csr : 8'bz;  // Controlled_Buffer controlled_buffer_17
  position_checker position_checker_1 (
    .CSc(Cell_CSC), .CSR(Cell_CSR), .Field_input_1(Field_cache_Datai_1), .Field_input_2(Field_cache_DataI_2),
    .Out(position_checker_1_out));
  or or_6 (or_6_out, and_7_out, Reset);
  move_checker move_checker_1 (
    .CSC(Cell_CSC), .CSR(Cell_CSR), .Is_wrong(move_checker_1_is_wrong), .KBD_command(KBD_command));
  Demultiplexer #(.width(7), .disabled(0), .enable("false")) demultiplexer_2 (
    .out0(demultiplexer_2_out0), .out1(demultiplexer_2_out1), .in(register_6_q), .sel(wait_KBD));
  and and_7 (and_7_out, Waiting_IO, or_9_out, and_8_out);
  or or_7 (Request_KBD, basic_controller_1_req_kbd, wait_KBD);
  D_Flip_Flop d_ff_1 (.clk(CLK), .D(CLK), .Q(d_ff_1_q), .reset(and_8_out));  // open: Qn, preset, en
  or or_8 (Waiting_IO, wait_KBD, SPI_communication_in_progress);
  or or_9 (or_9_out, and_11_out, spi_module_master_1_communication_end);
  and and_8 (and_8_out, ~CLK, d_ff_1_q);  // AND_Gate
  or or_10 (SPI_communication_in_progress, demultiplexer_2_out0[6], demultiplexer_2_out0[5], demultiplexer_2_out0[4], demultiplexer_2_out0[3], demultiplexer_2_out0[2], demultiplexer_2_out0[1], demultiplexer_2_out0[0]);
  or or_11 (Request_KBD_energy, basic_controller_1_req_kbd_num, and_9_out);
  and and_9 (and_9_out, demultiplexer_2_out1[0], wait_KBD);
  assign {controlled_buffer_9_out, controlled_buffer_18_out} = and_11_out ? {KBD_energy_increment, KBD_command} : 16'bz;  // Controlled_Buffer controlled_buffer_18
  assign {controlled_buffer_9_out, controlled_buffer_18_out} = spi_module_master_1_communication_end ? spi_module_master_1_recv_data : 16'bz;  // Controlled_Buffer controlled_buffer_19
  and and_10 (and_10_out, CLK, SPI_communication_in_progress, ~SPI_busy);  // AND_Gate
  LED led_1 (.in(spi_module_master_1_input_transanction_end));
  Pull_Resistor pull_resistor_1 (.node(SPI_busy));
  LED led_2 (.in(spi_module_master_1_communication_end));
  LED led_3 (.in(spi_module_master_1_output_transanction_end));
  and and_11 (and_11_out, wait_KBD, KBD_Ready);
  SPI_module__master spi_module_master_1 (
    .In_clock(and_10_out), .MISO(MISO), .CLK(SPI_clock), .MOSI(MOSI),
    .Output_transanction_end(spi_module_master_1_output_transanction_end),
    .Input_transanction_end(spi_module_master_1_input_transanction_end),
    .Control_command({wait_KBD, register_6_q}), .Send_command(register_7_q[4:0]),
    .Send_energy({register_8_q, register_7_q[7:5]}), .Recv_data(spi_module_master_1_recv_data),
    .Communication_end(spi_module_master_1_communication_end));
  Pull_Resistor pull_resistor_2 (.node(MISO));

  // Other names for the same wires on the sheet: wait_IO = Waiting_IO; wait_SPI = SPI_communication_in_progress

  // Notes on the sheet:
  //   contents of rom_1 (hex, n*v repeats v):
  //   d0 f9 d1 ff a1 d0 ff d1 ff a1 88 a1 d0 fc d1 2e a1 d0 fb d1 10 a1 d0 fc d1 c a1 d0 f9 d1 0 a1 d0 ff
  //   d1 0 a1 88 a1 d0 ea d1 1 a1 d2 ff a9 88 a1 8a a9 d0 fc d1 26 a1 d0 fc d1 80 a1 d0 fb b1 d0 10 71 e1
  //   55 0 d0 f9 d1 18 a1 d0 e9 b1 9d a1 d0 fe a1 ee 33 d0 11 71 e1 6a 0 d0 f9 d1 3 a1 d0 ea b1 9d a1 d0
  //   ff a1 ee 33 d0 12 71 e1 82 0 d0 f9 d1 c0 a1 d0 ea b1 91 e3 7c 91 a1 d0 ff a1 ee 33 d0 13 71 e1 9a 0
  //   d0 f9 d1 24 a1 d0 e9 b1 91 e3 94 91 a1 d0 fe a1 ee 33 d0 8 71 e1 d7 d0 ff d1 0 a1 d2 ea b9 a1 d0 fc
  //   d1 2e a1 d0 f9 d1 42 a1 d0 fc d1 81 a1 d0 fb b1 d2 8 56 a2 d0 fc d1 4 a1 d0 fb b1 d0 f9 d2 d0 56 a2
  //   d0 ff d1 0 a1 d2 ea b9 a1 ee 33 d0 f9 d1 c3 a1 d1 0 d0 ff a1 d0 ea b1 d0 ff a1 ee 33
endmodule
