// Logisim project SPI interface.circ as structural Verilog
module SPI_module__cell (
  input  CS,
  input  CLK,
  input  MOSI,
  input  err,
  input  [10:0] energy_in,
  input  [3:0] type_select_in,
  input  [1:0] player_select_in,
  output clk_out,
  output is_selected,
  output move_end_1,
  output move_end_2,
  output [1:0] is_task,
  output task_conf,
  output [4:0] command,
  output [10:0] energy_out,
  output input_transanction_end,
  output [1:0] type_select_out,
  output [1:0] player_select_out,
  output MISO,
  output output_transanction_end
);

  wire and_3_out, and_4_out, and_5_out, command_decoder_1_is_direction, command_decoder_1_is_energy,
       command_decoder_1_is_player, command_decoder_1_is_task, command_decoder_1_is_type,
       command_decoder_1_is_write, not_1_out, or_1_out, or_2_out, or_3_out, or_4_out,
       special_sequence_decoder_1_err, special_sequence_decoder_1_is_transancition,
       transanction_sender_1_miso;
  wire [3:0] input_shifter_1_buffer_ptr;
  wire [10:0] transaction_parser_1_energy;
  wire [15:0] input_shifter_1_data_out;

  and and_1 (clk_out, CS, CLK);
  not not_1 (not_1_out, CS);
  or or_1 (or_1_out, not_1_out, special_sequence_decoder_1_is_transancition);
  or or_2 (or_2_out, not_1_out, ~special_sequence_decoder_1_is_transancition);  // OR_Gate
  transaction_parser transaction_parser_1 (
    .CLK(clk_out), .MOSI(MOSI), .Reset(or_2_out), .Command(command), .Energy(transaction_parser_1_energy),
    .Data_ready(input_transanction_end));
  input_shifter input_shifter_1 (
    .MOSI(MOSI), .CLK(clk_out), .Reset(or_1_out), .Data_out(input_shifter_1_data_out),
    .buffer_ptr(input_shifter_1_buffer_ptr));
  special_sequence_decoder special_sequence_decoder_1 (
    .Data(input_shifter_1_data_out), .Buffer_pointer(input_shifter_1_buffer_ptr), .RST(not_1_out),
    .move_end_1(move_end_1), .is_transancition(special_sequence_decoder_1_is_transancition),
    .move_end_2(move_end_2), .is_task(is_task), .is_selected(is_selected),
    .ERR(special_sequence_decoder_1_err), .CLK(clk_out));
  or or_3 (or_3_out, is_task[0], is_task[1]);
  and and_2 (task_conf, or_3_out, clk_out, MOSI);
  command_decoder command_decoder_1 (
    .Command_in(command), .is_direction(command_decoder_1_is_direction),
    .is_energy(command_decoder_1_is_energy), .is_type(command_decoder_1_is_type),
    .is_task(command_decoder_1_is_task), .is_player(command_decoder_1_is_player),
    .is_write(command_decoder_1_is_write));  // open: direction, is_clear
  or or_4 (or_4_out, command_decoder_1_is_direction, command_decoder_1_is_energy);
  and and_3 (and_3_out, or_3_out, err);
  and and_4 (and_4_out, command_decoder_1_is_write, err, input_transanction_end);
  and and_5 (and_5_out, ~command_decoder_1_is_write, input_transanction_end);  // AND_Gate
  transanction_sender transanction_sender_1 (
    .CLK(clk_out), .Energy(energy_in), .Type_select(type_select_in[1:0]), .Task_select(type_select_in[3:2]),
    .Player_select(player_select_in), .Input_transaction_end__not_Reset(and_5_out),
    .MISO(transanction_sender_1_miso), .Output_transanction_end(output_transanction_end),
    .Is_player(command_decoder_1_is_player), .Is_task(command_decoder_1_is_task),
    .Is_type(command_decoder_1_is_type), .Is_energy(or_4_out));
  Multiplexer #(.width(11), .enable("false")) multiplexer_1 (
    .in0({11{1'b0}}), .in1(transaction_parser_1_energy), .out(energy_out), .sel(or_4_out));
  Multiplexer #(.width(2), .enable("false")) multiplexer_2 (
    .in0(2'b00), .in1(transaction_parser_1_energy[1:0]), .out(type_select_out),
    .sel(command_decoder_1_is_type));
  Multiplexer #(.width(2), .enable("false")) multiplexer_3 (
    .in0(2'b00), .in1(transaction_parser_1_energy[1:0]), .out(player_select_out),
    .sel(command_decoder_1_is_player));
  or or_5 (MISO, special_sequence_decoder_1_err, and_3_out, and_4_out, transanction_sender_1_miso);

  // Other names for the same wires on the sheet: clk_t = clk_out; input_transaction_end = input_transanction_end

  // Notes on the sheet:
  //   player_select_out: pull=down
  //   type_select_out: pull=down
  //   energy_out: pull=down
  //   is_task: pull=down
  //   command: pull=down
  //   energy_in: pull=down
  //   MOSI: pull=down
  //   CLK: pull=down
  //   type_select_in: pull=down
  //   err: pull=down
  //   player_select_in: pull=down
endmodule

module input_shifter (
  input  MOSI,
  input  CLK,
  input  Reset,
  output [15:0] Data_out,
  output [3:0] buffer_ptr
);

  Register #(.width(16)) register_1 (.D({Data_out[14:0], MOSI}), .en(1'b1), .Q(Data_out), .clk(CLK), .clr(Reset));
  Counter #(.width(4), .max('hf)) counter_1 (
    .load(1'b0), .count(1'b1), .Q(buffer_ptr), .clk(CLK), .clr(Reset));  // open: D, carry

  // Notes on the sheet:
  //   Reset: pull=down
  //   Data_out: pull=down
  //   MOSI: pull=down
  //   buffer_ptr: pull=down
  //   CLK: pull=down
endmodule

module special_sequence_decoder (
  input  [15:0] Data,
  input  [3:0] Buffer_pointer,
  input  CLK,
  input  RST,
  output move_end_1,
  output is_transancition,
  output is_selected,
  output move_end_2,
  output [1:0] is_task,
  output ERR
);

  wire and_1_out, and_2_out, and_3_out, and_4_out, and_5_out, and_6_out, and_7_out, comparator_1_eq,
       comparator_2_eq, comparator_3_eq, comparator_4_eq, comparator_5_eq, comparator_6_eq, comparator_6_gt,
       lock, or_1_out, or_2_out;

  Comparator #(.width(16)) comparator_1 (.a(Data), .b(16'h1), .eq(comparator_1_eq));  // open: gt, lt
  Comparator #(.width(16)) comparator_2 (.a(Data), .b(16'h3), .eq(comparator_2_eq));  // open: gt, lt
  Comparator #(.width(4)) comparator_3 (.a(Buffer_pointer), .b(4'b0001), .eq(comparator_3_eq));  // open: gt, lt
  Comparator #(.width(4)) comparator_4 (.a(Buffer_pointer), .b(4'b0010), .eq(comparator_4_eq));  // open: gt, lt
  Comparator #(.width(4)) comparator_5 (.a(Buffer_pointer), .b(4'b0011), .eq(comparator_5_eq));  // open: gt, lt
  Comparator #(.width(4)) comparator_6 (
    .a(Buffer_pointer), .b(4'b0101), .gt(comparator_6_gt), .eq(comparator_6_eq));  // open: lt
  and and_1 (and_1_out, comparator_1_eq, comparator_3_eq);
  and and_2 (and_2_out, comparator_1_eq, comparator_4_eq);
  and and_3 (and_3_out, comparator_1_eq, comparator_5_eq);
  and and_4 (and_4_out, comparator_2_eq, comparator_4_eq);
  and and_5 (and_5_out, comparator_6_eq, Data[0]);
  and and_6 (and_6_out, Data[1], comparator_6_eq);
  or or_1 (or_1_out, comparator_6_gt, and_6_out, and_5_out, and_4_out, and_3_out, and_2_out);
  and and_7 (and_7_out, ~lock, CLK);  // AND_Gate
  D_Flip_Flop d_ff_1 (.clk(lock), .D(and_2_out), .Q(is_transancition), .reset(RST));  // open: Qn, preset, en
  D_Flip_Flop d_ff_2 (.clk(lock), .D(and_3_out), .Q(is_selected), .reset(RST));  // open: Qn, preset, en
  D_Flip_Flop d_ff_3 (.clk(lock), .D(and_4_out), .Q(move_end_2), .reset(RST));  // open: Qn, preset, en
  D_Flip_Flop d_ff_4 (.clk(lock), .D(and_5_out), .Q(is_task[0]), .reset(RST));  // open: Qn, preset, en
  D_Flip_Flop d_ff_5 (.clk(lock), .D(and_6_out), .Q(is_task[1]), .reset(RST));  // open: Qn, preset, en
  D_Flip_Flop #(.trigger("falling")) d_ff_6 (
    .clk(and_7_out), .D(or_1_out), .Q(lock), .reset(RST));  // open: Qn, preset, en
  and and_8 (move_end_1, ~lock, and_1_out);  // AND_Gate
  or or_2 (or_2_out, is_task[0], is_task[1], move_end_2, is_selected, is_transancition);
  and and_9 (ERR, ~or_2_out, lock);  // AND_Gate

  // Notes on the sheet:
  //   ERR: pull=down
  //   CLK: pull=down
  //   RST: pull=down
  //   Data: pull=down
  //   Buffer_pointer: pull=down
endmodule

module transaction_parser (
  input  CLK,
  input  MOSI,
  input  Reset,
  output [4:0] Command,
  output [10:0] Energy,
  output Data_ready
);

  wire and_1_out, and_2_out, and_3_out, and_4_out, and_5_out, and_6_out, and_7_out,
       command_decoder_1_is_clear, command_decoder_1_is_direction, command_decoder_1_is_energy,
       command_decoder_1_is_player, command_decoder_1_is_type, command_decoder_1_is_write, comparator_1_eq,
       comparator_2_eq, d_ff_1_q, nor_1_out, or_1_out, or_2_out, or_3_out;
  wire [3:0] input_shifter_1_buffer_ptr;
  wire [15:11] input_shifter_1_data_out;

  and and_1 (and_1_out, ~Data_ready, CLK);  // AND_Gate
  input_shifter input_shifter_1 (
    .MOSI(MOSI), .CLK(and_1_out), .Reset(Reset), .Data_out({input_shifter_1_data_out, Energy}),
    .buffer_ptr(input_shifter_1_buffer_ptr));
  Comparator #(.width(4)) comparator_1 (
    .a(input_shifter_1_buffer_ptr), .b(4'b0101), .eq(comparator_1_eq));  // open: gt, lt
  Comparator #(.width(4)) comparator_2 (
    .a(input_shifter_1_buffer_ptr), .b(4'b0111), .eq(comparator_2_eq));  // open: gt, lt
  command_decoder command_decoder_1 (
    .Command_in(Command), .is_direction(command_decoder_1_is_direction),
    .is_energy(command_decoder_1_is_energy), .is_type(command_decoder_1_is_type),
    .is_clear(command_decoder_1_is_clear), .is_player(command_decoder_1_is_player),
    .is_write(command_decoder_1_is_write));  // open: direction, is_task
  nor nor_1 (nor_1_out, input_shifter_1_buffer_ptr[0], input_shifter_1_buffer_ptr[1], input_shifter_1_buffer_ptr[3], input_shifter_1_buffer_ptr[2]);
  or or_1 (or_1_out, command_decoder_1_is_direction, command_decoder_1_is_energy);
  or or_2 (or_2_out, command_decoder_1_is_type, command_decoder_1_is_player);
  and and_2 (and_2_out, ~d_ff_1_q, and_1_out);  // AND_Gate
  Register #(.width(5)) register_1 (.D(Energy[4:0]), .en(1'b1), .Q(Command), .clk(d_ff_1_q), .clr(Reset));
  and and_3 (and_3_out, comparator_1_eq, command_decoder_1_is_clear);
  and and_4 (and_4_out, nor_1_out, or_1_out);
  and and_5 (and_5_out, comparator_2_eq, or_2_out);
  D_Flip_Flop #(.trigger("falling")) d_ff_1 (
    .clk(and_2_out), .D(comparator_1_eq), .Q(d_ff_1_q), .reset(Reset));  // open: Qn, preset, en
  or or_3 (or_3_out, and_3_out, and_4_out, and_5_out);
  and and_6 (and_6_out, d_ff_1_q, or_3_out);
  and and_7 (and_7_out, ~command_decoder_1_is_write, d_ff_1_q);  // AND_Gate
  or or_4 (Data_ready, and_7_out, and_6_out);
endmodule

module command_decoder (
  input  [4:0] Command_in,
  output [1:0] direction,
  output is_direction,
  output is_energy,
  output is_type,
  output is_task,
  output is_clear,
  output is_player,
  output is_write
);

  wire demultiplexer_1_out2, not_1_out;

  Multiplexer #(.width(2), .enable("false")) multiplexer_1 (
    .in0(2'b00), .in1(Command_in[1:0]), .out(direction), .sel(Command_in[2]));
  not not_1 (not_1_out, Command_in[2]);
  Demultiplexer #(.select(2), .enable("false")) demultiplexer_1 (
    .out0(is_energy), .out1(is_type), .out2(demultiplexer_1_out2), .out3(is_player), .in(not_1_out),
    .sel(Command_in[1:0]));
  Demultiplexer #(.enable("false")) demultiplexer_2 (
    .out0(is_task), .out1(is_clear), .in(demultiplexer_1_out2), .sel(Command_in[3]));

  assign is_direction = Command_in[2];
  assign is_write = Command_in[3];

  // Notes on the sheet:
  //   Command_in: pull=down
  //   is_type: pull=down
  //   is_energy: pull=down
  //   is_clear: pull=down
  //   is_task: pull=down
  //   is_direction: pull=down
  //   direction: pull=down
  //   is_player: pull=down
  //   is_write: pull=down
endmodule

module output_shifter (
  input  [10:0] Data_in,
  input  CLK,
  input  Reset,
  output MISO,
  output [3:0] buffer_ptr
);

  wire and_1_out, and_2_out, comparator_1_eq, d_ff_1_q, or_1_out;
  wire [9:0] register_1_q;
  wire [10:0] multiplexer_1_out;

  and and_1 (and_1_out, ~CLK, d_ff_1_q);  // AND_Gate
  D_Flip_Flop d_ff_1 (.clk(CLK), .D(CLK), .Q(d_ff_1_q), .reset(and_1_out));  // open: Qn, preset, en
  Counter #(.width(4), .max('hf)) counter_1 (
    .load(1'b0), .count(1'b1), .Q(buffer_ptr), .clk(CLK), .clr(Reset));  // open: D, carry
  Comparator #(.width(4), .mode("unsigned")) comparator_1 (
    .a(4'b0000), .b(buffer_ptr), .eq(comparator_1_eq));  // open: gt, lt
  Multiplexer #(.width(11), .enable("false")) multiplexer_1 (
    .in0({1'b0, register_1_q}), .in1(Data_in), .out(multiplexer_1_out), .sel(comparator_1_eq));
  and and_2 (and_2_out, comparator_1_eq, ~Reset);  // AND_Gate
  Register #(.width(11), .trigger("high")) register_1 (
    .D(multiplexer_1_out), .en(1'b1), .Q({register_1_q, MISO}), .clk(or_1_out), .clr(Reset));
  or or_1 (or_1_out, and_1_out, and_2_out);
  // Probe on {register_1_q, MISO}

  // Notes on the sheet:
  //   MISO: pull=down
  //   CLK: pull=down
  //   buffer_ptr: pull=down
  //   Reset: pull=down
  //   Data_in: pull=down
endmodule

module transanction_sender (
  input  Is_player,
  input  Is_task,
  input  Is_type,
  input  Is_energy,
  input  CLK,
  input  [10:0] Energy,
  input  [1:0] Type_select,
  input  [1:0] Task_select,
  input  [1:0] Player_select,
  input  Input_transaction_end__not_Reset,
  output MISO,
  output Output_transanction_end
);

  wire and_1_out, and_2_out, comparator_1_eq, comparator_2_eq, d_ff_1_q, not_1_out, or_1_out, or_3_out;
  wire [1:0] controlled_buffer_1_out;
  wire [3:0] output_shifter_1_buffer_ptr;
  wire [10:0] multiplexer_1_out, or_2_out;

  assign controlled_buffer_1_out = Is_task ? Task_select : 2'bz;  // Controlled_Buffer controlled_buffer_1
  assign controlled_buffer_1_out = Is_player ? Player_select : 2'bz;  // Controlled_Buffer controlled_buffer_2
  assign controlled_buffer_1_out = Is_type ? Type_select : 2'bz;  // Controlled_Buffer controlled_buffer_3
  or or_1 (or_1_out, Is_player, Is_task, Is_type);
  Multiplexer #(.width(11), .enable("false")) multiplexer_1 (
    .in0({11{1'b0}}), .in1(Energy), .out(multiplexer_1_out), .sel(Is_energy));
  Pull_Resistor pull_resistor_1 (.node(controlled_buffer_1_out));
  assign or_2_out = multiplexer_1_out | {{9{1'b0}}, controlled_buffer_1_out};  // OR_Gate or_2, 11 bits wide
  or or_3 (or_3_out, not_1_out, d_ff_1_q);
  not not_1 (not_1_out, Input_transaction_end__not_Reset);
  output_shifter output_shifter_1 (
    .Data_in(or_2_out), .CLK(CLK), .Reset(or_3_out), .MISO(MISO), .buffer_ptr(output_shifter_1_buffer_ptr));
  and and_1 (and_1_out, ~d_ff_1_q, CLK);  // AND_Gate
  and and_2 (and_2_out, or_1_out, comparator_1_eq);
  Comparator #(.width(4), .mode("unsigned")) comparator_1 (
    .a(output_shifter_1_buffer_ptr), .b(4'b0010), .eq(comparator_1_eq));  // open: gt, lt
  Comparator #(.width(4), .mode("unsigned")) comparator_2 (
    .a(output_shifter_1_buffer_ptr), .b(4'b1011), .eq(comparator_2_eq));  // open: gt, lt
  D_Flip_Flop #(.trigger("falling")) d_ff_1 (
    .clk(and_1_out), .D(Output_transanction_end), .Q(d_ff_1_q), .reset(not_1_out));  // open: Qn, preset, en
  or or_4 (Output_transanction_end, and_2_out, d_ff_1_q, comparator_2_eq);

  // Notes on the sheet:
  //   Output_transanction_end: pull=down
  //   MISO: pull=down
endmodule
