// Logisim project cell controller.circ as structural Verilog: 2 circuits, main circuit Cell controller
module Cell_controller (
  input  CSR,
  input  [11:0] in_2,
  input  CSC,
  input  [1:0] SPI,
  input  [11:0] in_5,
  input  [11:0] in_6,
  input  [11:0] in_7,
  output [11:0] out_8,
  output MISO,
  output [11:0] out_10,
  output [11:0] out_11,
  output [11:0] out_12,
  output [4:0] out_13,
  output [4:0] out_14,
  output [4:0] out_15,
  output [4:0] out_16,
  output [4:0] out_17,
  output [4:0] out_18,
  output [4:0] out_19,
  output [4:0] out_20,
  output [4:0] out_21,
  output [4:0] out_22,
  output [4:0] out_23,
  output [7:0] out_24,
  output [7:0] out_25,
  output [7:0] out_26,
  output [7:0] out_27,
  output [7:0] out_28,
  output [7:0] out_29,
  output [7:0] out_30,
  output [7:0] out_31,
  output [7:0] out_32,
  output [7:0] out_33,
  output [7:0] out_34,
  output [7:0] out_35,
  output [7:0] out_36,
  output [7:0] out_37,
  output [7:0] out_38,
  output [7:0] out_39,
  output [7:0] out_40,
  output [7:0] out_41,
  output [7:0] out_42,
  output [7:0] out_43,
  output [7:0] out_44,
  output [7:0] out_45
);


  assign out_13 = 5'b10101;
  assign out_14 = 5'b01010;
  assign out_15 = 5'b10101;
  assign out_16 = 5'b01010;
  assign out_17 = 5'b10101;
  assign out_18 = 5'b01010;
  assign out_19 = 5'b10101;
  assign out_20 = 5'b01010;
  assign out_21 = 5'b10101;
  assign out_22 = 5'b01010;
  assign out_23 = 5'b10101;
  assign out_24 = 8'h25;
  assign out_25 = 8'h31;
  assign out_26 = 8'h1;
  assign out_27 = 8'h25;
  assign out_28 = 8'h31;
  assign out_29 = 8'h1;
  assign out_30 = 8'h25;
  assign out_31 = 8'h31;
  assign out_32 = 8'h1;
  assign out_33 = 8'h25;
  assign out_34 = 8'h31;
  assign out_35 = 8'ha;
  assign out_36 = 8'h6;
  assign out_37 = 8'hfe;
  assign out_38 = 8'ha;
  assign out_39 = 8'h6;
  assign out_40 = 8'hfe;
  assign out_41 = 8'ha;
  assign out_42 = 8'h6;
  assign out_43 = 8'hfe;
  assign out_44 = 8'ha;
  assign out_45 = 8'h6;

  // Notes on the sheet:
  //   Number mtx output
  //   Orange mtx output
  //   Blue mtx output
endmodule

module local_test (
);

  wire undriven, undriven_2, undriven_4, undriven_6;
  wire [2:0] undriven_3, undriven_5;
  wire [4:0] cell_controller_1_out_13, cell_controller_1_out_14, cell_controller_1_out_15,
       cell_controller_1_out_16, cell_controller_1_out_17, cell_controller_1_out_18,
       cell_controller_1_out_19, cell_controller_1_out_20, cell_controller_1_out_21,
       cell_controller_1_out_22, cell_controller_1_out_23, cell_controller_2_out_13,
       cell_controller_2_out_14, cell_controller_2_out_15, cell_controller_2_out_16,
       cell_controller_2_out_17, cell_controller_2_out_18, cell_controller_2_out_19,
       cell_controller_2_out_20, cell_controller_2_out_21, cell_controller_2_out_22,
       cell_controller_2_out_23, cell_controller_3_out_13, cell_controller_3_out_14,
       cell_controller_3_out_15, cell_controller_3_out_16, cell_controller_3_out_17,
       cell_controller_3_out_18, cell_controller_3_out_19, cell_controller_3_out_20,
       cell_controller_3_out_21, cell_controller_3_out_22, cell_controller_3_out_23,
       cell_controller_4_out_13, cell_controller_4_out_14, cell_controller_4_out_15,
       cell_controller_4_out_16, cell_controller_4_out_17, cell_controller_4_out_18,
       cell_controller_4_out_19, cell_controller_4_out_20, cell_controller_4_out_21,
       cell_controller_4_out_22, cell_controller_4_out_23;
  wire [7:0] cell_controller_1_out_24, cell_controller_1_out_25, cell_controller_1_out_26,
       cell_controller_1_out_27, cell_controller_1_out_28, cell_controller_1_out_29,
       cell_controller_1_out_30, cell_controller_1_out_31, cell_controller_1_out_32,
       cell_controller_1_out_33, cell_controller_1_out_34, cell_controller_1_out_35,
       cell_controller_1_out_36, cell_controller_1_out_37, cell_controller_1_out_38,
       cell_controller_1_out_39, cell_controller_1_out_40, cell_controller_1_out_41,
       cell_controller_1_out_42, cell_controller_1_out_43, cell_controller_1_out_44,
       cell_controller_1_out_45, cell_controller_2_out_24, cell_controller_2_out_25,
       cell_controller_2_out_26, cell_controller_2_out_27, cell_controller_2_out_28,
       cell_controller_2_out_29, cell_controller_2_out_30, cell_controller_2_out_31,
       cell_controller_2_out_32, cell_controller_2_out_33, cell_controller_2_out_34,
       cell_controller_2_out_35, cell_controller_2_out_36, cell_controller_2_out_37,
       cell_controller_2_out_38, cell_controller_2_out_39, cell_controller_2_out_40,
       cell_controller_2_out_41, cell_controller_2_out_42, cell_controller_2_out_43,
       cell_controller_2_out_44, cell_controller_2_out_45, cell_controller_3_out_24,
       cell_controller_3_out_25, cell_controller_3_out_26, cell_controller_3_out_27,
       cell_controller_3_out_28, cell_controller_3_out_29, cell_controller_3_out_30,
       cell_controller_3_out_31, cell_controller_3_out_32, cell_controller_3_out_33,
       cell_controller_3_out_34, cell_controller_3_out_35, cell_controller_3_out_36,
       cell_controller_3_out_37, cell_controller_3_out_38, cell_controller_3_out_39,
       cell_controller_3_out_40, cell_controller_3_out_41, cell_controller_3_out_42,
       cell_controller_3_out_43, cell_controller_3_out_44, cell_controller_3_out_45,
       cell_controller_4_out_24, cell_controller_4_out_25, cell_controller_4_out_26,
       cell_controller_4_out_27, cell_controller_4_out_28, cell_controller_4_out_29,
       cell_controller_4_out_30, cell_controller_4_out_31, cell_controller_4_out_32,
       cell_controller_4_out_33, cell_controller_4_out_34, cell_controller_4_out_35,
       cell_controller_4_out_36, cell_controller_4_out_37, cell_controller_4_out_38,
       cell_controller_4_out_39, cell_controller_4_out_40, cell_controller_4_out_41,
       cell_controller_4_out_42, cell_controller_4_out_43, cell_controller_4_out_44, cell_controller_4_out_45;

  Cell_controller cell_controller_1 (
    .out_13(cell_controller_1_out_13), .out_24(cell_controller_1_out_24), .out_14(cell_controller_1_out_14),
    .out_35(cell_controller_1_out_35), .out_25(cell_controller_1_out_25), .out_15(cell_controller_1_out_15),
    .out_36(cell_controller_1_out_36), .out_26(cell_controller_1_out_26), .out_16(cell_controller_1_out_16),
    .out_37(cell_controller_1_out_37), .out_17(cell_controller_1_out_17), .out_27(cell_controller_1_out_27),
    .out_38(cell_controller_1_out_38), .out_18(cell_controller_1_out_18), .out_28(cell_controller_1_out_28),
    .out_19(cell_controller_1_out_19), .out_39(cell_controller_1_out_39), .out_29(cell_controller_1_out_29),
    .out_20(cell_controller_1_out_20), .out_40(cell_controller_1_out_40), .out_30(cell_controller_1_out_30),
    .out_21(cell_controller_1_out_21), .out_41(cell_controller_1_out_41), .out_22(cell_controller_1_out_22),
    .out_31(cell_controller_1_out_31), .out_42(cell_controller_1_out_42), .out_23(cell_controller_1_out_23),
    .out_32(cell_controller_1_out_32), .out_43(cell_controller_1_out_43), .out_33(cell_controller_1_out_33),
    .out_44(cell_controller_1_out_44), .out_34(cell_controller_1_out_34), .out_45(cell_controller_1_out_45),
    .CSC(undriven_4), .CSR(undriven_2), .MISO(undriven_3[2]), .SPI(undriven_3[1:0]));  // open: in_5, out_11, in_2, out_8, in_6, out_10, in_7, out_12
  DotMatrix #(.matrixcols(11), .matrixrows(5)) dotmatrix_1 (
    .col0(cell_controller_1_out_13), .col1(cell_controller_1_out_14), .col2(cell_controller_1_out_15),
    .col3(cell_controller_1_out_16), .col4(cell_controller_1_out_17), .col5(cell_controller_1_out_18),
    .col6(cell_controller_1_out_19), .col7(cell_controller_1_out_20), .col8(cell_controller_1_out_21),
    .col9(cell_controller_1_out_22), .col10(cell_controller_1_out_23));
  DotMatrix #(.matrixcols(11), .matrixrows(8)) dotmatrix_2 (
    .col0(cell_controller_1_out_24), .col1(cell_controller_1_out_25), .col2(cell_controller_1_out_26),
    .col3(cell_controller_1_out_27), .col4(cell_controller_1_out_28), .col5(cell_controller_1_out_29),
    .col6(cell_controller_1_out_30), .col7(cell_controller_1_out_31), .col8(cell_controller_1_out_32),
    .col9(cell_controller_1_out_33), .col10(cell_controller_1_out_34));
  DotMatrix #(.matrixcols(11), .matrixrows(8)) dotmatrix_3 (
    .col0(cell_controller_1_out_35), .col1(cell_controller_1_out_36), .col2(cell_controller_1_out_37),
    .col3(cell_controller_1_out_38), .col4(cell_controller_1_out_39), .col5(cell_controller_1_out_40),
    .col6(cell_controller_1_out_41), .col7(cell_controller_1_out_42), .col8(cell_controller_1_out_43),
    .col9(cell_controller_1_out_44), .col10(cell_controller_1_out_45));
  Cell_controller cell_controller_2 (
    .out_13(cell_controller_2_out_13), .out_24(cell_controller_2_out_24), .out_14(cell_controller_2_out_14),
    .out_35(cell_controller_2_out_35), .out_25(cell_controller_2_out_25), .out_15(cell_controller_2_out_15),
    .out_36(cell_controller_2_out_36), .out_26(cell_controller_2_out_26), .out_16(cell_controller_2_out_16),
    .out_37(cell_controller_2_out_37), .out_17(cell_controller_2_out_17), .out_27(cell_controller_2_out_27),
    .out_38(cell_controller_2_out_38), .out_18(cell_controller_2_out_18), .out_28(cell_controller_2_out_28),
    .out_19(cell_controller_2_out_19), .out_39(cell_controller_2_out_39), .out_29(cell_controller_2_out_29),
    .out_20(cell_controller_2_out_20), .out_40(cell_controller_2_out_40), .out_30(cell_controller_2_out_30),
    .out_21(cell_controller_2_out_21), .out_41(cell_controller_2_out_41), .out_22(cell_controller_2_out_22),
    .out_31(cell_controller_2_out_31), .out_42(cell_controller_2_out_42), .out_23(cell_controller_2_out_23),
    .out_32(cell_controller_2_out_32), .out_43(cell_controller_2_out_43), .out_33(cell_controller_2_out_33),
    .out_44(cell_controller_2_out_44), .out_34(cell_controller_2_out_34), .out_45(cell_controller_2_out_45),
    .CSC(undriven_4), .CSR(undriven), .MISO(undriven_3[2]), .SPI(undriven_3[1:0]));  // open: in_5, out_11, in_2, out_8, in_6, out_10, in_7, out_12
  DotMatrix #(.matrixcols(11), .matrixrows(5)) dotmatrix_4 (
    .col0(cell_controller_2_out_13), .col1(cell_controller_2_out_14), .col2(cell_controller_2_out_15),
    .col3(cell_controller_2_out_16), .col4(cell_controller_2_out_17), .col5(cell_controller_2_out_18),
    .col6(cell_controller_2_out_19), .col7(cell_controller_2_out_20), .col8(cell_controller_2_out_21),
    .col9(cell_controller_2_out_22), .col10(cell_controller_2_out_23));
  DotMatrix #(.matrixcols(11), .matrixrows(8)) dotmatrix_5 (
    .col0(cell_controller_2_out_24), .col1(cell_controller_2_out_25), .col2(cell_controller_2_out_26),
    .col3(cell_controller_2_out_27), .col4(cell_controller_2_out_28), .col5(cell_controller_2_out_29),
    .col6(cell_controller_2_out_30), .col7(cell_controller_2_out_31), .col8(cell_controller_2_out_32),
    .col9(cell_controller_2_out_33), .col10(cell_controller_2_out_34));
  DotMatrix #(.matrixcols(11), .matrixrows(8)) dotmatrix_6 (
    .col0(cell_controller_2_out_35), .col1(cell_controller_2_out_36), .col2(cell_controller_2_out_37),
    .col3(cell_controller_2_out_38), .col4(cell_controller_2_out_39), .col5(cell_controller_2_out_40),
    .col6(cell_controller_2_out_41), .col7(cell_controller_2_out_42), .col8(cell_controller_2_out_43),
    .col9(cell_controller_2_out_44), .col10(cell_controller_2_out_45));
  DotMatrix #(.matrixcols(11), .matrixrows(5)) dotmatrix_7 (
    .col0(cell_controller_3_out_13), .col1(cell_controller_3_out_14), .col2(cell_controller_3_out_15),
    .col3(cell_controller_3_out_16), .col4(cell_controller_3_out_17), .col5(cell_controller_3_out_18),
    .col6(cell_controller_3_out_19), .col7(cell_controller_3_out_20), .col8(cell_controller_3_out_21),
    .col9(cell_controller_3_out_22), .col10(cell_controller_3_out_23));
  Cell_controller cell_controller_3 (
    .out_13(cell_controller_3_out_13), .out_24(cell_controller_3_out_24), .out_14(cell_controller_3_out_14),
    .out_35(cell_controller_3_out_35), .out_25(cell_controller_3_out_25), .out_15(cell_controller_3_out_15),
    .out_36(cell_controller_3_out_36), .out_26(cell_controller_3_out_26), .out_16(cell_controller_3_out_16),
    .out_37(cell_controller_3_out_37), .out_17(cell_controller_3_out_17), .out_27(cell_controller_3_out_27),
    .out_38(cell_controller_3_out_38), .out_18(cell_controller_3_out_18), .out_28(cell_controller_3_out_28),
    .out_19(cell_controller_3_out_19), .out_39(cell_controller_3_out_39), .out_29(cell_controller_3_out_29),
    .out_20(cell_controller_3_out_20), .out_40(cell_controller_3_out_40), .out_30(cell_controller_3_out_30),
    .out_21(cell_controller_3_out_21), .out_41(cell_controller_3_out_41), .out_22(cell_controller_3_out_22),
    .out_31(cell_controller_3_out_31), .out_42(cell_controller_3_out_42), .out_23(cell_controller_3_out_23),
    .out_32(cell_controller_3_out_32), .out_43(cell_controller_3_out_43), .out_33(cell_controller_3_out_33),
    .out_44(cell_controller_3_out_44), .out_34(cell_controller_3_out_34), .out_45(cell_controller_3_out_45),
    .CSC(undriven_6), .CSR(undriven_2), .MISO(undriven_5[2]), .SPI(undriven_5[1:0]));  // open: in_5, out_11, in_2, out_8, in_6, out_10, in_7, out_12
  DotMatrix #(.matrixcols(11), .matrixrows(8)) dotmatrix_8 (
    .col0(cell_controller_3_out_24), .col1(cell_controller_3_out_25), .col2(cell_controller_3_out_26),
    .col3(cell_controller_3_out_27), .col4(cell_controller_3_out_28), .col5(cell_controller_3_out_29),
    .col6(cell_controller_3_out_30), .col7(cell_controller_3_out_31), .col8(cell_controller_3_out_32),
    .col9(cell_controller_3_out_33), .col10(cell_controller_3_out_34));
  DotMatrix #(.matrixcols(11), .matrixrows(8)) dotmatrix_9 (
    .col0(cell_controller_3_out_35), .col1(cell_controller_3_out_36), .col2(cell_controller_3_out_37),
    .col3(cell_controller_3_out_38), .col4(cell_controller_3_out_39), .col5(cell_controller_3_out_40),
    .col6(cell_controller_3_out_41), .col7(cell_controller_3_out_42), .col8(cell_controller_3_out_43),
    .col9(cell_controller_3_out_44), .col10(cell_controller_3_out_45));
  Cell_controller cell_controller_4 (
    .out_13(cell_controller_4_out_13), .out_24(cell_controller_4_out_24), .out_14(cell_controller_4_out_14),
    .out_35(cell_controller_4_out_35), .out_25(cell_controller_4_out_25), .out_15(cell_controller_4_out_15),
    .out_36(cell_controller_4_out_36), .out_26(cell_controller_4_out_26), .out_16(cell_controller_4_out_16),
    .out_37(cell_controller_4_out_37), .out_17(cell_controller_4_out_17), .out_27(cell_controller_4_out_27),
    .out_38(cell_controller_4_out_38), .out_18(cell_controller_4_out_18), .out_28(cell_controller_4_out_28),
    .out_19(cell_controller_4_out_19), .out_39(cell_controller_4_out_39), .out_29(cell_controller_4_out_29),
    .out_20(cell_controller_4_out_20), .out_40(cell_controller_4_out_40), .out_30(cell_controller_4_out_30),
    .out_21(cell_controller_4_out_21), .out_41(cell_controller_4_out_41), .out_22(cell_controller_4_out_22),
    .out_31(cell_controller_4_out_31), .out_42(cell_controller_4_out_42), .out_23(cell_controller_4_out_23),
    .out_32(cell_controller_4_out_32), .out_43(cell_controller_4_out_43), .out_33(cell_controller_4_out_33),
    .out_44(cell_controller_4_out_44), .out_34(cell_controller_4_out_34), .out_45(cell_controller_4_out_45),
    .CSC(undriven_6), .CSR(undriven), .MISO(undriven_5[2]), .SPI(undriven_5[1:0]));  // open: in_5, out_11, in_2, out_8, in_6, out_10, in_7, out_12
  DotMatrix #(.matrixcols(11), .matrixrows(5)) dotmatrix_10 (
    .col0(cell_controller_4_out_13), .col1(cell_controller_4_out_14), .col2(cell_controller_4_out_15),
    .col3(cell_controller_4_out_16), .col4(cell_controller_4_out_17), .col5(cell_controller_4_out_18),
    .col6(cell_controller_4_out_19), .col7(cell_controller_4_out_20), .col8(cell_controller_4_out_21),
    .col9(cell_controller_4_out_22), .col10(cell_controller_4_out_23));
  DotMatrix #(.matrixcols(11), .matrixrows(8)) dotmatrix_11 (
    .col0(cell_controller_4_out_24), .col1(cell_controller_4_out_25), .col2(cell_controller_4_out_26),
    .col3(cell_controller_4_out_27), .col4(cell_controller_4_out_28), .col5(cell_controller_4_out_29),
    .col6(cell_controller_4_out_30), .col7(cell_controller_4_out_31), .col8(cell_controller_4_out_32),
    .col9(cell_controller_4_out_33), .col10(cell_controller_4_out_34));
  DotMatrix #(.matrixcols(11), .matrixrows(8)) dotmatrix_12 (
    .col0(cell_controller_4_out_35), .col1(cell_controller_4_out_36), .col2(cell_controller_4_out_37),
    .col3(cell_controller_4_out_38), .col4(cell_controller_4_out_39), .col5(cell_controller_4_out_40),
    .col6(cell_controller_4_out_41), .col7(cell_controller_4_out_42), .col8(cell_controller_4_out_43),
    .col9(cell_controller_4_out_44), .col10(cell_controller_4_out_45));
endmodule
