// Logisim project display controller.circ as structural Verilog: 26 circuits, main circuit Player_move
module Player_move (
  input  [1:0] in_1,
  output [7:0] out_2,
  output [7:0] out_3,
  output [7:0] out_4,
  output [7:0] out_5,
  output [7:0] out_6,
  output [7:0] out_7,
  output [7:0] out_8,
  output [7:0] out_9,
  output [7:0] out_10,
  output [7:0] out_11,
  output [7:0] out_12,
  output [7:0] out_13,
  output [7:0] out_14,
  output [7:0] out_15,
  output [7:0] out_16,
  output [7:0] out_17,
  output [7:0] out_18,
  output [7:0] out_19,
  output [7:0] out_20,
  output [7:0] out_21,
  output [7:0] out_22,
  output [7:0] out_23
);

  Transistor #(.width(8)) transistor_1 (.in({8{1'b0}}), .out(out_21), .gate(in_1[1]));
  Transistor #(.width(8)) transistor_2 (.in({8{1'b0}}), .out(out_23), .gate(in_1[1]));
  Transistor #(.width(8)) transistor_3 (.in({8{1'b0}}), .out(out_22), .gate(in_1[1]));
  Transistor #(.\type ("n"), .width(8)) transistor_4 (.in({8{1'b1}}), .out(out_13), .gate(in_1[1]));
  Transistor #(.\type ("n"), .width(8)) transistor_5 (.in({8{1'b1}}), .out(out_15), .gate(in_1[1]));
  Transistor #(.\type ("n"), .width(8)) transistor_6 (.in({8{1'b1}}), .out(out_14), .gate(in_1[1]));
  Transistor #(.width(8)) transistor_7 (.in({8{1'b0}}), .out(out_11), .gate(in_1[0]));
  Transistor #(.width(8)) transistor_8 (.in({8{1'b0}}), .out(out_12), .gate(in_1[0]));
  Transistor #(.\type ("n"), .width(8)) transistor_9 (.in({8{1'b1}}), .out(out_2), .gate(in_1[0]));
  Transistor #(.\type ("n"), .width(8)) transistor_10 (.in({8{1'b1}}), .out(out_3), .gate(in_1[0]));
  Transistor #(.width(8)) transistor_11 (.in({8{1'b0}}), .out(out_17), .gate(in_1[1]));
  Transistor #(.width(8)) transistor_12 (.in({8{1'b0}}), .out(out_19), .gate(in_1[1]));
  Transistor #(.width(8)) transistor_13 (.in({8{1'b0}}), .out(out_18), .gate(in_1[1]));
  Transistor #(.width(8)) transistor_14 (.in({8{1'b0}}), .out(out_20), .gate(in_1[1]));
  Transistor #(.\type ("n"), .width(8)) transistor_15 (.in({8{1'b1}}), .out(out_19), .gate(in_1[1]));
  Transistor #(.\type ("n"), .width(8)) transistor_16 (.in({8{1'b1}}), .out(out_16), .gate(in_1[1]));
  Transistor #(.\type ("n"), .width(8)) transistor_17 (.in({8{1'b1}}), .out(out_18), .gate(in_1[1]));
  Transistor #(.\type ("n"), .width(8)) transistor_18 (.in({8{1'b1}}), .out(out_17), .gate(in_1[1]));
  Transistor #(.width(8)) transistor_19 (.in({8{1'b0}}), .out(out_10), .gate(in_1[0]));
  Transistor #(.width(8)) transistor_20 (.in({8{1'b0}}), .out(out_8), .gate(in_1[0]));
  Transistor #(.width(8)) transistor_21 (.in({8{1'b0}}), .out(out_9), .gate(in_1[0]));
  Transistor #(.width(8)) transistor_22 (.in({8{1'b0}}), .out(out_7), .gate(in_1[0]));
  Transistor #(.\type ("n"), .width(8)) transistor_23 (.in({8{1'b1}}), .out(out_6), .gate(in_1[0]));
  Transistor #(.\type ("n"), .width(8)) transistor_24 (.in({8{1'b1}}), .out(out_7), .gate(in_1[0]));
  Transistor #(.\type ("n"), .width(8)) transistor_25 (.in({8{1'b1}}), .out(out_4), .gate(in_1[0]));
  Transistor #(.\type ("n"), .width(8)) transistor_26 (.in({8{1'b1}}), .out(out_5), .gate(in_1[0]));
  Transistor #(.width(8)) transistor_27 (.in({8{1'b0}}), .out(out_13), .gate(in_1[1]));
  Transistor #(.width(8)) transistor_28 (.in({8{1'b0}}), .out(out_16), .gate(in_1[1]));
  Transistor #(.width(8)) transistor_29 (.in({8{1'b0}}), .out(out_14), .gate(in_1[1]));
  Transistor #(.width(8)) transistor_30 (.in({8{1'b0}}), .out(out_15), .gate(in_1[1]));
  Transistor #(.\type ("n"), .width(8)) transistor_31 (.in({8{1'b1}}), .out(out_23), .gate(in_1[1]));
  Transistor #(.\type ("n"), .width(8)) transistor_32 (.in({8{1'b1}}), .out(out_22), .gate(in_1[1]));
  Transistor #(.\type ("n"), .width(8)) transistor_33 (.in({8{1'b1}}), .out(out_20), .gate(in_1[1]));
  Transistor #(.\type ("n"), .width(8)) transistor_34 (.in({8{1'b1}}), .out(out_21), .gate(in_1[1]));
  Transistor #(.width(8)) transistor_35 (.in({8{1'b0}}), .out(out_6), .gate(in_1[0]));
  Transistor #(.width(8)) transistor_36 (.in({8{1'b0}}), .out(out_3), .gate(in_1[0]));
  Transistor #(.width(8)) transistor_37 (.in({8{1'b0}}), .out(out_5), .gate(in_1[0]));
  Transistor #(.width(8)) transistor_38 (.in({8{1'b0}}), .out(out_4), .gate(in_1[0]));
  Transistor #(.\type ("n"), .width(8)) transistor_39 (.in({8{1'b1}}), .out(out_9), .gate(in_1[0]));
  Transistor #(.\type ("n"), .width(8)) transistor_40 (.in({8{1'b1}}), .out(out_11), .gate(in_1[0]));
  Transistor #(.\type ("n"), .width(8)) transistor_41 (.in({8{1'b1}}), .out(out_8), .gate(in_1[0]));
  Transistor #(.\type ("n"), .width(8)) transistor_42 (.in({8{1'b1}}), .out(out_10), .gate(in_1[0]));
  Transistor #(.width(8)) transistor_43 (.in({8{1'b0}}), .out(out_2), .gate(in_1[0]));
  Transistor #(.\type ("n"), .width(8)) transistor_44 (.in({8{1'b1}}), .out(out_12), .gate(in_1[0]));
  DotMatrix #(.matrixcols(11), .matrixrows(8)) dotmatrix_1 (
    .col0(out_13), .col1(out_14), .col2(out_15), .col3(out_16), .col4(out_17), .col5(out_18), .col6(out_19),
    .col7(out_20), .col8(out_21), .col9(out_22), .col10(out_23));
  DotMatrix #(.matrixcols(11), .matrixrows(8)) dotmatrix_2 (
    .col0(out_2), .col1(out_3), .col2(out_4), .col3(out_5), .col4(out_6), .col5(out_7), .col6(out_8),
    .col7(out_9), .col8(out_10), .col9(out_11), .col10(out_12));

  // Notes on the sheet:
  //   Оранжевый
  //   Синий
endmodule

module Type (
  input  in_1,
  input  [3:0] in_2,
  output [7:0] out_3,
  output [7:0] out_4,
  output [7:0] out_5,
  output [7:0] out_6,
  output [7:0] out_7,
  output [7:0] out_8,
  output [7:0] out_9,
  output [7:0] out_10,
  output [7:0] out_11,
  output [7:0] out_12,
  output [7:0] out_13
);

  wire and_1_out, and_2_out, decoder_1_out0, decoder_1_out1, decoder_1_out2, decoder_1_out3, decoder_1_out4,
       or_1_out, or_2_out;
  wire [2:2] or_3_out;

  Decoder #(.select(3)) decoder_1 (
    .out0(decoder_1_out0), .out1(decoder_1_out1), .out2(decoder_1_out2), .out3(decoder_1_out3),
    .out4(decoder_1_out4), .sel({or_3_out[2], in_2[1:0]}), .en(or_1_out));  // open: out5, out6, out7
  or or_1 (or_1_out, or_3_out[2], in_1);
  or or_2 (or_2_out, decoder_1_out0, in_2[0], in_2[1], in_2[2], in_2[3]);
  DotMatrix #(.matrixcols(11), .matrixrows(8)) dotmatrix_1 (
    .col0(out_3), .col1(out_4), .col2(out_5), .col3(out_6), .col4(out_7), .col5(out_8), .col6(out_9),
    .col7(out_10), .col8(out_11), .col9(out_12), .col10(out_13));
  Pull_Resistor pull_resistor_1 (.node(decoder_1_out4));
  or or_3 (or_3_out[2], in_2[2], in_2[3]);
  and and_1 (and_1_out, decoder_1_out4, in_2[2]);
  and and_2 (and_2_out, decoder_1_out4, in_2[3]);
  Pull_Resistor pull_resistor_2 (.node(decoder_1_out1));
  Pull_Resistor pull_resistor_3 (.node(decoder_1_out0));
  Pull_Resistor pull_resistor_4 (.node(decoder_1_out3));
  Pull_Resistor pull_resistor_5 (.node(and_2_out));
  Pull_Resistor pull_resistor_6 (.node(decoder_1_out2));
  Pull_Resistor pull_resistor_7 (.node(and_1_out));
  Transistor #(.\type ("n"), .width(8)) transistor_1 (.in({8{1'b1}}), .out(out_3), .gate(decoder_1_out0));
  Transistor #(.\type ("n"), .width(8)) transistor_2 (.in({8{1'b1}}), .out(out_4), .gate(decoder_1_out0));
  Transistor #(.\type ("n"), .width(8)) transistor_3 (.in({8{1'b1}}), .out(out_5), .gate(decoder_1_out0));
  Transistor #(.\type ("n"), .width(8)) transistor_4 (.in({8{1'b1}}), .out(out_7), .gate(decoder_1_out0));
  Transistor #(.\type ("n"), .width(8)) transistor_5 (.in({8{1'b1}}), .out(out_6), .gate(decoder_1_out0));
  Transistor #(.\type ("n"), .width(8)) transistor_6 (.in({8{1'b1}}), .out(out_11), .gate(decoder_1_out0));
  Transistor #(.\type ("n"), .width(8)) transistor_7 (.in({8{1'b1}}), .out(out_10), .gate(decoder_1_out0));
  Transistor #(.\type ("n"), .width(8)) transistor_8 (.in({8{1'b1}}), .out(out_9), .gate(decoder_1_out0));
  Transistor #(.\type ("n"), .width(8)) transistor_9 (.in({8{1'b1}}), .out(out_8), .gate(decoder_1_out0));
  Transistor #(.\type ("n"), .width(8)) transistor_10 (.in({8{1'b1}}), .out(out_12), .gate(decoder_1_out0));
  Transistor #(.\type ("n"), .width(8)) transistor_11 (.in({8{1'b1}}), .out(out_13), .gate(decoder_1_out0));
  Transistor #(.\type ("n"), .width(8)) transistor_12 (.in(8'he7), .out(out_4), .gate(decoder_1_out1));
  Transistor #(.\type ("n"), .width(8)) transistor_13 (.in(8'he7), .out(out_5), .gate(decoder_1_out1));
  Transistor #(.\type ("n"), .width(8)) transistor_14 (.in(8'he7), .out(out_3), .gate(decoder_1_out1));
  Transistor #(.\type ("n"), .width(8)) transistor_15 (.in(8'he7), .out(out_6), .gate(decoder_1_out1));
  Transistor #(.\type ("n"), .width(8)) transistor_16 (.in({8{1'b0}}), .out(out_8), .gate(decoder_1_out1));
  Transistor #(.\type ("n"), .width(8)) transistor_17 (.in({8{1'b0}}), .out(out_9), .gate(decoder_1_out1));
  Transistor #(.\type ("n"), .width(8)) transistor_18 (.in({8{1'b0}}), .out(out_7), .gate(decoder_1_out1));
  Transistor #(.\type ("n"), .width(8)) transistor_19 (.in(8'he7), .out(out_10), .gate(decoder_1_out1));
  Transistor #(.\type ("n"), .width(8)) transistor_20 (.in(8'he7), .out(out_11), .gate(decoder_1_out1));
  Transistor #(.\type ("n"), .width(8)) transistor_21 (.in(8'he7), .out(out_12), .gate(decoder_1_out1));
  Transistor #(.\type ("n"), .width(8)) transistor_22 (.in(8'he7), .out(out_13), .gate(decoder_1_out1));
  Transistor #(.\type ("n"), .width(8)) transistor_23 (.in({8{1'b0}}), .out(out_4), .gate(decoder_1_out2));
  Transistor #(.\type ("n"), .width(8)) transistor_24 (.in(8'h6c), .out(out_6), .gate(decoder_1_out2));
  Transistor #(.\type ("n"), .width(8)) transistor_25 (.in(8'hf8), .out(out_5), .gate(decoder_1_out2));
  Transistor #(.\type ("n"), .width(8)) transistor_26 (.in({8{1'b1}}), .out(out_3), .gate(decoder_1_out2));
  Transistor #(.\type ("n"), .width(8)) transistor_27 (.in(8'h6c), .out(out_10), .gate(decoder_1_out2));
  Transistor #(.\type ("n"), .width(8)) transistor_28 (.in(8'h56), .out(out_7), .gate(decoder_1_out2));
  Transistor #(.\type ("n"), .width(8)) transistor_29 (.in(8'h56), .out(out_9), .gate(decoder_1_out2));
  Transistor #(.\type ("n"), .width(8)) transistor_30 (.in(8'hd3), .out(out_8), .gate(decoder_1_out2));
  Transistor #(.\type ("n"), .width(8)) transistor_31 (.in({8{1'b0}}), .out(out_12), .gate(decoder_1_out2));
  Transistor #(.\type ("n"), .width(8)) transistor_32 (.in({8{1'b1}}), .out(out_13), .gate(decoder_1_out2));
  Transistor #(.\type ("n"), .width(8)) transistor_33 (.in(8'hf8), .out(out_11), .gate(decoder_1_out2));
  Transistor #(.\type ("n"), .width(8)) transistor_34 (.in(8'h91), .out(out_3), .gate(decoder_1_out3));
  Transistor #(.\type ("n"), .width(8)) transistor_35 (.in({8{1'b0}}), .out(out_4), .gate(decoder_1_out3));
  Transistor #(.\type ("n"), .width(8)) transistor_36 (.in(8'h6b), .out(out_8), .gate(decoder_1_out3));
  Transistor #(.\type ("n"), .width(8)) transistor_37 (.in(8'h18), .out(out_6), .gate(decoder_1_out3));
  Transistor #(.\type ("n"), .width(8)) transistor_38 (.in(8'h4a), .out(out_5), .gate(decoder_1_out3));
  Transistor #(.\type ("n"), .width(8)) transistor_39 (.in(8'h39), .out(out_7), .gate(decoder_1_out3));
  Transistor #(.\type ("n"), .width(8)) transistor_40 (.in(8'h29), .out(out_11), .gate(decoder_1_out3));
  Transistor #(.\type ("n"), .width(8)) transistor_41 (.in(8'hc), .out(out_10), .gate(decoder_1_out3));
  Transistor #(.\type ("n"), .width(8)) transistor_42 (.in(8'h80), .out(out_12), .gate(decoder_1_out3));
  Transistor #(.\type ("n"), .width(8)) transistor_43 (.in(8'hce), .out(out_9), .gate(decoder_1_out3));
  Transistor #(.\type ("n"), .width(8)) transistor_44 (.in(8'h12), .out(out_13), .gate(decoder_1_out3));
  Transistor #(.\type ("n"), .width(8)) transistor_45 (.in(8'hc0), .out(out_3), .gate(and_1_out));
  Transistor #(.\type ("n"), .width(8)) transistor_46 (.in(8'hc0), .out(out_4), .gate(and_1_out));
  Transistor #(.\type ("n"), .width(8)) transistor_47 (.in(8'hc0), .out(out_7), .gate(and_1_out));
  Transistor #(.\type ("n"), .width(8)) transistor_48 (.in(8'hc0), .out(out_5), .gate(and_1_out));
  Transistor #(.\type ("n"), .width(8)) transistor_49 (.in(8'hc0), .out(out_6), .gate(and_1_out));
  Transistor #(.\type ("n"), .width(8)) transistor_50 (.in(8'hc0), .out(out_8), .gate(and_1_out));
  Transistor #(.\type ("n"), .width(8)) transistor_51 (.in(8'hc0), .out(out_11), .gate(and_1_out));
  Transistor #(.\type ("n"), .width(8)) transistor_52 (.in(8'hc0), .out(out_12), .gate(and_1_out));
  Transistor #(.\type ("n"), .width(8)) transistor_53 (.in(8'hc0), .out(out_10), .gate(and_1_out));
  Transistor #(.\type ("n"), .width(8)) transistor_54 (.in(8'hc0), .out(out_9), .gate(and_1_out));
  Transistor #(.\type ("n"), .width(8)) transistor_55 (.in(8'hc0), .out(out_13), .gate(and_1_out));
  Transistor #(.\type ("n"), .width(8)) transistor_56 (.in(8'h3), .out(out_3), .gate(and_2_out));
  Transistor #(.\type ("n"), .width(8)) transistor_57 (.in(8'h3), .out(out_4), .gate(and_2_out));
  Transistor #(.\type ("n"), .width(8)) transistor_58 (.in(8'h3), .out(out_5), .gate(and_2_out));
  Transistor #(.\type ("n"), .width(8)) transistor_59 (.in(8'h3), .out(out_7), .gate(and_2_out));
  Transistor #(.\type ("n"), .width(8)) transistor_60 (.in(8'h3), .out(out_6), .gate(and_2_out));
  Transistor #(.\type ("n"), .width(8)) transistor_61 (.in(8'h3), .out(out_10), .gate(and_2_out));
  Transistor #(.\type ("n"), .width(8)) transistor_62 (.in(8'h3), .out(out_8), .gate(and_2_out));
  Transistor #(.\type ("n"), .width(8)) transistor_63 (.in(8'h3), .out(out_9), .gate(and_2_out));
  Transistor #(.\type ("n"), .width(8)) transistor_64 (.in(8'h3), .out(out_11), .gate(and_2_out));
  Transistor #(.\type ("n"), .width(8)) transistor_65 (.in(8'h3), .out(out_13), .gate(and_2_out));
  Transistor #(.\type ("n"), .width(8)) transistor_66 (.in(8'h3), .out(out_12), .gate(and_2_out));
  Transistor #(.width(8)) transistor_67 (.in({8{1'b0}}), .out(out_3), .gate(or_2_out));
  Transistor #(.width(8)) transistor_68 (.in({8{1'b0}}), .out(out_4), .gate(or_2_out));
  Transistor #(.width(8)) transistor_69 (.in({8{1'b0}}), .out(out_6), .gate(or_2_out));
  Transistor #(.width(8)) transistor_70 (.in({8{1'b0}}), .out(out_5), .gate(or_2_out));
  Transistor #(.width(8)) transistor_71 (.in({8{1'b0}}), .out(out_8), .gate(or_2_out));
  Transistor #(.width(8)) transistor_72 (.in({8{1'b0}}), .out(out_10), .gate(or_2_out));
  Transistor #(.width(8)) transistor_73 (.in({8{1'b0}}), .out(out_9), .gate(or_2_out));
  Transistor #(.width(8)) transistor_74 (.in({8{1'b0}}), .out(out_7), .gate(or_2_out));
  Transistor #(.width(8)) transistor_75 (.in({8{1'b0}}), .out(out_13), .gate(or_2_out));
  Transistor #(.width(8)) transistor_76 (.in({8{1'b0}}), .out(out_11), .gate(or_2_out));
  Transistor #(.width(8)) transistor_77 (.in({8{1'b0}}), .out(out_12), .gate(or_2_out));

  // Notes on the sheet:
  //   Транспорт
  //   2
  //   Щит
  //   3
  //   4
  //   Энергия
  //   Занята
  //   1
  //   Занята
  //   1
  //   Занята
  //   1
  //   Занята
  //   1
endmodule

module Player_Type (
  input  [1:0] in_1,
  input  [3:0] in_2,
  output [7:0] out_3,
  output [7:0] out_4,
  output [7:0] out_5,
  output [7:0] out_6,
  output [7:0] out_7,
  output [7:0] out_8,
  output [7:0] out_9,
  output [7:0] out_10,
  output [7:0] out_11,
  output [7:0] out_12,
  output [7:0] out_13,
  output [7:0] out_14,
  output [7:0] out_15,
  output [7:0] out_16,
  output [7:0] out_17,
  output [7:0] out_18,
  output [7:0] out_19,
  output [7:0] out_20,
  output [7:0] out_21,
  output [7:0] out_22,
  output [7:0] out_23,
  output [7:0] out_24
);

  wire and_5_out, and_6_out;
  wire [2:0] and_1_out;
  wire [3:0] and_3_out;

  and and_1 (and_1_out[0], in_1[0], in_2[0]);
  and and_2 (and_1_out[1], in_2[1], in_1[0]);
  and and_3 (and_3_out[0], in_1[1], in_2[0]);
  and and_4 (and_3_out[1], in_1[1], in_2[1]);
  xor xor_1 (and_3_out[3], in_2[3], and_6_out);
  xor xor_2 (and_1_out[2], in_2[2], and_5_out);
  and and_5 (and_5_out, in_1[0], in_2[2]);
  and and_6 (and_6_out, in_1[1], in_2[3]);
  DotMatrix #(.matrixcols(11), .matrixrows(8)) dotmatrix_1 (
    .col0(out_14), .col1(out_15), .col2(out_16), .col3(out_17), .col4(out_18), .col5(out_19), .col6(out_20),
    .col7(out_21), .col8(out_22), .col9(out_23), .col10(out_24));
  Type type_1 (
    .in_1(in_1[0]), .in_2({1'b0, and_1_out}), .out_3(out_14), .out_4(out_15), .out_5(out_16), .out_6(out_17),
    .out_7(out_18), .out_8(out_19), .out_9(out_20), .out_10(out_21), .out_11(out_22), .out_12(out_23),
    .out_13(out_24));
  DotMatrix #(.matrixcols(11), .matrixrows(8)) dotmatrix_2 (
    .col0(out_3), .col1(out_4), .col2(out_5), .col3(out_6), .col4(out_7), .col5(out_8), .col6(out_9),
    .col7(out_10), .col8(out_11), .col9(out_12), .col10(out_13));
  Type type_2 (
    .in_1(in_1[1]), .in_2({and_3_out[3], 1'b0, and_3_out[1:0]}), .out_3(out_3), .out_4(out_4), .out_5(out_5),
    .out_6(out_6), .out_7(out_7), .out_8(out_8), .out_9(out_9), .out_10(out_10), .out_11(out_11),
    .out_12(out_12), .out_13(out_13));

  // Notes on the sheet:
  //   Оранжевый
  //   Синий
endmodule

module Numder (
  input  [9:0] in_1,
  output [4:0] out_2,
  output [4:0] out_3,
  output [4:0] out_4
);

  // Probe on {in_1[9:3], {3{in_1[3]}}}
  Col_1 col_1_1 (
    .D(in_1[3]), .C(in_1[3]), .B(in_1[3]), .A(in_1[3]), .e(out_2[4]), .d_2(out_2[3]), .c_2(out_2[2]),
    .b_2(out_2[1]), .a_2(out_2[0]));
  Col_2 col_2_1 (
    .D(in_1[3]), .C(in_1[3]), .B(in_1[3]), .A(in_1[3]), .e(out_3[4]), .d_2(out_3[3]), .c_2(out_3[2]),
    .b_2(out_3[1]), .a_2(out_3[0]));
  Col_3 col_3_1 (
    .D(in_1[3]), .C(in_1[3]), .B(in_1[3]), .A(in_1[3]), .e(out_4[4]), .d_2(out_4[3]), .c_2(out_4[2]),
    .b_2(out_4[1]), .a_2(out_4[0]));
  DotMatrix #(.matrixcols(3), .matrixrows(5)) dotmatrix_1 (.col0(out_2), .col1(out_3), .col2(out_4));

  assign in_1[2:0] = {3{in_1[3]}};
endmodule

module Output_Numder (
  input  [9:0] Energy,
  output [4:0] out_2,
  output [4:0] out_3,
  output [4:0] out_4,
  output [4:0] out_5,
  output [4:0] out_6,
  output [4:0] out_7,
  output [4:0] out_8,
  output [4:0] out_9,
  output [4:0] out_10,
  output [4:0] out_11,
  output [4:0] out_12
);

  // Probe on Energy
  BCD2 bcd2_1 (
    .in_1(Energy), .out_2(out_2), .out_3(out_3), .out_4(out_4), .out_5(out_6), .out_6(out_7), .out_7(out_8),
    .out_8(out_10), .out_9(out_11), .out_10(out_12));

  assign out_5 = {5{1'b0}};
  assign out_9 = {5{1'b0}};
endmodule

module Adding_Chip (
  input  A0,
  input  A1,
  input  A2,
  input  A3,
  output S0,
  output S1,
  output S2,
  output S3
);

  wire and_1_out, and_2_out, and_3_out, and_4_out, and_5_out, and_6_out, and_7_out, and_8_out, and_9_out,
       not_1_out, not_2_out, not_3_out, not_4_out;

  not not_1 (not_1_out, A3);
  not not_2 (not_2_out, A1);
  not not_3 (not_3_out, A2);
  not not_4 (not_4_out, A0);
  and and_1 (and_1_out, A2, A0);
  and and_2 (and_2_out, A2, A1);
  and and_3 (and_3_out, A2, not_2_out, not_4_out);
  and and_4 (and_4_out, A3, A0);
  and and_5 (and_5_out, not_3_out, A1);
  and and_6 (and_6_out, A1, A0);
  and and_7 (and_7_out, A3, not_4_out);
  and and_8 (and_8_out, A2, A1, not_4_out);
  and and_9 (and_9_out, not_1_out, not_3_out, A0);
  or or_1 (S3, and_1_out, and_2_out, A3);
  or or_2 (S2, and_3_out, and_4_out);
  or or_3 (S1, and_5_out, and_6_out, and_7_out);
  or or_4 (S0, and_7_out, and_8_out, and_9_out);
endmodule

module full_diget_namber (
  input  [9:0] in_1,
  input  in_2,
  output [4:0] out_3,
  output [4:0] out_4,
  output [4:0] out_5,
  output [4:0] out_6,
  output [4:0] out_7,
  output [4:0] out_8,
  output [4:0] out_9,
  output [4:0] out_10,
  output [4:0] out_11,
  output [4:0] out_12,
  output [4:0] out_13
);

  wire [4:0] inversion_1_out_2, inversion_1_out_3, inversion_1_out_4, inversion_1_out_5, inversion_1_out_6,
       inversion_1_out_7, inversion_1_out_8, inversion_1_out_9, inversion_1_out_10, inversion_1_out_11,
       inversion_1_out_12, output_numder_1_out_2, output_numder_1_out_3, output_numder_1_out_4,
       output_numder_1_out_5, output_numder_1_out_6, output_numder_1_out_7, output_numder_1_out_8,
       output_numder_1_out_9, output_numder_1_out_10, output_numder_1_out_11, output_numder_1_out_12;

  DotMatrix #(.matrixcols(11), .matrixrows(5)) dotmatrix_1 (
    .col0(out_3), .col1(out_4), .col2(out_5), .col3(out_6), .col4(out_7), .col5(out_8), .col6(out_9),
    .col7(out_10), .col8(out_11), .col9(out_12), .col10(out_13));
  Transistor #(.\type ("n"), .width(5)) transistor_1 (.in(inversion_1_out_4), .out(out_5), .gate(in_2));
  Transistor #(.\type ("n"), .width(5)) transistor_2 (.in(inversion_1_out_2), .out(out_3), .gate(in_2));
  Transistor #(.\type ("n"), .width(5)) transistor_3 (.in(inversion_1_out_3), .out(out_4), .gate(in_2));
  Transistor #(.\type ("n"), .width(5)) transistor_4 (.in(inversion_1_out_5), .out(out_6), .gate(in_2));
  inversion inversion_1 (
    .in_1(in_1), .out_2(inversion_1_out_2), .out_3(inversion_1_out_3), .out_4(inversion_1_out_4),
    .out_5(inversion_1_out_5), .out_6(inversion_1_out_6), .out_7(inversion_1_out_7),
    .out_8(inversion_1_out_8), .out_9(inversion_1_out_9), .out_10(inversion_1_out_10),
    .out_11(inversion_1_out_11), .out_12(inversion_1_out_12));
  Transistor #(.\type ("n"), .width(5)) transistor_5 (.in(inversion_1_out_9), .out(out_10), .gate(in_2));
  Transistor #(.\type ("n"), .width(5)) transistor_6 (.in(inversion_1_out_11), .out(out_12), .gate(in_2));
  Transistor #(.\type ("n"), .width(5)) transistor_7 (.in(inversion_1_out_6), .out(out_7), .gate(in_2));
  Transistor #(.\type ("n"), .width(5)) transistor_8 (.in(inversion_1_out_12), .out(out_13), .gate(in_2));
  Transistor #(.\type ("n"), .width(5)) transistor_9 (.in(inversion_1_out_10), .out(out_11), .gate(in_2));
  Transistor #(.\type ("n"), .width(5)) transistor_10 (.in(inversion_1_out_7), .out(out_8), .gate(in_2));
  Transistor #(.\type ("n"), .width(5)) transistor_11 (.in(inversion_1_out_8), .out(out_9), .gate(in_2));
  Transistor #(.width(5)) transistor_12 (.in(output_numder_1_out_2), .out(out_3), .gate(in_2));
  Transistor #(.width(5)) transistor_13 (.in(output_numder_1_out_3), .out(out_4), .gate(in_2));
  Output_Numder output_numder_1 (
    .Energy(in_1), .out_2(output_numder_1_out_2), .out_3(output_numder_1_out_3),
    .out_4(output_numder_1_out_4), .out_5(output_numder_1_out_5), .out_6(output_numder_1_out_6),
    .out_7(output_numder_1_out_7), .out_8(output_numder_1_out_8), .out_9(output_numder_1_out_9),
    .out_10(output_numder_1_out_10), .out_11(output_numder_1_out_11), .out_12(output_numder_1_out_12));
  Transistor #(.width(5)) transistor_14 (.in(output_numder_1_out_4), .out(out_5), .gate(in_2));
  Transistor #(.width(5)) transistor_15 (.in(output_numder_1_out_10), .out(out_11), .gate(in_2));
  Transistor #(.width(5)) transistor_16 (.in(output_numder_1_out_7), .out(out_8), .gate(in_2));
  Transistor #(.width(5)) transistor_17 (.in(output_numder_1_out_8), .out(out_9), .gate(in_2));
  Transistor #(.width(5)) transistor_18 (.in(output_numder_1_out_6), .out(out_7), .gate(in_2));
  Transistor #(.width(5)) transistor_19 (.in(output_numder_1_out_5), .out(out_6), .gate(in_2));
  Transistor #(.width(5)) transistor_20 (.in(output_numder_1_out_11), .out(out_12), .gate(in_2));
  Transistor #(.width(5)) transistor_21 (.in(output_numder_1_out_9), .out(out_10), .gate(in_2));
  Transistor #(.width(5)) transistor_22 (.in(output_numder_1_out_12), .out(out_13), .gate(in_2));
endmodule

module BCD2 (
  input  [9:0] in_1,
  output [4:0] out_2,
  output [4:0] out_3,
  output [4:0] out_4,
  output [4:0] out_5,
  output [4:0] out_6,
  output [4:0] out_7,
  output [4:0] out_8,
  output [4:0] out_9,
  output [4:0] out_10
);

  wire adding_chip_1_s0, adding_chip_1_s1, adding_chip_1_s2, adding_chip_2_s0, adding_chip_2_s1,
       adding_chip_2_s2, adding_chip_2_s3, adding_chip_3_s0, adding_chip_3_s1, adding_chip_3_s2,
       adding_chip_3_s3, adding_chip_4_s0, adding_chip_4_s1, adding_chip_4_s2, adding_chip_4_s3,
       adding_chip_5_s0, adding_chip_5_s1, adding_chip_5_s2, adding_chip_5_s3, adding_chip_6_s0,
       adding_chip_6_s1, adding_chip_6_s2, adding_chip_6_s3, adding_chip_7_s0, adding_chip_7_s1,
       adding_chip_7_s2, adding_chip_7_s3, adding_chip_8_s0, adding_chip_8_s1, adding_chip_8_s2,
       adding_chip_8_s3, adding_chip_9_s0, adding_chip_9_s1, adding_chip_9_s2, adding_chip_9_s3,
       adding_chip_10_s0, adding_chip_10_s1, adding_chip_10_s2, adding_chip_10_s3, adding_chip_11_s0,
       adding_chip_11_s1, adding_chip_11_s2, adding_chip_11_s3, adding_chip_12_s0, adding_chip_12_s1,
       adding_chip_12_s2, adding_chip_12_s3, and_1_out, or_1_out, or_2_out, or_3_out, or_4_out, or_5_out;
  wire [4:0] col_1_1_e, col_1_2_e, col_1_3_e, col_2_1_e, col_2_2_e, col_2_3_e, col_3_1_e, col_3_2_e,
       col_3_3_e;
  wire [9:0] transistor_4_out;

  Transistor #(.\type ("n"), .width(5)) transistor_1 (.in(col_1_1_e), .out(out_2), .gate(or_1_out));
  Col_1 col_1_1 (
    .D(adding_chip_1_s2), .C(adding_chip_1_s1), .B(adding_chip_1_s0), .A(adding_chip_12_s3),
    .e(col_1_1_e[0]), .d_2(col_1_1_e[1]), .c_2(col_1_1_e[2]), .b_2(col_1_1_e[3]), .a_2(col_1_1_e[4]));
  Transistor #(.\type ("n"), .width(5)) transistor_2 (.in(col_2_1_e), .out(out_3), .gate(or_1_out));
  DotMatrix #(.matrixcols(3), .matrixrows(5)) dotmatrix_1 (.col0(out_2), .col1(out_3), .col2(out_4));
  or or_1 (or_1_out, adding_chip_1_s2, adding_chip_1_s1, adding_chip_1_s0, adding_chip_12_s3);
  Col_2 col_2_1 (
    .D(adding_chip_1_s2), .C(adding_chip_1_s1), .B(adding_chip_1_s0), .A(adding_chip_12_s3),
    .e(col_2_1_e[0]), .d_2(col_2_1_e[1]), .c_2(col_2_1_e[2]), .b_2(col_2_1_e[3]), .a_2(col_2_1_e[4]));
  Transistor #(.\type ("n"), .width(5)) transistor_3 (.in(col_3_1_e), .out(out_4), .gate(or_1_out));
  Adding_Chip adding_chip_1 (
    .A0(adding_chip_10_s3), .A1(adding_chip_8_s3), .A2(adding_chip_6_s3), .A3(1'b0), .S0(adding_chip_1_s0),
    .S1(adding_chip_1_s1), .S2(adding_chip_1_s2));  // open: S3
  Col_3 col_3_1 (
    .D(adding_chip_1_s2), .C(adding_chip_1_s1), .B(adding_chip_1_s0), .A(adding_chip_12_s3),
    .e(col_3_1_e[0]), .d_2(col_3_1_e[1]), .c_2(col_3_1_e[2]), .b_2(col_3_1_e[3]), .a_2(col_3_1_e[4]));
  or or_2 (or_2_out, or_1_out, or_3_out);
  // Probe on in_1
  Transistor #(.width(10)) transistor_4 (.in(in_1), .out(transistor_4_out), .gate(and_1_out));
  Adding_Chip adding_chip_2 (
    .A0(transistor_4_out[7]), .A1(transistor_4_out[8]), .A2(transistor_4_out[9]), .A3(1'b0),
    .S0(adding_chip_2_s0), .S1(adding_chip_2_s1), .S2(adding_chip_2_s2), .S3(adding_chip_2_s3));
  Adding_Chip adding_chip_3 (
    .A0(transistor_4_out[6]), .A1(adding_chip_2_s0), .A2(adding_chip_2_s1), .A3(adding_chip_2_s2),
    .S0(adding_chip_3_s0), .S1(adding_chip_3_s1), .S2(adding_chip_3_s2), .S3(adding_chip_3_s3));
  Adding_Chip adding_chip_4 (
    .A0(transistor_4_out[5]), .A1(adding_chip_3_s0), .A2(adding_chip_3_s1), .A3(adding_chip_3_s2),
    .S0(adding_chip_4_s0), .S1(adding_chip_4_s1), .S2(adding_chip_4_s2), .S3(adding_chip_4_s3));
  Adding_Chip adding_chip_5 (
    .A0(transistor_4_out[4]), .A1(adding_chip_4_s0), .A2(adding_chip_4_s1), .A3(adding_chip_4_s2),
    .S0(adding_chip_5_s0), .S1(adding_chip_5_s1), .S2(adding_chip_5_s2), .S3(adding_chip_5_s3));
  Adding_Chip adding_chip_6 (
    .A0(adding_chip_4_s3), .A1(adding_chip_3_s3), .A2(adding_chip_2_s3), .A3(1'b0), .S0(adding_chip_6_s0),
    .S1(adding_chip_6_s1), .S2(adding_chip_6_s2), .S3(adding_chip_6_s3));
  Adding_Chip adding_chip_7 (
    .A0(transistor_4_out[3]), .A1(adding_chip_5_s0), .A2(adding_chip_5_s1), .A3(adding_chip_5_s2),
    .S0(adding_chip_7_s0), .S1(adding_chip_7_s1), .S2(adding_chip_7_s2), .S3(adding_chip_7_s3));
  Adding_Chip adding_chip_8 (
    .A0(adding_chip_5_s3), .A1(adding_chip_6_s0), .A2(adding_chip_6_s1), .A3(adding_chip_6_s2),
    .S0(adding_chip_8_s0), .S1(adding_chip_8_s1), .S2(adding_chip_8_s2), .S3(adding_chip_8_s3));
  Adding_Chip adding_chip_9 (
    .A0(transistor_4_out[2]), .A1(adding_chip_7_s0), .A2(adding_chip_7_s1), .A3(adding_chip_7_s2),
    .S0(adding_chip_9_s0), .S1(adding_chip_9_s1), .S2(adding_chip_9_s2), .S3(adding_chip_9_s3));
  Adding_Chip adding_chip_10 (
    .A0(adding_chip_7_s3), .A1(adding_chip_8_s0), .A2(adding_chip_8_s1), .A3(adding_chip_8_s2),
    .S0(adding_chip_10_s0), .S1(adding_chip_10_s1), .S2(adding_chip_10_s2), .S3(adding_chip_10_s3));
  Adding_Chip adding_chip_11 (
    .A0(transistor_4_out[1]), .A1(adding_chip_9_s0), .A2(adding_chip_9_s1), .A3(adding_chip_9_s2),
    .S0(adding_chip_11_s0), .S1(adding_chip_11_s1), .S2(adding_chip_11_s2), .S3(adding_chip_11_s3));
  Adding_Chip adding_chip_12 (
    .A0(adding_chip_9_s3), .A1(adding_chip_10_s0), .A2(adding_chip_10_s1), .A3(adding_chip_10_s2),
    .S0(adding_chip_12_s0), .S1(adding_chip_12_s1), .S2(adding_chip_12_s2), .S3(adding_chip_12_s3));
  or or_3 (or_3_out, adding_chip_12_s2, adding_chip_12_s1, adding_chip_12_s0, adding_chip_11_s3);
  Transistor #(.\type ("n"), .width(5)) transistor_5 (.in(col_1_2_e), .out(out_5), .gate(or_2_out));
  Transistor #(.\type ("n"), .width(5)) transistor_6 (.in(col_2_2_e), .out(out_6), .gate(or_2_out));
  DotMatrix #(.matrixcols(3), .matrixrows(5)) dotmatrix_2 (.col0(out_5), .col1(out_6), .col2(out_7));
  Transistor #(.\type ("n"), .width(10)) transistor_7 (.in(10'h3e7), .out(transistor_4_out), .gate(and_1_out));
  Col_1 col_1_2 (
    .D(adding_chip_12_s2), .C(adding_chip_12_s1), .B(adding_chip_12_s0), .A(adding_chip_11_s3),
    .e(col_1_2_e[0]), .d_2(col_1_2_e[1]), .c_2(col_1_2_e[2]), .b_2(col_1_2_e[3]), .a_2(col_1_2_e[4]));
  Transistor #(.\type ("n"), .width(5)) transistor_8 (.in(col_3_2_e), .out(out_7), .gate(or_2_out));
  and and_1 (and_1_out, in_1[9], in_1[8], in_1[7], in_1[6], in_1[5], or_5_out);
  or or_4 (or_4_out, adding_chip_1_s2, adding_chip_1_s1, adding_chip_1_s0, adding_chip_12_s3, adding_chip_12_s2, adding_chip_12_s1, adding_chip_12_s0, adding_chip_11_s3, adding_chip_11_s2, adding_chip_11_s1, adding_chip_11_s0, transistor_4_out[0]);
  Col_3 col_3_2 (
    .D(adding_chip_12_s2), .C(adding_chip_12_s1), .B(adding_chip_12_s0), .A(adding_chip_11_s3),
    .e(col_3_2_e[0]), .d_2(col_3_2_e[1]), .c_2(col_3_2_e[2]), .b_2(col_3_2_e[3]), .a_2(col_3_2_e[4]));
  Col_2 col_2_2 (
    .D(adding_chip_12_s2), .C(adding_chip_12_s1), .B(adding_chip_12_s0), .A(adding_chip_11_s3),
    .e(col_2_2_e[0]), .d_2(col_2_2_e[1]), .c_2(col_2_2_e[2]), .b_2(col_2_2_e[3]), .a_2(col_2_2_e[4]));
  or or_5 (or_5_out, in_1[4], in_1[3]);
  Transistor #(.\type ("n"), .width(5)) transistor_9 (.in(col_1_3_e), .out(out_8), .gate(or_4_out));
  DotMatrix #(.matrixcols(3), .matrixrows(5)) dotmatrix_3 (.col0(out_8), .col1(out_9), .col2(out_10));
  Col_2 col_2_3 (
    .D(adding_chip_11_s2), .C(adding_chip_11_s1), .B(adding_chip_11_s0), .A(transistor_4_out[0]),
    .e(col_2_3_e[0]), .d_2(col_2_3_e[1]), .c_2(col_2_3_e[2]), .b_2(col_2_3_e[3]), .a_2(col_2_3_e[4]));
  Col_1 col_1_3 (
    .D(adding_chip_11_s2), .C(adding_chip_11_s1), .B(adding_chip_11_s0), .A(transistor_4_out[0]),
    .e(col_1_3_e[0]), .d_2(col_1_3_e[1]), .c_2(col_1_3_e[2]), .b_2(col_1_3_e[3]), .a_2(col_1_3_e[4]));
  Transistor #(.\type ("n"), .width(5)) transistor_10 (.in(col_3_3_e), .out(out_10), .gate(or_4_out));
  Transistor #(.\type ("n"), .width(5)) transistor_11 (.in(col_2_3_e), .out(out_9), .gate(or_4_out));
  Col_3 col_3_3 (
    .D(adding_chip_11_s2), .C(adding_chip_11_s1), .B(adding_chip_11_s0), .A(transistor_4_out[0]),
    .e(col_3_3_e[0]), .d_2(col_3_3_e[1]), .c_2(col_3_3_e[2]), .b_2(col_3_3_e[3]), .a_2(col_3_3_e[4]));
  Transistor #(.width(5)) transistor_12 (.in({5{1'b0}}), .out(out_4), .gate(or_1_out));
  Transistor #(.width(5)) transistor_13 (.in({5{1'b0}}), .out(out_7), .gate(or_2_out));
  Transistor #(.width(5)) transistor_14 (.in({5{1'b0}}), .out(out_8), .gate(or_4_out));
  Transistor #(.width(5)) transistor_15 (.in({5{1'b0}}), .out(out_3), .gate(or_1_out));
  Transistor #(.width(5)) transistor_16 (.in({5{1'b0}}), .out(out_2), .gate(or_1_out));
  Transistor #(.width(5)) transistor_17 (.in({5{1'b0}}), .out(out_5), .gate(or_2_out));
  Transistor #(.width(5)) transistor_18 (.in({5{1'b0}}), .out(out_6), .gate(or_2_out));
  Transistor #(.width(5)) transistor_19 (.in({5{1'b0}}), .out(out_10), .gate(or_4_out));
  Transistor #(.width(5)) transistor_20 (.in({5{1'b0}}), .out(out_9), .gate(or_4_out));
endmodule

module inversion (
  input  [9:0] in_1,
  output [4:0] out_2,
  output [4:0] out_3,
  output [4:0] out_4,
  output [4:0] out_5,
  output [4:0] out_6,
  output [4:0] out_7,
  output [4:0] out_8,
  output [4:0] out_9,
  output [4:0] out_10,
  output [4:0] out_11,
  output [4:0] out_12
);

  wire nor_1_out;
  wire [4:0] output_numder_1_out_2, output_numder_1_out_3, output_numder_1_out_4, output_numder_1_out_5,
       output_numder_1_out_6, output_numder_1_out_7, output_numder_1_out_8, output_numder_1_out_9,
       output_numder_1_out_10, output_numder_1_out_11, output_numder_1_out_12, transistor_1_out,
       transistor_2_out, transistor_3_out, transistor_4_out, transistor_5_out, transistor_6_out,
       transistor_7_out, transistor_8_out, transistor_9_out, transistor_10_out, transistor_11_out;

  DotMatrix #(.matrixcols(11), .matrixrows(5)) dotmatrix_1 (
    .col0(out_2), .col1(out_3), .col2(out_4), .col3(out_5), .col4(out_6), .col5(out_7), .col6(out_8),
    .col7(out_9), .col8(out_10), .col9(out_11), .col10(out_12));
  nor nor_1 (nor_1_out, in_1[0], in_1[1], in_1[2], in_1[3], in_1[4], in_1[5], in_1[6], in_1[7], in_1[8], in_1[9]);
  Transistor #(.\type ("n"), .width(5)) transistor_1 (.in({5{1'b0}}), .out(transistor_1_out), .gate(nor_1_out));
  Transistor #(.\type ("n"), .width(5)) transistor_2 (.in(5'b01110), .out(transistor_2_out), .gate(nor_1_out));
  Transistor #(.\type ("n"), .width(5)) transistor_3 (.in(5'b01110), .out(transistor_3_out), .gate(nor_1_out));
  Transistor #(.\type ("n"), .width(5)) transistor_4 (.in(5'b01110), .out(transistor_4_out), .gate(nor_1_out));
  Transistor #(.\type ("n"), .width(5)) transistor_5 (.in(5'b01110), .out(transistor_5_out), .gate(nor_1_out));
  Transistor #(.\type ("n"), .width(5)) transistor_6 (.in(5'b01110), .out(transistor_6_out), .gate(nor_1_out));
  Transistor #(.\type ("n"), .width(5)) transistor_7 (.in(5'b01110), .out(transistor_7_out), .gate(nor_1_out));
  Transistor #(.\type ("n"), .width(5)) transistor_8 (.in(5'b01110), .out(transistor_8_out), .gate(nor_1_out));
  Transistor #(.\type ("n"), .width(5)) transistor_9 (.in(5'b01110), .out(transistor_9_out), .gate(nor_1_out));
  Transistor #(.\type ("n"), .width(5)) transistor_10 (.in(5'b01110), .out(transistor_10_out), .gate(nor_1_out));
  Transistor #(.\type ("n"), .width(5)) transistor_11 (.in({5{1'b0}}), .out(transistor_11_out), .gate(nor_1_out));
  Transistor #(.width(5)) transistor_12 (.in(output_numder_1_out_2), .out(transistor_1_out), .gate(nor_1_out));
  Output_Numder output_numder_1 (
    .Energy(in_1), .out_2(output_numder_1_out_2), .out_3(output_numder_1_out_3),
    .out_4(output_numder_1_out_4), .out_5(output_numder_1_out_5), .out_6(output_numder_1_out_6),
    .out_7(output_numder_1_out_7), .out_8(output_numder_1_out_8), .out_9(output_numder_1_out_9),
    .out_10(output_numder_1_out_10), .out_11(output_numder_1_out_11), .out_12(output_numder_1_out_12));
  Transistor #(.width(5)) transistor_13 (.in(output_numder_1_out_5), .out(transistor_5_out), .gate(nor_1_out));
  Transistor #(.width(5)) transistor_14 (.in(output_numder_1_out_4), .out(transistor_4_out), .gate(nor_1_out));
  Transistor #(.width(5)) transistor_15 (.in(output_numder_1_out_3), .out(transistor_2_out), .gate(nor_1_out));
  Transistor #(.width(5)) transistor_16 (.in(output_numder_1_out_6), .out(transistor_3_out), .gate(nor_1_out));
  assign out_8 = ~transistor_6_out;  // NOT_Gate not_1, 5 bits wide
  assign out_7 = ~transistor_7_out;  // NOT_Gate not_2, 5 bits wide
  assign out_6 = ~transistor_3_out;  // NOT_Gate not_3, 5 bits wide
  assign out_5 = ~transistor_5_out;  // NOT_Gate not_4, 5 bits wide
  assign out_4 = ~transistor_4_out;  // NOT_Gate not_5, 5 bits wide
  assign out_3 = ~transistor_2_out;  // NOT_Gate not_6, 5 bits wide
  assign out_2 = ~transistor_1_out;  // NOT_Gate not_7, 5 bits wide
  Transistor #(.width(5)) transistor_17 (.in(output_numder_1_out_7), .out(transistor_7_out), .gate(nor_1_out));
  Transistor #(.width(5)) transistor_18 (.in(output_numder_1_out_9), .out(transistor_9_out), .gate(nor_1_out));
  Transistor #(.width(5)) transistor_19 (.in(output_numder_1_out_10), .out(transistor_8_out), .gate(nor_1_out));
  Transistor #(.width(5)) transistor_20 (.in(output_numder_1_out_8), .out(transistor_6_out), .gate(nor_1_out));
  assign out_12 = ~transistor_11_out;  // NOT_Gate not_8, 5 bits wide
  assign out_11 = ~transistor_10_out;  // NOT_Gate not_9, 5 bits wide
  assign out_10 = ~transistor_8_out;  // NOT_Gate not_10, 5 bits wide
  assign out_9 = ~transistor_9_out;  // NOT_Gate not_11, 5 bits wide
  Transistor #(.width(5)) transistor_21 (.in(output_numder_1_out_11), .out(transistor_10_out), .gate(nor_1_out));
  Transistor #(.width(5)) transistor_22 (.in(output_numder_1_out_12), .out(transistor_11_out), .gate(nor_1_out));
endmodule

module Col_1 (
  input  D,
  input  C,
  input  B,
  input  A,
  output e,
  output d_2,
  output c_2,
  output b_2,
  output a_2
);

  wire and_1_out, and_2_out, and_3_out, and_4_out, and_5_out, and_6_out, and_7_out, and_8_out, and_9_out,
       and_10_out, and_11_out, and_12_out, and_13_out, and_14_out, and_15_out, and_16_out, and_17_out,
       and_18_out, not_1_out, not_2_out, not_3_out, not_4_out, not_5_out, not_6_out, not_7_out, not_8_out,
       not_9_out, not_10_out, not_11_out, not_12_out, not_13_out, not_14_out, not_15_out, not_16_out,
       not_17_out, not_18_out, not_19_out, not_20_out, not_21_out, not_22_out, not_23_out, not_24_out,
       not_25_out, not_26_out, not_27_out, not_28_out, not_29_out, not_30_out, not_31_out, not_32_out,
       not_33_out, not_34_out, not_35_out, not_36_out;

  not not_1 (not_1_out, D);
  and and_1 (and_1_out, not_1_out, not_2_out);
  not not_2 (not_2_out, C);
  not not_3 (not_3_out, C);
  and and_2 (and_2_out, not_3_out, not_4_out);
  not not_4 (not_4_out, B);
  not not_5 (not_5_out, D);
  not not_6 (not_6_out, B);
  and and_3 (and_3_out, not_5_out, not_6_out, A);
  not not_7 (not_7_out, D);
  and and_4 (and_4_out, not_7_out, B, not_8_out);
  not not_8 (not_8_out, A);
  not not_9 (not_9_out, D);
  not not_10 (not_10_out, C);
  and and_5 (and_5_out, not_9_out, not_10_out, not_11_out);
  not not_11 (not_11_out, A);
  not not_12 (not_12_out, C);
  and and_6 (and_6_out, not_12_out, not_13_out, not_14_out);
  not not_13 (not_13_out, B);
  not not_14 (not_14_out, A);
  not not_15 (not_15_out, D);
  and and_7 (and_7_out, not_15_out, B, not_16_out);
  not not_16 (not_16_out, A);
  not not_17 (not_17_out, D);
  and and_8 (and_8_out, not_17_out, not_18_out);
  not not_18 (not_18_out, A);
  not not_19 (not_19_out, D);
  not not_20 (not_20_out, C);
  and and_9 (and_9_out, not_19_out, not_20_out, B);
  not not_21 (not_21_out, D);
  and and_10 (and_10_out, not_21_out, C, not_22_out);
  not not_22 (not_22_out, B);
  and and_11 (and_11_out, D, not_23_out, not_24_out);
  not not_23 (not_23_out, C);
  not not_24 (not_24_out, B);
  not not_25 (not_25_out, D);
  and and_12 (and_12_out, not_25_out, not_26_out);
  not not_26 (not_26_out, B);
  not not_27 (not_27_out, C);
  and and_13 (and_13_out, not_27_out, not_28_out);
  not not_28 (not_28_out, B);
  not not_29 (not_29_out, D);
  and and_14 (and_14_out, not_29_out, C, not_30_out);
  not not_30 (not_30_out, A);
  not not_31 (not_31_out, D);
  and and_15 (and_15_out, not_31_out, not_32_out);
  not not_32 (not_32_out, A);
  not not_33 (not_33_out, D);
  and and_16 (and_16_out, not_33_out, B);
  not not_34 (not_34_out, D);
  and and_17 (and_17_out, not_34_out, C);
  not not_35 (not_35_out, C);
  and and_18 (and_18_out, D, not_35_out, not_36_out);
  not not_36 (not_36_out, B);
  or or_1 (e, and_1_out, and_2_out, and_3_out, and_4_out);
  or or_2 (d_2, and_5_out, and_6_out, and_7_out);
  or or_3 (c_2, and_8_out, and_9_out, and_10_out, and_11_out);
  or or_4 (b_2, and_12_out, and_13_out, and_14_out);
  or or_5 (a_2, and_15_out, and_16_out, and_17_out, and_18_out);
endmodule

module Col_2 (
  input  D,
  input  C,
  input  B,
  input  A,
  output e,
  output d_2,
  output c_2,
  output b_2,
  output a_2
);

  wire and_1_out, and_2_out, and_3_out, and_4_out, and_5_out, and_6_out, and_7_out, and_8_out, and_9_out,
       and_10_out, and_11_out, and_12_out, not_1_out, not_2_out, not_3_out, not_4_out, not_5_out, not_6_out,
       not_7_out, not_8_out, not_9_out, not_10_out, not_11_out, not_12_out, not_13_out, not_14_out,
       not_15_out, not_16_out, not_17_out, not_18_out, not_19_out, not_20_out, not_21_out, not_22_out,
       not_23_out, not_24_out, not_25_out, not_26_out, not_27_out, not_28_out;

  not not_1 (not_1_out, D);
  and and_1 (and_1_out, not_1_out, not_2_out);
  not not_2 (not_2_out, C);
  not not_3 (not_3_out, C);
  and and_2 (and_2_out, not_3_out, not_4_out);
  not not_4 (not_4_out, B);
  not not_5 (not_5_out, D);
  and and_3 (and_3_out, not_5_out, not_6_out, A);
  not not_6 (not_6_out, B);
  not not_7 (not_7_out, D);
  and and_4 (and_4_out, not_7_out, B, not_8_out);
  not not_8 (not_8_out, A);
  not not_9 (not_9_out, D);
  not not_10 (not_10_out, C);
  not not_11 (not_11_out, B);
  not not_12 (not_12_out, D);
  and and_5 (and_5_out, not_12_out, not_13_out, A);
  not not_13 (not_13_out, C);
  not not_14 (not_14_out, D);
  not not_15 (not_15_out, C);
  and and_6 (and_6_out, not_14_out, not_15_out, B);
  not not_16 (not_16_out, D);
  and and_7 (and_7_out, not_16_out, C, not_17_out);
  not not_17 (not_17_out, B);
  not not_18 (not_18_out, D);
  and and_8 (and_8_out, not_18_out, C, not_19_out);
  not not_19 (not_19_out, A);
  and and_9 (and_9_out, D, not_20_out, not_21_out);
  not not_20 (not_20_out, C);
  not not_21 (not_21_out, B);
  not not_22 (not_22_out, D);
  not not_23 (not_23_out, C);
  not not_24 (not_24_out, B);
  not not_25 (not_25_out, C);
  and and_10 (and_10_out, not_25_out, not_26_out);
  not not_26 (not_26_out, B);
  not not_27 (not_27_out, D);
  and and_11 (and_11_out, not_27_out, A);
  not not_28 (not_28_out, D);
  and and_12 (and_12_out, not_28_out, B);
  or or_1 (e, and_1_out, and_2_out, and_3_out, and_4_out);
  and and_13 (d_2, not_9_out, not_10_out, not_11_out, A);
  or or_2 (c_2, and_5_out, and_6_out, and_7_out, and_8_out, and_9_out);
  and and_14 (b_2, not_22_out, not_23_out, not_24_out, A);
  or or_3 (a_2, and_10_out, and_11_out, and_12_out);
endmodule

module Col_3 (
  input  D,
  input  C,
  input  B,
  input  A,
  output e,
  output d_2,
  output c_2,
  output b_2,
  output a_2
);

  wire and_1_out, and_2_out, and_3_out, and_4_out, and_5_out, and_6_out, and_7_out, and_8_out, and_9_out,
       and_10_out, and_11_out, and_12_out, and_13_out, and_14_out, and_15_out, and_16_out, and_17_out,
       not_1_out, not_2_out, not_3_out, not_4_out, not_5_out, not_6_out, not_7_out, not_8_out, not_9_out,
       not_10_out, not_11_out, not_12_out, not_13_out, not_14_out, not_15_out, not_16_out, not_17_out,
       not_18_out, not_19_out, not_20_out, not_21_out, not_22_out, not_23_out, not_24_out, not_25_out,
       not_26_out, not_27_out, not_28_out, not_29_out, not_30_out, not_31_out;

  not not_1 (not_1_out, D);
  not not_2 (not_2_out, C);
  and and_1 (and_1_out, not_2_out, not_3_out);
  not not_3 (not_3_out, B);
  not not_4 (not_4_out, D);
  and and_2 (and_2_out, not_4_out, not_5_out, not_6_out);
  not not_5 (not_5_out, B);
  not not_6 (not_6_out, A);
  not not_7 (not_7_out, D);
  and and_3 (and_3_out, not_7_out, B, A);
  not not_8 (not_8_out, D);
  and and_4 (and_4_out, not_8_out, C);
  not not_9 (not_9_out, C);
  and and_5 (and_5_out, D, not_9_out, not_10_out);
  not not_10 (not_10_out, B);
  not not_11 (not_11_out, D);
  and and_6 (and_6_out, not_11_out, not_12_out);
  not not_12 (not_12_out, A);
  not not_13 (not_13_out, D);
  and and_7 (and_7_out, not_13_out, B);
  not not_14 (not_14_out, D);
  and and_8 (and_8_out, not_14_out, C);
  and and_9 (and_9_out, D, not_15_out, not_16_out);
  not not_15 (not_15_out, C);
  not not_16 (not_16_out, B);
  not not_17 (not_17_out, D);
  not not_18 (not_18_out, C);
  and and_10 (and_10_out, not_17_out, not_18_out, not_19_out);
  not not_19 (not_19_out, A);
  not not_20 (not_20_out, D);
  and and_11 (and_11_out, not_20_out, not_21_out, not_22_out);
  not not_21 (not_21_out, B);
  not not_22 (not_22_out, A);
  not not_23 (not_23_out, D);
  and and_12 (and_12_out, not_23_out, B, A);
  and and_13 (and_13_out, D, not_24_out, not_25_out);
  not not_24 (not_24_out, C);
  not not_25 (not_25_out, B);
  not not_26 (not_26_out, D);
  and and_14 (and_14_out, not_26_out, not_27_out);
  not not_27 (not_27_out, A);
  not not_28 (not_28_out, D);
  and and_15 (and_15_out, not_28_out, B);
  not not_29 (not_29_out, D);
  and and_16 (and_16_out, not_29_out, C);
  and and_17 (and_17_out, D, not_30_out, not_31_out);
  not not_30 (not_30_out, C);
  not not_31 (not_31_out, B);
  or or_1 (e, not_1_out, and_1_out);
  or or_2 (d_2, and_2_out, and_3_out, and_4_out, and_5_out);
  or or_3 (c_2, and_6_out, and_7_out, and_8_out, and_9_out);
  or or_4 (b_2, and_10_out, and_11_out, and_12_out, and_13_out);
  or or_5 (a_2, and_14_out, and_15_out, and_16_out, and_17_out);
endmodule

module Big_col_1 (
  input  Inversion,
  input  Zero,
  input  D,
  input  C,
  input  B,
  input  A,
  output [14:0] out_7
);

  wire and_1_out, and_2_out, and_3_out, and_4_out, and_5_out, and_6_out, and_7_out, and_8_out, and_9_out,
       and_10_out, and_11_out, and_12_out, and_13_out, and_14_out, and_15_out, and_16_out, and_17_out,
       and_18_out, and_19_out, not_1_out, not_2_out, not_3_out, not_4_out, not_5_out, not_6_out, not_7_out,
       not_8_out, not_9_out, not_10_out, not_11_out, not_12_out, not_13_out, not_14_out, not_15_out,
       not_16_out, not_17_out, not_18_out, not_19_out, not_20_out, not_21_out, not_22_out, not_23_out,
       not_24_out, not_25_out, not_26_out, not_27_out, not_28_out, not_29_out, not_30_out, not_31_out,
       not_32_out, not_33_out, not_34_out, not_35_out, not_36_out, or_1_out, or_2_out, or_3_out, or_4_out,
       or_5_out, or_6_out;
  wire [14:0] not_37_out;
  wire [14:2] and_20_out;

  not not_1 (not_1_out, D);
  and and_1 (and_1_out, not_1_out, not_2_out);
  not not_2 (not_2_out, C);
  not not_3 (not_3_out, C);
  and and_2 (and_2_out, not_3_out, not_4_out);
  not not_4 (not_4_out, B);
  not not_5 (not_5_out, D);
  and and_3 (and_3_out, not_5_out, not_6_out, A);
  not not_6 (not_6_out, B);
  not not_7 (not_7_out, D);
  and and_4 (and_4_out, not_7_out, B, not_8_out);
  not not_8 (not_8_out, A);
  not not_9 (not_9_out, D);
  and and_5 (and_5_out, not_9_out, not_10_out, not_11_out);
  not not_10 (not_10_out, C);
  not not_11 (not_11_out, A);
  not not_12 (not_12_out, C);
  not not_13 (not_13_out, B);
  and and_6 (and_6_out, not_12_out, not_13_out, not_14_out);
  not not_14 (not_14_out, A);
  not not_15 (not_15_out, D);
  and and_7 (and_7_out, not_15_out, B, not_16_out);
  not not_16 (not_16_out, A);
  not not_17 (not_17_out, D);
  not not_18 (not_18_out, A);
  not not_19 (not_19_out, D);
  not not_20 (not_20_out, C);
  not not_21 (not_21_out, D);
  not not_22 (not_22_out, B);
  not not_23 (not_23_out, C);
  not not_24 (not_24_out, B);
  not not_25 (not_25_out, D);
  not not_26 (not_26_out, B);
  not not_27 (not_27_out, C);
  not not_28 (not_28_out, B);
  not not_29 (not_29_out, D);
  not not_30 (not_30_out, A);
  not not_31 (not_31_out, D);
  not not_32 (not_32_out, A);
  not not_33 (not_33_out, D);
  not not_34 (not_34_out, D);
  not not_35 (not_35_out, C);
  not not_36 (not_36_out, B);
  and and_8 (and_8_out, A, C, ~B, D);  // AND_Gate
  or or_1 (or_1_out, and_1_out, and_2_out, and_3_out, and_4_out);
  or or_2 (or_2_out, and_5_out, and_6_out, and_7_out);
  and and_9 (and_9_out, not_17_out, not_18_out);
  and and_10 (and_10_out, not_19_out, not_20_out, B);
  and and_11 (and_11_out, not_21_out, C, not_22_out);
  and and_12 (and_12_out, D, not_23_out, not_24_out);
  and and_13 (and_13_out, not_25_out, not_26_out);
  or or_3 (or_3_out, and_13_out, and_14_out, and_15_out);
  and and_14 (and_14_out, not_27_out, not_28_out);
  and and_15 (and_15_out, not_29_out, C, not_30_out);
  and and_16 (and_16_out, not_31_out, not_32_out);
  and and_17 (and_17_out, not_33_out, B);
  and and_18 (and_18_out, not_34_out, C);
  and and_19 (and_19_out, D, not_35_out, not_36_out);
  or or_4 (or_4_out, and_9_out, and_10_out, and_11_out, and_12_out);
  or or_5 (or_5_out, and_16_out, and_17_out, and_18_out, and_19_out);
  and and_20 (and_20_out[2], Zero, or_1_out);
  and and_21 (and_20_out[5], Zero, or_2_out);
  and and_22 (and_20_out[11], Zero, or_3_out);
  and and_23 (and_20_out[14], Zero, or_5_out);
  and and_24 (and_20_out[8], Zero, or_6_out);
  or or_6 (or_6_out, or_4_out, and_8_out);
  Multiplexer #(.width(15), .enable("false")) multiplexer_1 (
    .in0({{3{and_20_out[14]}}, {3{and_20_out[11]}}, {3{and_20_out[8]}}, {3{and_20_out[5]}}, {3{and_20_out[2]}}}),
    .in1(not_37_out), .out(out_7), .sel(Inversion));
  assign not_37_out = ~{{3{and_20_out[14]}}, {3{and_20_out[11]}}, {3{and_20_out[8]}}, {3{and_20_out[5]}}, {3{and_20_out[2]}}};  // NOT_Gate not_37, 15 bits wide
endmodule

module Big_col_2 (
  input  Inversion,
  input  Zero,
  input  D,
  input  C,
  input  B,
  input  A,
  output [14:0] out_7
);

  wire and_1_out, and_2_out, and_3_out, and_4_out, and_5_out, and_6_out, and_7_out, and_8_out, and_9_out,
       and_10_out, and_11_out, and_12_out, and_13_out, and_14_out, and_15_out, not_1_out, not_2_out,
       not_3_out, not_4_out, not_5_out, not_6_out, not_7_out, not_8_out, not_9_out, not_10_out, not_11_out,
       not_12_out, not_13_out, not_14_out, not_15_out, not_16_out, not_17_out, not_18_out, not_19_out,
       not_20_out, not_21_out, not_22_out, not_23_out, not_24_out, not_25_out, not_26_out, not_27_out,
       not_28_out, or_1_out, or_2_out, or_3_out, or_4_out;
  wire [14:0] not_29_out;
  wire [14:2] and_16_out;

  not not_1 (not_1_out, D);
  not not_2 (not_2_out, C);
  not not_3 (not_3_out, C);
  not not_4 (not_4_out, B);
  not not_5 (not_5_out, D);
  not not_6 (not_6_out, B);
  not not_7 (not_7_out, D);
  not not_8 (not_8_out, A);
  not not_9 (not_9_out, D);
  not not_10 (not_10_out, C);
  not not_11 (not_11_out, B);
  not not_12 (not_12_out, D);
  not not_13 (not_13_out, C);
  not not_14 (not_14_out, D);
  not not_15 (not_15_out, C);
  not not_16 (not_16_out, D);
  not not_17 (not_17_out, B);
  not not_18 (not_18_out, D);
  not not_19 (not_19_out, A);
  not not_20 (not_20_out, C);
  not not_21 (not_21_out, B);
  not not_22 (not_22_out, D);
  not not_23 (not_23_out, C);
  not not_24 (not_24_out, B);
  not not_25 (not_25_out, C);
  not not_26 (not_26_out, B);
  not not_27 (not_27_out, D);
  not not_28 (not_28_out, D);
  and and_1 (and_1_out, not_1_out, not_2_out);
  and and_2 (and_2_out, not_3_out, not_4_out);
  and and_3 (and_3_out, not_5_out, not_6_out, A);
  and and_4 (and_4_out, not_7_out, B, not_8_out);
  and and_5 (and_5_out, not_9_out, not_10_out, not_11_out, A);
  and and_6 (and_6_out, not_12_out, not_13_out, A);
  and and_7 (and_7_out, not_14_out, not_15_out, B);
  and and_8 (and_8_out, not_16_out, C, not_17_out);
  and and_9 (and_9_out, not_18_out, C, not_19_out);
  and and_10 (and_10_out, D, not_20_out, not_21_out);
  and and_11 (and_11_out, not_22_out, not_23_out, not_24_out, A);
  and and_12 (and_12_out, not_25_out, not_26_out);
  and and_13 (and_13_out, not_27_out, A);
  and and_14 (and_14_out, not_28_out, B);
  or or_1 (or_1_out, and_1_out, and_2_out, and_3_out, and_4_out);
  or or_2 (or_2_out, and_6_out, and_7_out, and_8_out, and_9_out, and_10_out);
  or or_3 (or_3_out, and_12_out, and_13_out, and_14_out);
  and and_15 (and_15_out, A, C, ~B, D);  // AND_Gate
  and and_16 (and_16_out[2], Zero, or_1_out);
  and and_17 (and_16_out[5], and_5_out, Zero);
  and and_18 (and_16_out[8], Zero, or_4_out);
  or or_4 (or_4_out, or_2_out, and_15_out);
  and and_19 (and_16_out[11], and_11_out, Zero);
  and and_20 (and_16_out[14], or_3_out, Zero);
  assign not_29_out = ~{{3{and_16_out[14]}}, {3{and_16_out[11]}}, {3{and_16_out[8]}}, {3{and_16_out[5]}}, {3{and_16_out[2]}}};  // NOT_Gate not_29, 15 bits wide
  Multiplexer #(.width(15), .enable("false")) multiplexer_1 (
    .in0({{3{and_16_out[14]}}, {3{and_16_out[11]}}, {3{and_16_out[8]}}, {3{and_16_out[5]}}, {3{and_16_out[2]}}}),
    .in1(not_29_out), .out(out_7), .sel(Inversion));
endmodule

module Big_col_3 (
  input  Inversion,
  input  Zero,
  input  D,
  input  C,
  input  B,
  input  A,
  output [14:0] out_7
);

  wire and_1_out, and_2_out, and_3_out, and_4_out, and_5_out, and_6_out, and_7_out, and_8_out, and_9_out,
       and_10_out, and_11_out, and_12_out, and_13_out, and_14_out, and_15_out, and_16_out, and_17_out,
       and_18_out, not_1_out, not_2_out, not_3_out, not_4_out, not_5_out, not_6_out, not_7_out, not_8_out,
       not_9_out, not_10_out, not_11_out, not_12_out, not_13_out, not_14_out, not_15_out, not_16_out,
       not_17_out, not_18_out, not_19_out, not_20_out, not_21_out, not_22_out, not_23_out, not_24_out,
       not_25_out, not_26_out, not_27_out, not_28_out, not_29_out, not_30_out, not_31_out, or_1_out,
       or_2_out, or_3_out, or_4_out, or_5_out, or_6_out;
  wire [14:0] not_32_out;
  wire [14:2] and_19_out;

  not not_1 (not_1_out, C);
  not not_2 (not_2_out, B);
  not not_3 (not_3_out, D);
  not not_4 (not_4_out, B);
  not not_5 (not_5_out, A);
  not not_6 (not_6_out, D);
  not not_7 (not_7_out, D);
  not not_8 (not_8_out, C);
  not not_9 (not_9_out, B);
  not not_10 (not_10_out, D);
  not not_11 (not_11_out, A);
  not not_12 (not_12_out, D);
  not not_13 (not_13_out, D);
  not not_14 (not_14_out, C);
  not not_15 (not_15_out, B);
  not not_16 (not_16_out, D);
  not not_17 (not_17_out, C);
  not not_18 (not_18_out, A);
  not not_19 (not_19_out, D);
  not not_20 (not_20_out, B);
  not not_21 (not_21_out, A);
  not not_22 (not_22_out, D);
  not not_23 (not_23_out, C);
  not not_24 (not_24_out, B);
  not not_25 (not_25_out, D);
  not not_26 (not_26_out, A);
  not not_27 (not_27_out, D);
  not not_28 (not_28_out, D);
  not not_29 (not_29_out, C);
  not not_30 (not_30_out, B);
  not not_31 (not_31_out, D);
  and and_1 (and_1_out, not_1_out, not_2_out);
  and and_2 (and_2_out, not_3_out, not_4_out, not_5_out);
  and and_3 (and_3_out, not_6_out, B, A);
  and and_4 (and_4_out, not_7_out, C);
  and and_5 (and_5_out, D, not_8_out, not_9_out);
  and and_6 (and_6_out, not_10_out, not_11_out);
  and and_7 (and_7_out, not_12_out, B);
  and and_8 (and_8_out, not_13_out, C);
  and and_9 (and_9_out, D, not_14_out, not_15_out);
  and and_10 (and_10_out, not_16_out, not_17_out, not_18_out);
  and and_11 (and_11_out, not_19_out, not_20_out, not_21_out);
  and and_12 (and_12_out, not_22_out, B, A);
  and and_13 (and_13_out, D, not_23_out, not_24_out);
  and and_14 (and_14_out, not_25_out, not_26_out);
  and and_15 (and_15_out, not_27_out, B);
  and and_16 (and_16_out, not_28_out, C);
  and and_17 (and_17_out, D, not_29_out, not_30_out);
  and and_18 (and_18_out, A, C, ~B, D);  // AND_Gate
  or or_1 (or_1_out, not_31_out, and_1_out);
  or or_2 (or_2_out, and_2_out, and_3_out, and_4_out, and_5_out);
  or or_3 (or_3_out, and_6_out, and_7_out, and_8_out, and_9_out);
  or or_4 (or_4_out, and_10_out, and_11_out, and_12_out, and_13_out);
  or or_5 (or_5_out, and_14_out, and_15_out, and_16_out, and_17_out);
  and and_19 (and_19_out[2], Zero, or_1_out);
  and and_20 (and_19_out[5], Zero, or_2_out);
  or or_6 (or_6_out, or_3_out, and_18_out);
  and and_21 (and_19_out[8], Zero, or_6_out);
  and and_22 (and_19_out[11], Zero, or_4_out);
  and and_23 (and_19_out[14], or_5_out, Zero);
  Multiplexer #(.width(15), .enable("false")) multiplexer_1 (
    .in0({{3{and_19_out[14]}}, {3{and_19_out[11]}}, {3{and_19_out[8]}}, {3{and_19_out[5]}}, {3{and_19_out[2]}}}),
    .in1(not_32_out), .out(out_7), .sel(Inversion));
  assign not_32_out = ~{{3{and_19_out[14]}}, {3{and_19_out[11]}}, {3{and_19_out[8]}}, {3{and_19_out[5]}}, {3{and_19_out[2]}}};  // NOT_Gate not_32, 15 bits wide
endmodule

module Output_big_numder (
  input  [6:0] in_1,
  input  INV,
  output [14:0] out_3,
  output [14:0] out_4,
  output [14:0] out_5,
  output [14:0] out_6,
  output [14:0] out_7,
  output [14:0] out_8,
  output [14:0] out_9,
  output [14:0] out_10,
  output [14:0] out_11
);

  Big_col_1 big_col_1_1 (
    .Zero(in_1[5]), .D(in_1[3]), .C(in_1[2]), .B(in_1[1]), .A(in_1[0]), .out_7(out_3), .Inversion(INV));
  Big_col_2 big_col_2_1 (
    .Zero(in_1[5]), .D(in_1[3]), .C(in_1[2]), .B(in_1[1]), .A(in_1[0]), .out_7(out_6), .Inversion(INV));
  Big_col_3 big_col_3_1 (
    .Zero(in_1[5]), .D(in_1[3]), .C(in_1[2]), .B(in_1[1]), .A(in_1[0]), .out_7(out_9), .Inversion(INV));

  assign out_4 = out_3;
  assign out_5 = out_3;
  assign out_7 = out_6;
  assign out_8 = out_6;
  assign out_10 = out_9;
  assign out_11 = out_9;
endmodule

module Width (
  input  \Принята_ли_клетка ,
  input  new_task,
  output [1:0] out_3,
  output [14:0] out_4,
  output [14:0] out_5,
  output [14:0] out_6,
  output [14:0] out_7,
  output [14:0] out_8,
  output [14:0] out_9,
  output [14:0] out_10,
  output [14:0] out_11,
  output [14:0] out_12
);

  wire [1:0] random_1_out;
  wire [2:0] inc_1_out_2;

  Random #(.width(2), .seed(1)) random_1 (.clk(new_task), .out(random_1_out));  // open: next, clr
  assign out_3 = \Принята_ли_клетка  ? random_1_out : 2'bz;  // Controlled_Buffer controlled_buffer_1
  inc inc_1 (.in_1(random_1_out), .out_2(inc_1_out_2));
  DotMatrix #(.matrixcols(9), .matrixrows(15)) dotmatrix_1 (
    .col0(out_4), .col1(out_4), .col2(out_4), .col3(out_7), .col4(out_7), .col5(out_7), .col6(out_10),
    .col7(out_10), .col8(out_10));
  // Probe on inc_1_out_2
  Big_col_1 big_col_1_1 (
    .Zero(new_task), .D(1'b0), .C(inc_1_out_2[2]), .B(inc_1_out_2[1]), .A(inc_1_out_2[0]), .out_7(out_4),
    .Inversion(1'b0));
  Big_col_2 big_col_2_1 (
    .Zero(new_task), .D(1'b0), .C(inc_1_out_2[2]), .B(inc_1_out_2[1]), .A(inc_1_out_2[0]), .out_7(out_7),
    .Inversion(1'b0));
  Big_col_3 big_col_3_1 (
    .Zero(new_task), .D(1'b0), .C(inc_1_out_2[2]), .B(inc_1_out_2[1]), .A(inc_1_out_2[0]), .out_7(out_10),
    .Inversion(1'b0));

  assign out_5 = out_4;
  assign out_6 = out_4;
  assign out_8 = out_7;
  assign out_9 = out_7;
  assign out_11 = out_10;
  assign out_12 = out_10;
endmodule

module task2_0 (
  input  [15:0] \Удали_меня_позже ,
  input  Clk,
  input  MOSI,
  output \генератор 
);

  input_shifter input_shifter_1 (.MOSI(MOSI), .CLK(Clk));  // open: Reset, Data_out, buffer_ptr
  DotMatrix #(.matrixcols(9), .matrixrows(15)) dotmatrix_1 ();  // open: col0, col1, col2, col3, col4, col5, col6, col7, col8
  DotMatrix #(.matrixcols(9), .matrixrows(15)) dotmatrix_2 ();  // open: col0, col1, col2, col3, col4, col5, col6, col7, col8
  DotMatrix #(.matrixcols(24), .matrixrows(2)) dotmatrix_3 (
    .col0(2'b11), .col1(2'b11), .col2(2'b11), .col3(2'b11), .col4(2'b11), .col5(2'b11), .col6(2'b11),
    .col7(2'b11), .col8(2'b11), .col9(2'b11), .col10(2'b11), .col11(2'b11), .col12(2'b11), .col13(2'b11),
    .col14(2'b11), .col15(2'b11), .col16(2'b11), .col17(2'b11), .col18(2'b11), .col19(2'b11), .col20(2'b11),
    .col21(2'b11), .col22(2'b11), .col23(2'b11));
  DotMatrix #(.matrixcols(7), .matrixrows(5)) dotmatrix_4 ();  // open: col0, col1, col2, col3, col4, col5, col6
  DotMatrix #(.matrixcols(7), .matrixrows(5)) dotmatrix_5 ();  // open: col0, col1, col2, col3, col4, col5, col6
  DotMatrix #(.matrixcols(24), .matrixrows(2)) dotmatrix_6 (
    .col0(2'b11), .col1(2'b11), .col2(2'b11), .col3(2'b11), .col4(2'b11), .col5(2'b11), .col6(2'b11),
    .col7(2'b11), .col8(2'b11), .col9(2'b11), .col10(2'b11), .col11(2'b11), .col12(2'b11), .col13(2'b11),
    .col14(2'b11), .col15(2'b11), .col16(2'b11), .col17(2'b11), .col18(2'b11), .col19(2'b11), .col20(2'b11),
    .col21(2'b11), .col22(2'b11), .col23(2'b11));
  DotMatrix #(.matrixcols(7), .matrixrows(5)) dotmatrix_7 ();  // open: col0, col1, col2, col3, col4, col5, col6
  DotMatrix #(.matrixcols(7), .matrixrows(5)) dotmatrix_8 ();  // open: col0, col1, col2, col3, col4, col5, col6
  DotMatrix #(.matrixcols(7), .matrixrows(5)) dotmatrix_9 ();  // open: col0, col1, col2, col3, col4, col5, col6
  DotMatrix #(.matrixcols(7), .matrixrows(5)) dotmatrix_10 ();  // open: col0, col1, col2, col3, col4, col5, col6
  DotMatrix #(.matrixcols(23), .matrixrows(2)) dotmatrix_11 (
    .col0(2'b11), .col1(2'b11), .col2(2'b11), .col3(2'b11), .col4(2'b11), .col5(2'b11), .col6(2'b11),
    .col7(2'b11), .col8(2'b11), .col9(2'b11), .col10(2'b11), .col11(2'b11), .col12(2'b11), .col13(2'b11),
    .col14(2'b11), .col15(2'b11), .col16(2'b11), .col17(2'b11), .col18(2'b11), .col19(2'b11), .col20(2'b11),
    .col21(2'b11), .col22(2'b11));
  DotMatrix #(.matrixcols(7), .matrixrows(5)) dotmatrix_12 ();  // open: col0, col1, col2, col3, col4, col5, col6
  DotMatrix #(.matrixcols(7), .matrixrows(5)) dotmatrix_13 ();  // open: col0, col1, col2, col3, col4, col5, col6
  DotMatrix #(.matrixcols(23), .matrixrows(2)) dotmatrix_14 (
    .col0(2'b11), .col1(2'b11), .col2(2'b11), .col3(2'b11), .col4(2'b11), .col5(2'b11), .col6(2'b11),
    .col7(2'b11), .col8(2'b11), .col9(2'b11), .col10(2'b11), .col11(2'b11), .col12(2'b11), .col13(2'b11),
    .col14(2'b11), .col15(2'b11), .col16(2'b11), .col17(2'b11), .col18(2'b11), .col19(2'b11), .col20(2'b11),
    .col21(2'b11), .col22(2'b11));
  DotMatrix #(.matrixcols(7), .matrixrows(5)) dotmatrix_15 ();  // open: col0, col1, col2, col3, col4, col5, col6
  DotMatrix #(.matrixcols(7), .matrixrows(5)) dotmatrix_16 ();  // open: col0, col1, col2, col3, col4, col5, col6

  assign \генератор  = \Удали_меня_позже [4];
endmodule

module height (
  input  \Принята_ли_клетка ,
  input  new_task,
  output [1:0] out_3,
  output [14:0] out_4,
  output [14:0] out_5,
  output [14:0] out_6,
  output [14:0] out_7,
  output [14:0] out_8,
  output [14:0] out_9,
  output [14:0] out_10,
  output [14:0] out_11,
  output [14:0] out_12
);

  wire [1:0] random_1_out;
  wire [2:0] inc_1_out_2;

  Joystick joystick_1 ();  // open: x, y
  Joystick joystick_2 ();  // open: x, y
  Random #(.width(2)) random_1 (.clk(new_task), .out(random_1_out));  // open: next, clr
  assign out_3 = \Принята_ли_клетка  ? random_1_out : 2'bz;  // Controlled_Buffer controlled_buffer_1
  // Probe on inc_1_out_2
  inc inc_1 (.in_1(random_1_out), .out_2(inc_1_out_2));
  DotMatrix #(.matrixcols(9), .matrixrows(15)) dotmatrix_1 (
    .col0(out_4), .col1(out_4), .col2(out_4), .col3(out_7), .col4(out_7), .col5(out_7), .col6(out_10),
    .col7(out_10), .col8(out_10));
  Big_col_1 big_col_1_1 (
    .Zero(new_task), .D(1'b0), .C(inc_1_out_2[2]), .B(inc_1_out_2[1]), .A(inc_1_out_2[0]), .out_7(out_4),
    .Inversion(1'b0));
  Big_col_2 big_col_2_1 (
    .Zero(new_task), .D(1'b0), .C(inc_1_out_2[2]), .B(inc_1_out_2[1]), .A(inc_1_out_2[0]), .out_7(out_7),
    .Inversion(1'b0));
  Big_col_3 big_col_3_1 (
    .Zero(new_task), .D(1'b0), .C(inc_1_out_2[2]), .B(inc_1_out_2[1]), .A(inc_1_out_2[0]), .out_7(out_10),
    .Inversion(1'b0));

  assign out_5 = out_4;
  assign out_6 = out_4;
  assign out_8 = out_7;
  assign out_9 = out_7;
  assign out_11 = out_10;
  assign out_12 = out_10;
endmodule

module local_test (
  input  [15:0] in_1,
  output [3:0] out_2
);

  wire n, \task2_0_1_генератор , y;
  wire [14:0] height_1_out_4, height_1_out_5, height_1_out_6, height_1_out_7, height_1_out_8, height_1_out_9,
       height_1_out_10, height_1_out_11, height_1_out_12, width_1_out_4, width_1_out_5, width_1_out_6,
       width_1_out_7, width_1_out_8, width_1_out_9, width_1_out_10, width_1_out_11, width_1_out_12;

  task2_0 task2_0_1 (.\Удали_меня_позже (in_1), .\генератор (\task2_0_1_генератор ));  // open: Clk, MOSI
  LED led_1 (.in(1'b1));
  LED led_2 (.in(1'b1));
  LED led_3 (.in(1'b1));
  DotMatrix #(.matrixcols(9), .matrixrows(15)) dotmatrix_1 (
    .col0(width_1_out_4), .col1(width_1_out_5), .col2(width_1_out_6), .col3(width_1_out_7),
    .col4(width_1_out_8), .col5(width_1_out_9), .col6(width_1_out_10), .col7(width_1_out_11),
    .col8(width_1_out_12));
  Width width_1 (
    .new_task(\task2_0_1_генератор ), .out_4(width_1_out_4), .out_5(width_1_out_5), .out_6(width_1_out_6),
    .out_7(width_1_out_7), .out_8(width_1_out_8), .out_9(width_1_out_9), .out_10(width_1_out_10),
    .out_11(width_1_out_11), .out_12(width_1_out_12), .out_3(out_2[1:0]), .\Принята_ли_клетка (y));
  LED led_4 (.in(1'b1));
  LED led_5 (.in(1'b1));
  LED led_6 (.in(1'b1));
  LED led_7 (.in(1'b1));
  LED led_8 (.in(1'b1));
  Button button_1 (.out(y));
  LED led_9 (.in(1'b1));
  LED led_10 (.in(1'b1));
  LED led_11 (.in(1'b1));
  LED led_12 (.in(1'b1));
  LED led_13 (.in(1'b1));
  LED led_14 (.in(1'b1));
  Button button_2 (.out(n));
  DotMatrix #(.matrixcols(9), .matrixrows(15)) dotmatrix_2 (
    .col0(height_1_out_4), .col1(height_1_out_5), .col2(height_1_out_6), .col3(height_1_out_7),
    .col4(height_1_out_8), .col5(height_1_out_9), .col6(height_1_out_10), .col7(height_1_out_11),
    .col8(height_1_out_12));
  height height_1 (
    .new_task(\task2_0_1_генератор ), .out_4(height_1_out_4), .out_5(height_1_out_5), .out_6(height_1_out_6),
    .out_7(height_1_out_7), .out_8(height_1_out_8), .out_9(height_1_out_9), .out_10(height_1_out_10),
    .out_11(height_1_out_11), .out_12(height_1_out_12), .\Принята_ли_клетка (y), .out_3(out_2[3:2]));
  // Probe on out_2[1:0]
  // Probe on out_2[3:2]
  // output_shifter output_shifter_1: pin names not known
endmodule

module table_first (
  input  [1:0] Weight,
  input  [1:0] Hight,
  output [4:0] out_3,
  output [4:0] out_4,
  output [4:0] out_5,
  output [4:0] out_6,
  output [4:0] out_7,
  output [4:0] out_8,
  output [4:0] out_9,
  output Busy
);

  wire [2:0] inc_1_out_2, inc_2_out_2;

  inc inc_1 (.in_1(Weight), .out_2(inc_1_out_2));
  inc inc_2 (.in_1(Hight), .out_2(inc_2_out_2));
  Col_1 col_1_1 (
    .D(1'b0), .C(inc_1_out_2[2]), .B(inc_1_out_2[1]), .A(inc_1_out_2[0]), .e(out_3[0]), .d_2(out_3[1]),
    .c_2(out_3[2]), .b_2(out_3[3]), .a_2(out_3[4]));
  Col_2 col_2_1 (
    .D(1'b0), .C(inc_1_out_2[2]), .B(inc_1_out_2[1]), .A(inc_1_out_2[0]), .e(out_4[0]), .d_2(out_4[1]),
    .c_2(out_4[2]), .b_2(out_4[3]), .a_2(out_4[4]));
  Col_3 col_3_1 (
    .D(1'b0), .C(inc_1_out_2[2]), .B(inc_1_out_2[1]), .A(inc_1_out_2[0]), .e(out_5[0]), .d_2(out_5[1]),
    .c_2(out_5[2]), .b_2(out_5[3]), .a_2(out_5[4]));
  Col_1 col_1_2 (
    .D(1'b0), .C(inc_2_out_2[2]), .B(inc_2_out_2[1]), .A(inc_2_out_2[0]), .e(out_7[0]), .d_2(out_7[1]),
    .c_2(out_7[2]), .b_2(out_7[3]), .a_2(out_7[4]));
  Col_2 col_2_2 (
    .D(1'b0), .C(inc_2_out_2[2]), .B(inc_2_out_2[1]), .A(inc_2_out_2[0]), .e(out_8[0]), .d_2(out_8[1]),
    .c_2(out_8[2]), .b_2(out_8[3]), .a_2(out_8[4]));
  Col_3 col_3_2 (
    .D(1'b0), .C(inc_2_out_2[2]), .B(inc_2_out_2[1]), .A(inc_2_out_2[0]), .e(out_9[0]), .d_2(out_9[1]),
    .c_2(out_9[2]), .b_2(out_9[3]), .a_2(out_9[4]));
  or or_1 (Busy, inc_2_out_2[0], inc_2_out_2[1], inc_2_out_2[2]);

  assign out_6 = {5{1'b0}};
endmodule

module \table  (
  input  Busy,
  input  [1:0] Weight,
  input  [1:0] Hight,
  output [4:0] out_4,
  output [4:0] out_5,
  output [4:0] out_6,
  output Busy_2,
  output [4:0] out_8,
  output [4:0] out_9,
  output [4:0] out_10,
  output [4:0] out_11
);

  wire [2:0] inc_1_out_2, undriven;
  wire [4:0] col_1_1_e, col_2_1_e, col_3_1_e;

  inc inc_1 (.in_1(Weight), .out_2(inc_1_out_2));
  or or_1 (Busy_2, out_4[0], out_4[1], out_4[2], out_4[3], out_4[4]);
  Multiplexer #(.width(5), .enable("false")) multiplexer_1 (.in0({5{1'b0}}), .in1(col_1_1_e), .out(out_4), .sel(Busy));
  Multiplexer #(.width(5), .enable("false")) multiplexer_2 (.in0({5{1'b0}}), .in1(col_2_1_e), .out(out_5), .sel(Busy));
  Multiplexer #(.width(5), .enable("false")) multiplexer_3 (.in0({5{1'b0}}), .in1(col_3_1_e), .out(out_6), .sel(Busy));
  Col_1 col_1_1 (
    .D(1'b0), .C(inc_1_out_2[2]), .B(inc_1_out_2[1]), .A(inc_1_out_2[0]), .e(col_1_1_e[0]),
    .d_2(col_1_1_e[1]), .c_2(col_1_1_e[2]), .b_2(col_1_1_e[3]), .a_2(col_1_1_e[4]));
  Col_2 col_2_1 (
    .D(1'b0), .C(inc_1_out_2[2]), .B(inc_1_out_2[1]), .A(inc_1_out_2[0]), .e(col_2_1_e[0]),
    .d_2(col_2_1_e[1]), .c_2(col_2_1_e[2]), .b_2(col_2_1_e[3]), .a_2(col_2_1_e[4]));
  Col_3 col_3_1 (
    .D(1'b0), .C(inc_1_out_2[2]), .B(inc_1_out_2[1]), .A(inc_1_out_2[0]), .e(col_3_1_e[0]),
    .d_2(col_3_1_e[1]), .c_2(col_3_1_e[2]), .b_2(col_3_1_e[3]), .a_2(col_3_1_e[4]));
  Col_1 col_1_2 (
    .D(1'b0), .C(undriven[2]), .B(undriven[1]), .A(undriven[0]), .e(out_9[0]), .d_2(out_9[1]),
    .c_2(out_9[2]), .b_2(out_9[3]), .a_2(out_9[4]));
  Col_2 col_2_2 (
    .D(1'b0), .C(undriven[2]), .B(undriven[1]), .A(undriven[0]), .e(out_10[0]), .d_2(out_10[1]),
    .c_2(out_10[2]), .b_2(out_10[3]), .a_2(out_10[4]));
  Col_3 col_3_2 (
    .D(1'b0), .C(undriven[2]), .B(undriven[1]), .A(undriven[0]), .e(out_11[0]), .d_2(out_11[1]),
    .c_2(out_11[2]), .b_2(out_11[3]), .a_2(out_11[4]));

  assign out_8 = {5{1'b0}};
endmodule

module Table_all (
  input  [1:0] in_1,
  input  [1:0] in_2
);

  wire table_first_1_busy, undriven, undriven_2;
  wire [1:0] controlled_buffer_1_out, controlled_buffer_2_out, controlled_buffer_3_out,
       controlled_buffer_4_out;
  wire [4:0] table_1_out_4, table_1_out_5, table_1_out_6, table_1_out_8, table_1_out_9, table_1_out_10,
       table_1_out_11, table_2_out_4, table_2_out_5, table_2_out_6, table_2_out_8, table_2_out_9,
       table_2_out_10, table_2_out_11, table_first_1_out_3, table_first_1_out_4, table_first_1_out_5,
       table_first_1_out_6, table_first_1_out_7, table_first_1_out_8, table_first_1_out_9;
  wire [15:0] input_shifter_1_data_out;

  input_shifter input_shifter_1 (.CLK(undriven), .Data_out(input_shifter_1_data_out));  // open: MOSI, Reset, buffer_ptr
  DotMatrix #(.matrixcols(7), .matrixrows(5)) dotmatrix_1 (
    .col0(table_first_1_out_3), .col1(table_first_1_out_4), .col2(table_first_1_out_5),
    .col3(table_first_1_out_6), .col4(table_first_1_out_7), .col5(table_first_1_out_8),
    .col6(table_first_1_out_9));
  table_first table_first_1 (
    .Weight(in_1), .Hight(in_2), .Busy(table_first_1_busy), .out_3(table_first_1_out_3),
    .out_4(table_first_1_out_4), .out_5(table_first_1_out_5), .out_6(table_first_1_out_6),
    .out_7(table_first_1_out_7), .out_8(table_first_1_out_8), .out_9(table_first_1_out_9));
  assign controlled_buffer_1_out = table_first_1_busy ? in_1 : 2'bz;  // Controlled_Buffer controlled_buffer_1
  assign controlled_buffer_2_out = table_first_1_busy ? in_2 : 2'bz;  // Controlled_Buffer controlled_buffer_2
  DotMatrix #(.matrixcols(7), .matrixrows(5)) dotmatrix_2 (
    .col0(table_1_out_4), .col1(table_1_out_5), .col2(table_1_out_6), .col3(table_1_out_8),
    .col4(table_1_out_9), .col5(table_1_out_10), .col6(table_1_out_11));
  \table  table_1 (
    .Weight(controlled_buffer_1_out), .Hight(controlled_buffer_2_out), .out_4(table_1_out_4),
    .out_5(table_1_out_5), .out_6(table_1_out_6), .out_8(table_1_out_8), .out_9(table_1_out_9),
    .out_10(table_1_out_10), .out_11(table_1_out_11));  // open: Busy_2, Busy
  assign controlled_buffer_3_out = undriven_2 ? in_1 : 2'bz;  // Controlled_Buffer controlled_buffer_3
  \table  table_2 (
    .Weight(controlled_buffer_3_out), .Hight(controlled_buffer_4_out), .out_4(table_2_out_4),
    .out_5(table_2_out_5), .out_6(table_2_out_6), .out_8(table_2_out_8), .out_9(table_2_out_9),
    .out_10(table_2_out_10), .out_11(table_2_out_11));  // open: Busy_2, Busy
  DotMatrix #(.matrixcols(7), .matrixrows(5)) dotmatrix_3 (
    .col0(table_2_out_4), .col1(table_2_out_5), .col2(table_2_out_6), .col3(table_2_out_8),
    .col4(table_2_out_9), .col5(table_2_out_10), .col6(table_2_out_11));
  assign controlled_buffer_4_out = undriven_2 ? in_2 : 2'bz;  // Controlled_Buffer controlled_buffer_4

  // Other names for the same wires on the sheet: H[1:0] = in_2; W[1:0] = in_1
endmodule

module inc (
  input  [1:0] in_1,
  output [2:0] out_2
);

  wire [0:0] and_1_out;

  assign {out_2[2], and_1_out[0]} = {and_1_out[0], 1'b1} & in_1;  // AND_Gate and_1, 2 bits wide
  assign out_2[1:0] = in_1 ^ {and_1_out[0], 1'b1};  // XOR_Gate xor_1, 2 bits wide
endmodule

module otladka (
  input  [11:0] in_1,
  input  [11:0] in_2,
  output [4:0] out_3,
  output [4:0] out_4,
  output [4:0] out_5,
  output [4:0] out_6,
  output [4:0] out_7,
  output [4:0] out_8,
  output [4:0] out_9,
  output [4:0] out_10,
  output [4:0] out_11,
  output [4:0] out_12,
  output [4:0] out_13,
  output [4:0] out_14,
  output [4:0] out_15,
  output [4:0] out_16,
  output [4:0] out_17,
  output [4:0] out_18,
  output [4:0] out_19,
  output [4:0] out_20,
  output [4:0] out_21,
  output [11:0] out_22,
  output [11:0] out_23
);

  wire L, or_2_out, R;
  wire [9:0] transistor_4_out;

  Transistor #(.\type ("n"), .width(5)) transistor_1 (.in(5'b01110), .out(out_20), .gate(R));
  Transistor #(.\type ("n"), .width(5)) transistor_2 (.in(5'b00100), .out(out_21), .gate(R));
  or or_1 (L, in_2[0], in_2[1], in_2[2], in_2[3], in_2[4], in_2[5], in_2[6], in_2[7], in_2[8], in_2[9]);
  Transistor #(.\type ("n"), .width(5)) transistor_3 (.in({5{1'b1}}), .out(out_19), .gate(R));
  Transistor #(.\type ("n"), .width(10)) transistor_4 (.in(in_2[9:0]), .out(transistor_4_out), .gate(L));
  Transistor #(.width(5)) transistor_5 (.in({5{1'b0}}), .out(out_21), .gate(R));
  Transistor #(.width(5)) transistor_6 (.in({5{1'b0}}), .out(out_20), .gate(R));
  Transistor #(.width(10)) transistor_7 (.in({10{1'b0}}), .out(transistor_4_out), .gate(or_2_out));
  or or_2 (or_2_out, R, L);
  Transistor #(.width(5)) transistor_8 (.in({5{1'b0}}), .out(out_19), .gate(R));
  Transistor #(.\type ("n"), .width(10)) transistor_9 (.in(in_1[9:0]), .out(transistor_4_out), .gate(R));
  DotMatrix #(.matrixcols(19), .matrixrows(5)) dotmatrix_1 (
    .col0(out_21), .col1(out_20), .col2(out_19), .col3({5{1'b0}}), .col4(out_17), .col5(out_16),
    .col6(out_15), .col7(out_14), .col8(out_13), .col9(out_12), .col10(out_11), .col11(out_10),
    .col12(out_9), .col13(out_8), .col14(out_7), .col15({5{1'b0}}), .col16(out_5), .col17(out_4),
    .col18(out_3));
  full_diget_namber full_diget_namber_1 (
    .in_1(transistor_4_out), .in_2(1'b0), .out_3(out_17), .out_4(out_16), .out_5(out_15), .out_6(out_14),
    .out_7(out_13), .out_8(out_12), .out_9(out_11), .out_10(out_10), .out_11(out_9), .out_12(out_8),
    .out_13(out_7));
  Transistor #(.\type ("n"), .width(5)) transistor_10 (.in({5{1'b1}}), .out(out_5), .gate(L));
  Transistor #(.\type ("n"), .width(5)) transistor_11 (.in(5'b00100), .out(out_3), .gate(L));
  Transistor #(.\type ("n"), .width(5)) transistor_12 (.in(5'b01110), .out(out_4), .gate(L));
  Transistor #(.width(5)) transistor_13 (.in({5{1'b0}}), .out(out_3), .gate(L));
  Transistor #(.width(5)) transistor_14 (.in({5{1'b0}}), .out(out_4), .gate(L));
  Transistor #(.width(5)) transistor_15 (.in({5{1'b0}}), .out(out_5), .gate(L));
  or or_3 (R, in_1[0], in_1[1], in_1[2], in_1[3], in_1[4], in_1[5], in_1[6], in_1[7], in_1[8], in_1[9]);

  assign in_2[10] = in_2[11];
  assign out_6 = {5{1'b0}};
  assign out_18 = {5{1'b0}};
  assign out_22 = {{2{in_2[11]}}, in_2[9:0]};
  assign out_23 = in_1;

  // Other names for the same wires on the sheet: _10_l = in_2[11]; L1[4:0] = out_5; L2[4:0] = out_4; L3[4:0] = out_3;
  //   _10_r = in_1[10]; _11_r = in_1[11]; R1[4:0] = out_21; R2[4:0] = out_20; R3[4:0] = out_19
endmodule

module otladka___v (
  input  [11:0] in_1,
  input  [11:0] in_2,
  output [4:0] out_3,
  output [4:0] out_4,
  output [4:0] out_5,
  output [4:0] out_6,
  output [4:0] out_7,
  output [4:0] out_8,
  output [4:0] out_9,
  output [4:0] out_10,
  output [4:0] out_11,
  output [4:0] out_12,
  output [4:0] out_13,
  output [4:0] out_14,
  output [4:0] out_15,
  output [4:0] out_16,
  output [4:0] out_17,
  output [4:0] out_18,
  output [4:0] out_19,
  output [4:0] out_20,
  output [4:0] out_21,
  output [11:0] out_22,
  output [11:0] out_23
);

  wire L, or_2_out, R;
  wire [9:0] transistor_4_out;

  Transistor #(.\type ("n"), .width(5)) transistor_1 (.in(5'b11100), .out(out_21), .gate(R));
  Transistor #(.\type ("n"), .width(5)) transistor_2 (.in(5'b00011), .out(out_20), .gate(R));
  or or_1 (L, in_2[0], in_2[1], in_2[2], in_2[3], in_2[4], in_2[5], in_2[6], in_2[7], in_2[8], in_2[9]);
  Transistor #(.\type ("n"), .width(5)) transistor_3 (.in(5'b11100), .out(out_19), .gate(R));
  Transistor #(.\type ("n"), .width(10)) transistor_4 (.in(in_2[9:0]), .out(transistor_4_out), .gate(L));
  Transistor #(.width(5)) transistor_5 (.in({5{1'b0}}), .out(out_20), .gate(R));
  Transistor #(.width(5)) transistor_6 (.in({5{1'b0}}), .out(out_21), .gate(R));
  Transistor #(.width(10)) transistor_7 (.in({10{1'b0}}), .out(transistor_4_out), .gate(or_2_out));
  or or_2 (or_2_out, R, L);
  Transistor #(.width(5)) transistor_8 (.in({5{1'b0}}), .out(out_19), .gate(R));
  Transistor #(.\type ("n"), .width(10)) transistor_9 (.in(in_1[9:0]), .out(transistor_4_out), .gate(R));
  DotMatrix #(.matrixcols(19), .matrixrows(5)) dotmatrix_1 (
    .col0(out_21), .col1(out_20), .col2(out_19), .col3({5{1'b0}}), .col4(out_17), .col5(out_16),
    .col6(out_15), .col7(out_14), .col8(out_13), .col9(out_12), .col10(out_11), .col11(out_10),
    .col12(out_9), .col13(out_8), .col14(out_7), .col15({5{1'b0}}), .col16(out_5), .col17(out_4),
    .col18(out_3));
  full_diget_namber full_diget_namber_1 (
    .in_1(transistor_4_out), .in_2(1'b0), .out_3(out_17), .out_4(out_16), .out_5(out_15), .out_6(out_14),
    .out_7(out_13), .out_8(out_12), .out_9(out_11), .out_10(out_10), .out_11(out_9), .out_12(out_8),
    .out_13(out_7));
  Transistor #(.\type ("n"), .width(5)) transistor_10 (.in(5'b00111), .out(out_3), .gate(L));
  Transistor #(.\type ("n"), .width(5)) transistor_11 (.in(5'b00111), .out(out_5), .gate(L));
  Transistor #(.\type ("n"), .width(5)) transistor_12 (.in(5'b11000), .out(out_4), .gate(L));
  Transistor #(.width(5)) transistor_13 (.in({5{1'b0}}), .out(out_5), .gate(L));
  Transistor #(.width(5)) transistor_14 (.in({5{1'b0}}), .out(out_3), .gate(L));
  Transistor #(.width(5)) transistor_15 (.in({5{1'b0}}), .out(out_4), .gate(L));
  or or_3 (R, in_1[0], in_1[1], in_1[2], in_1[3], in_1[4], in_1[5], in_1[6], in_1[7], in_1[8], in_1[9]);

  assign in_2[10] = in_2[11];
  assign out_6 = {5{1'b0}};
  assign out_18 = {5{1'b0}};
  assign out_22 = {{2{in_2[11]}}, in_2[9:0]};
  assign out_23 = in_1;

  // Other names for the same wires on the sheet: _10_r = in_1[10]; _11_r = in_1[11]; L1[4:0] = out_5; L2[4:0] = out_4;
  //   L3[4:0] = out_3; _10_l = in_2[11]; R1[4:0] = out_21; R2[4:0] = out_20; R3[4:0] = out_19
endmodule
