// Logisim project input controller.circ as structural Verilog: 4 circuits, main circuit local test
module local_test (
  input  in_1
);

  wire and_1_out, clock_1_out, counter_1_carry, input_controller_1_active_led, input_controller_1_data_ready,
       input_controller_1_error_led, input_controller_1_kbd_clear, input_controller_1_kbd_clock,
       input_controller_1_kbd_en, input_controller_1_user_action_led, keyboard_1_avail, nor_1_out;
  wire [4:0] input_controller_1_command_parsed_from_user_input;
  wire [6:0] keyboard_1_data;
  wire [10:0] input_controller_1_signed_number_parsed_from_user_input;

  Counter #(.width(2), .max('h3)) counter_1 (
    .carry(counter_1_carry), .clk(clock_1_out), .clr(nor_1_out));  // open: load, D, count, Q
  Clock clock_1 (.out(clock_1_out));
  Keyboard #(.buflen(5)) keyboard_1 (
    .clk(input_controller_1_kbd_clock), .re(input_controller_1_kbd_en), .clr(input_controller_1_kbd_clear),
    .avail(keyboard_1_avail), .data(keyboard_1_data));
  input_controller input_controller_1 (
    .Signed_number_parsed_from_user_input(input_controller_1_signed_number_parsed_from_user_input),
    .Command_parsed_from_user_input(input_controller_1_command_parsed_from_user_input),
    .KBD_clock(input_controller_1_kbd_clock), .KBD_clear(input_controller_1_kbd_clear),
    .KBD_available(keyboard_1_avail), .KBD_buffer(keyboard_1_data), .KBD_en(input_controller_1_kbd_en),
    .Enabled__clears_buffer_on_rising_edge(and_1_out), .Active_LED(input_controller_1_active_led),
    .User_action_LED(input_controller_1_user_action_led), .Error_LED(input_controller_1_error_led),
    .Data_ready(input_controller_1_data_ready));  // open: Request_number
  and and_1 (and_1_out, in_1, ~counter_1_carry);  // AND_Gate
  nor nor_1 (nor_1_out, input_controller_1_error_led, input_controller_1_data_ready);
  LED led_1 (.in(input_controller_1_active_led));
  LED led_2 (.in(input_controller_1_error_led));
  LED led_3 (.in(input_controller_1_user_action_led));
  // Probe on keyboard_1_data
  // Probe on input_controller_1_command_parsed_from_user_input
  // Probe on input_controller_1_signed_number_parsed_from_user_input

  // Notes on the sheet:
  //   in_1: pull=down
endmodule

module input_controller (
  input  KBD_available,
  input  [6:0] KBD_buffer,
  input  Enabled__clears_buffer_on_rising_edge,
  input  Request_number,
  output KBD_clock,
  output KBD_en,
  output KBD_clear,
  output [4:0] Command_parsed_from_user_input,
  output Data_ready,
  output Active_LED,
  output User_action_LED,
  output Error_LED,
  output [10:0] Signed_number_parsed_from_user_input
);

  wire and_1_out, and_2_out, clock_2_out, clock_3_out, d_ff_1_q, nor_1_out, not_1_out, not_2_out, or_1_out;
  wire [6:0] register_1_q;

  Clock clock_1 (.out(KBD_clock));
  Clock clock_2 (.out(clock_2_out));
  D_Flip_Flop d_ff_1 (
    .clk(clock_2_out), .D(Enabled__clears_buffer_on_rising_edge), .Q(d_ff_1_q), .reset(not_1_out));  // open: Qn, preset, en
  not not_1 (not_1_out, Enabled__clears_buffer_on_rising_edge);
  or or_1 (or_1_out, KBD_buffer[6], KBD_buffer[5], KBD_buffer[4], KBD_buffer[3], KBD_buffer[2], KBD_buffer[1], KBD_buffer[0]);
  and and_1 (and_1_out, Enabled__clears_buffer_on_rising_edge, ~d_ff_1_q);  // AND_Gate
  Register #(.width(7)) register_1 (
    .D(KBD_buffer), .en(Active_LED), .Q(register_1_q), .clk(and_2_out), .clr(and_1_out));
  and and_2 (and_2_out, or_1_out, clock_3_out);
  Clock clock_3 (.out(clock_3_out));
  and and_3 (Active_LED, Enabled__clears_buffer_on_rising_edge, not_2_out);
  not not_2 (not_2_out, Error_LED);
  nor nor_1 (nor_1_out, register_1_q[6], register_1_q[5], register_1_q[4], register_1_q[3], register_1_q[2], register_1_q[1], register_1_q[0]);
  command_decoder command_decoder_1 (
    .Char_input(register_1_q), .Command_output(Command_parsed_from_user_input), .err(Error_LED));
  nor nor_2 (Data_ready, Error_LED, nor_1_out);

  assign KBD_clear = 1'b0;
  assign KBD_en = KBD_available;

  // Notes on the sheet:
  //   KBD_buffer: pull=down
  //   KBD_available: pull=down
  //   Enabled__clears_buffer_on_rising_edge: pull=down
  //   Request_number: pull=down
endmodule

module command_decoder (
  input  [6:0] Char_input,
  output [4:0] Command_output,
  output err
);

  wire internal_comparator_1_is_equal;

  internal_comparator internal_comparator_1 (
    .input_1(Char_input), .input_2({7{1'b0}}), .forward_value_input({5{1'b0}}),
    .is_equal(internal_comparator_1_is_equal), .forwarded_value(Command_output));
  internal_comparator internal_comparator_2 (
    .input_1(Char_input), .input_2(7'b1100001), .forward_value_input(5'b00001),
    .is_equal(internal_comparator_1_is_equal), .forwarded_value(Command_output));
  internal_comparator internal_comparator_3 (
    .input_1(Char_input), .input_2(7'b1000001), .forward_value_input({5{1'b1}}),
    .is_equal(internal_comparator_1_is_equal), .forwarded_value(Command_output));
  Pull_Resistor pull_resistor_1 (.node(internal_comparator_1_is_equal));
  not not_1 (err, internal_comparator_1_is_equal);

  // Notes on the sheet:
  //   Char_input: pull=down
endmodule

module internal_comparator (
  input  [6:0] input_1,
  input  [6:0] input_2,
  input  [4:0] forward_value_input,
  output is_equal,
  output [4:0] forwarded_value
);

  wire nor_1_out;
  wire [6:0] xor_1_out;

  assign xor_1_out = input_1 ^ input_2;  // XOR_Gate xor_1, 7 bits wide
  nor nor_1 (nor_1_out, xor_1_out[0], xor_1_out[1], xor_1_out[2], xor_1_out[3], xor_1_out[4], xor_1_out[5], xor_1_out[6]);
  assign is_equal = nor_1_out ? nor_1_out : 1'bz;  // Controlled_Buffer controlled_buffer_1
  assign forwarded_value = nor_1_out ? forward_value_input : 5'bz;  // Controlled_Buffer controlled_buffer_2

  // Notes on the sheet:
  //   input_1: pull=down
  //   input_2: pull=down
  //   forward_value_input: pull=down
endmodule
