// Logisim project people_controller.circ as structural Verilog
module local_test (
  input  [4:0] in_1,
  input  [10:0] in_2,
  input  [7:0] in_3,
  input  in_4
);

  wire clock_1_out, spi_module_master_1_clk, spi_module_master_1_communication_end,
       spi_module_master_1_input_transanction_end, spi_module_master_1_mosi,
       spi_module_master_1_output_transanction_end;
  wire [14:0] fasa_1_out_4, fasa_1_out_5, fasa_1_out_6, fasa_1_out_7, fasa_1_out_8, fasa_1_out_9,
       fasa_1_out_10, fasa_1_out_11, fasa_1_out_12, fasa_1_out_13, fasa_1_out_14, fasa_1_out_15,
       fasa_1_out_16, fasa_1_out_17, fasa_1_out_18, fasa_1_out_19, fasa_1_out_20, fasa_1_out_21,
       fasa_1_out_22, fasa_1_out_23, fasa_1_out_24, fasa_1_out_25, fasa_1_out_26, fasa_1_out_27,
       fasa_1_out_28, fasa_1_out_29, fasa_1_out_30, fasa_1_out_31, fasa_1_out_32, fasa_1_out_33;

  Clock clock_1 (.out(clock_1_out));
  LED led_1 (.in(spi_module_master_1_input_transanction_end));
  SPI_module__master spi_module_master_1 (
    .In_clock(clock_1_out), .CLK(spi_module_master_1_clk), .MOSI(spi_module_master_1_mosi),
    .Output_transanction_end(spi_module_master_1_output_transanction_end),
    .Input_transanction_end(spi_module_master_1_input_transanction_end), .Control_command(in_3),
    .Send_command(in_1), .Send_energy(in_2), .Communication_end(spi_module_master_1_communication_end));  // open: MISO, Recv_data
  LED led_2 (.in(spi_module_master_1_output_transanction_end));
  LED led_3 (.in(spi_module_master_1_communication_end));
  DotMatrix #(.matrixcols(15), .matrixrows(15)) dotmatrix_1 (
    .col0(fasa_1_out_33), .col1(fasa_1_out_31), .col2(fasa_1_out_29), .col3(fasa_1_out_27),
    .col4(fasa_1_out_25), .col5(fasa_1_out_23), .col6(fasa_1_out_21), .col7(fasa_1_out_19),
    .col8(fasa_1_out_17), .col9(fasa_1_out_15), .col10(fasa_1_out_13), .col11(fasa_1_out_11),
    .col12(fasa_1_out_9), .col13(fasa_1_out_7), .col14(fasa_1_out_5));
  DotMatrix #(.matrixcols(15), .matrixrows(15)) dotmatrix_2 (
    .col0(fasa_1_out_32), .col1(fasa_1_out_30), .col2(fasa_1_out_28), .col3(fasa_1_out_26),
    .col4(fasa_1_out_24), .col5(fasa_1_out_22), .col6(fasa_1_out_20), .col7(fasa_1_out_18),
    .col8(fasa_1_out_16), .col9(fasa_1_out_14), .col10(fasa_1_out_12), .col11(fasa_1_out_10),
    .col12(fasa_1_out_8), .col13(fasa_1_out_6), .col14(fasa_1_out_4));
  Fasa fasa_1 (
    .out_4(fasa_1_out_4), .out_6(fasa_1_out_6), .out_8(fasa_1_out_8), .out_10(fasa_1_out_10),
    .out_12(fasa_1_out_12), .out_14(fasa_1_out_14), .out_16(fasa_1_out_16), .out_18(fasa_1_out_18),
    .out_20(fasa_1_out_20), .out_22(fasa_1_out_22), .out_24(fasa_1_out_24), .out_26(fasa_1_out_26),
    .CLK(spi_module_master_1_clk), .out_28(fasa_1_out_28), .out_30(fasa_1_out_30),
    .MOSI(spi_module_master_1_mosi), .out_32(fasa_1_out_32), .out_5(fasa_1_out_5), .out_7(fasa_1_out_7),
    .out_9(fasa_1_out_9), .out_11(fasa_1_out_11), .out_13(fasa_1_out_13), .out_15(fasa_1_out_15),
    .out_17(fasa_1_out_17), .out_19(fasa_1_out_19), .out_21(fasa_1_out_21), .out_23(fasa_1_out_23),
    .out_25(fasa_1_out_25), .out_27(fasa_1_out_27), .out_29(fasa_1_out_29), .out_31(fasa_1_out_31),
    .out_33(fasa_1_out_33), .CS(in_4));  // open: People
endmodule

module Fasa (
  input  CS,
  input  CLK,
  input  MOSI,
  output [14:0] out_4,
  output [14:0] out_5,
  output [14:0] out_6,
  output [14:0] out_7,
  output [14:0] out_8,
  output [14:0] out_9,
  output [14:0] out_10,
  output [14:0] out_11,
  output [14:0] out_12,
  output [14:0] out_13,
  output [14:0] out_14,
  output [14:0] out_15,
  output [14:0] out_16,
  output [14:0] out_17,
  output [14:0] out_18,
  output [14:0] out_19,
  output [14:0] out_20,
  output [14:0] out_21,
  output [14:0] out_22,
  output [14:0] out_23,
  output [14:0] out_24,
  output [14:0] out_25,
  output [14:0] out_26,
  output [14:0] out_27,
  output [14:0] out_28,
  output [14:0] out_29,
  output [14:0] out_30,
  output [14:0] out_31,
  output [14:0] out_32,
  output [14:0] out_33,
  output [1:0] People
);

  wire comparator_1_eq, not_1_out;
  wire [3:0] input_shifter_1_buffer_ptr;
  wire [15:0] input_shifter_1_data_out, register_1_q;

  not not_1 (not_1_out, CS);
  input_shifter input_shifter_1 (
    .MOSI(MOSI), .CLK(CLK), .Reset(not_1_out), .Data_out(input_shifter_1_data_out),
    .buffer_ptr(input_shifter_1_buffer_ptr));
  Comparator #(.width(4)) comparator_1 (
    .a(input_shifter_1_buffer_ptr), .b(4'b0101), .eq(comparator_1_eq));  // open: gt, lt
  Register #(.width(16)) register_1 (
    .D(input_shifter_1_data_out), .en(1'b1), .Q({register_1_q[15:4], People, register_1_q[1:0]}),
    .clk(comparator_1_eq), .clr(register_1_q[4]));
  DotMatrix #(.matrixcols(15), .matrixrows(15)) dotmatrix_1 (
    .col0(out_32), .col1(out_30), .col2(out_28), .col3(out_26), .col4(out_24), .col5(out_22), .col6(out_20),
    .col7(out_18), .col8(out_16), .col9(out_14), .col10(out_12), .col11(out_10), .col12(out_8),
    .col13(out_6), .col14(out_4));
  orange orange_1 (
    .in_1(People), .in_2(register_1_q[1:0]), .out_14(out_32), .out_9(out_30), .out_3(out_28),
    .out_15(out_26), .out_10(out_24), .out_4(out_22), .out_13(out_20), .out_8(out_18), .out_5(out_16),
    .out_16(out_14), .out_11(out_12), .out_6(out_10), .out_17(out_8), .out_12(out_6), .out_7(out_4));
  DotMatrix #(.matrixcols(15), .matrixrows(15)) dotmatrix_2 (
    .col0(out_33), .col1(out_31), .col2(out_29), .col3(out_27), .col4(out_25), .col5(out_23), .col6(out_21),
    .col7(out_19), .col8(out_17), .col9(out_15), .col10(out_13), .col11(out_11), .col12(out_9),
    .col13(out_7), .col14(out_5));
  blue blue_1 (
    .in_2(register_1_q[1:0]), .out_14(out_33), .out_9(out_31), .out_3(out_29), .out_15(out_27),
    .out_10(out_25), .out_4(out_23), .out_13(out_21), .out_8(out_19), .out_5(out_17), .out_16(out_15),
    .out_11(out_13), .out_6(out_11), .out_17(out_9), .out_12(out_7), .out_7(out_5), .in_1(People));
endmodule

module blue (
  input  [1:0] in_1,
  input  [1:0] in_2,
  output [14:0] out_3,
  output [14:0] out_4,
  output [14:0] out_5,
  output [14:0] out_6,
  output [14:0] out_7,
  output [14:0] out_8,
  output [14:0] out_9,
  output [14:0] out_10,
  output [14:0] out_11,
  output [14:0] out_12,
  output [14:0] out_13,
  output [14:0] out_14,
  output [14:0] out_15,
  output [14:0] out_16,
  output [14:0] out_17
);

  wire and_1_out, controlled_buffer_2_out, decoder_1_out0, decoder_1_out1, decoder_1_out2, decoder_1_out3,
       not_1_out;
  wire [1:0] pull_resistor_1_node;

  Decoder #(.select(2), .enable("false")) decoder_1 (
    .out0(decoder_1_out0), .out1(decoder_1_out1), .out2(decoder_1_out2), .out3(decoder_1_out3),
    .sel(pull_resistor_1_node));
  Pull_Resistor pull_resistor_1 (.node(pull_resistor_1_node));
  assign pull_resistor_1_node = in_1[0] ? in_2 : 2'bz;  // Controlled_Buffer controlled_buffer_1
  DotMatrix #(.matrixcols(15), .matrixrows(15)) dotmatrix_1 (
    .col0(out_14), .col1(out_9), .col2(out_3), .col3(out_15), .col4(out_10), .col5(out_4), .col6(out_13),
    .col7(out_8), .col8(out_5), .col9(out_16), .col10(out_11), .col11(out_6), .col12(out_17), .col13(out_12),
    .col14(out_7));
  assign controlled_buffer_2_out = not_1_out ? decoder_1_out0 : 1'bz;  // Controlled_Buffer controlled_buffer_2
  not not_1 (not_1_out, and_1_out);
  and and_1 (and_1_out, in_1[0], in_1[1]);
  Pull_Resistor pull_resistor_2 (.node(controlled_buffer_2_out));
  Transistor #(.\type ("n"), .width(15)) transistor_1 (.in({15{1'b0}}), .out(out_3), .gate(controlled_buffer_2_out));
  Transistor #(.\type ("n"), .width(15)) transistor_2 (.in({15{1'b0}}), .out(out_15), .gate(controlled_buffer_2_out));
  Transistor #(.\type ("n"), .width(15)) transistor_3 (.in({15{1'b0}}), .out(out_9), .gate(controlled_buffer_2_out));
  Transistor #(.\type ("n"), .width(15)) transistor_4 (.in({15{1'b0}}), .out(out_14), .gate(controlled_buffer_2_out));
  Transistor #(.\type ("n"), .width(15)) transistor_5 (.in({15{1'b0}}), .out(out_8), .gate(controlled_buffer_2_out));
  Transistor #(.\type ("n"), .width(15)) transistor_6 (.in({15{1'b0}}), .out(out_10), .gate(controlled_buffer_2_out));
  Transistor #(.\type ("n"), .width(15)) transistor_7 (.in({15{1'b0}}), .out(out_4), .gate(controlled_buffer_2_out));
  Transistor #(.\type ("n"), .width(15)) transistor_8 (.in({15{1'b0}}), .out(out_13), .gate(controlled_buffer_2_out));
  Transistor #(.\type ("n"), .width(15)) transistor_9 (.in({15{1'b0}}), .out(out_11), .gate(controlled_buffer_2_out));
  Transistor #(.\type ("n"), .width(15)) transistor_10 (.in({15{1'b0}}), .out(out_16), .gate(controlled_buffer_2_out));
  Transistor #(.\type ("n"), .width(15)) transistor_11 (.in({15{1'b0}}), .out(out_6), .gate(controlled_buffer_2_out));
  Transistor #(.\type ("n"), .width(15)) transistor_12 (.in({15{1'b0}}), .out(out_5), .gate(controlled_buffer_2_out));
  Transistor #(.\type ("n"), .width(15)) transistor_13 (.in({15{1'b0}}), .out(out_17), .gate(controlled_buffer_2_out));
  Transistor #(.\type ("n"), .width(15)) transistor_14 (.in({15{1'b0}}), .out(out_7), .gate(controlled_buffer_2_out));
  Transistor #(.\type ("n"), .width(15)) transistor_15 (.in({15{1'b0}}), .out(out_12), .gate(controlled_buffer_2_out));
  Transistor #(.\type ("n"), .width(15)) transistor_16 (.in(15'h180c), .out(out_9), .gate(decoder_1_out1));
  Transistor #(.\type ("n"), .width(15)) transistor_17 (.in(15'h2412), .out(out_3), .gate(decoder_1_out1));
  Transistor #(.\type ("n"), .width(15)) transistor_18 (.in(15'h23d6), .out(out_15), .gate(decoder_1_out1));
  Transistor #(.\type ("n"), .width(15)) transistor_19 (.in({15{1'b0}}), .out(out_14), .gate(decoder_1_out1));
  Transistor #(.\type ("n"), .width(15)) transistor_20 (.in(15'h2aa2), .out(out_13), .gate(decoder_1_out1));
  Transistor #(.\type ("n"), .width(15)) transistor_21 (.in(15'h383a), .out(out_10), .gate(decoder_1_out1));
  Transistor #(.\type ("n"), .width(15)) transistor_22 (.in(15'h2aa2), .out(out_8), .gate(decoder_1_out1));
  Transistor #(.\type ("n"), .width(15)) transistor_23 (.in(15'h2a82), .out(out_4), .gate(decoder_1_out1));
  Transistor #(.\type ("n"), .width(15)) transistor_24 (.in(15'h2aa2), .out(out_16), .gate(decoder_1_out1));
  Transistor #(.\type ("n"), .width(15)) transistor_25 (.in(15'h2a22), .out(out_5), .gate(decoder_1_out1));
  Transistor #(.\type ("n"), .width(15)) transistor_26 (.in(15'h2c02), .out(out_6), .gate(decoder_1_out1));
  Transistor #(.\type ("n"), .width(15)) transistor_27 (.in(15'h2882), .out(out_11), .gate(decoder_1_out1));
  Transistor #(.\type ("n"), .width(15)) transistor_28 (.in(15'h1838), .out(out_12), .gate(decoder_1_out1));
  Transistor #(.\type ("n"), .width(15)) transistor_29 (.in(15'h2bc4), .out(out_17), .gate(decoder_1_out1));
  Transistor #(.\type ("n"), .width(15)) transistor_30 (.in({15{1'b0}}), .out(out_7), .gate(decoder_1_out1));
  Transistor #(.\type ("n"), .width(15)) transistor_31 (.in(15'h80), .out(out_14), .gate(decoder_1_out2));
  Transistor #(.\type ("n"), .width(15)) transistor_32 (.in(15'h220), .out(out_3), .gate(decoder_1_out2));
  Transistor #(.\type ("n"), .width(15)) transistor_33 (.in({15{1'b0}}), .out(out_15), .gate(decoder_1_out2));
  Transistor #(.\type ("n"), .width(15)) transistor_34 (.in(15'h140), .out(out_9), .gate(decoder_1_out2));
  Transistor #(.\type ("n"), .width(15)) transistor_35 (.in(15'h21b2), .out(out_13), .gate(decoder_1_out2));
  Transistor #(.\type ("n"), .width(15)) transistor_36 (.in(15'h1084), .out(out_4), .gate(decoder_1_out2));
  Transistor #(.\type ("n"), .width(15)) transistor_37 (.in({15{1'b0}}), .out(out_10), .gate(decoder_1_out2));
  Transistor #(.\type ("n"), .width(15)) transistor_38 (.in(15'h43e1), .out(out_8), .gate(decoder_1_out2));
  Transistor #(.\type ("n"), .width(15)) transistor_39 (.in({15{1'b0}}), .out(out_6), .gate(decoder_1_out2));
  Transistor #(.\type ("n"), .width(15)) transistor_40 (.in(15'h1084), .out(out_16), .gate(decoder_1_out2));
  Transistor #(.\type ("n"), .width(15)) transistor_41 (.in(15'h26c2), .out(out_5), .gate(decoder_1_out2));
  Transistor #(.\type ("n"), .width(15)) transistor_42 (.in({15{1'b0}}), .out(out_11), .gate(decoder_1_out2));
  Transistor #(.\type ("n"), .width(15)) transistor_43 (.in(15'h140), .out(out_12), .gate(decoder_1_out2));
  Transistor #(.\type ("n"), .width(15)) transistor_44 (.in(15'h80), .out(out_7), .gate(decoder_1_out2));
  Transistor #(.\type ("n"), .width(15)) transistor_45 (.in(15'h220), .out(out_17), .gate(decoder_1_out2));
  Transistor #(.\type ("n"), .width(15)) transistor_46 (.in(15'h100), .out(out_3), .gate(decoder_1_out3));
  Transistor #(.\type ("n"), .width(15)) transistor_47 (.in({15{1'b0}}), .out(out_14), .gate(decoder_1_out3));
  Transistor #(.\type ("n"), .width(15)) transistor_48 (.in({15{1'b0}}), .out(out_9), .gate(decoder_1_out3));
  Transistor #(.\type ("n"), .width(15)) transistor_49 (.in(15'h300), .out(out_15), .gate(decoder_1_out3));
  Transistor #(.\type ("n"), .width(15)) transistor_50 (.in(15'h1ffe), .out(out_13), .gate(decoder_1_out3));
  Transistor #(.\type ("n"), .width(15)) transistor_51 (.in(15'h700), .out(out_10), .gate(decoder_1_out3));
  Transistor #(.\type ("n"), .width(15)) transistor_52 (.in(15'he00), .out(out_4), .gate(decoder_1_out3));
  Transistor #(.\type ("n"), .width(15)) transistor_53 (.in(15'h1ffe), .out(out_5), .gate(decoder_1_out3));
  Transistor #(.\type ("n"), .width(15)) transistor_54 (.in(15'h3ffe), .out(out_8), .gate(decoder_1_out3));
  Transistor #(.\type ("n"), .width(15)) transistor_55 (.in(15'he00), .out(out_16), .gate(decoder_1_out3));
  Transistor #(.\type ("n"), .width(15)) transistor_56 (.in(15'h700), .out(out_11), .gate(decoder_1_out3));
  Transistor #(.\type ("n"), .width(15)) transistor_57 (.in(15'h300), .out(out_6), .gate(decoder_1_out3));
  Transistor #(.\type ("n"), .width(15)) transistor_58 (.in(15'h100), .out(out_17), .gate(decoder_1_out3));
  Transistor #(.\type ("n"), .width(15)) transistor_59 (.in({15{1'b0}}), .out(out_12), .gate(decoder_1_out3));
  Transistor #(.\type ("n"), .width(15)) transistor_60 (.in({15{1'b0}}), .out(out_7), .gate(decoder_1_out3));
  Transistor #(.\type ("n"), .width(15)) transistor_61 (.in(15'h630), .out(out_9), .gate(and_1_out));
  Transistor #(.\type ("n"), .width(15)) transistor_62 (.in(15'h1c0), .out(out_14), .gate(and_1_out));
  Transistor #(.\type ("n"), .width(15)) transistor_63 (.in(15'h2002), .out(out_10), .gate(and_1_out));
  Transistor #(.\type ("n"), .width(15)) transistor_64 (.in(15'h1004), .out(out_15), .gate(and_1_out));
  Transistor #(.\type ("n"), .width(15)) transistor_65 (.in(15'h2002), .out(out_4), .gate(and_1_out));
  Transistor #(.\type ("n"), .width(15)) transistor_66 (.in(15'h808), .out(out_3), .gate(and_1_out));
  Transistor #(.\type ("n"), .width(15)) transistor_67 (.in(15'h4001), .out(out_13), .gate(and_1_out));
  Transistor #(.\type ("n"), .width(15)) transistor_68 (.in(15'h5f81), .out(out_8), .gate(and_1_out));
  Transistor #(.\type ("n"), .width(15)) transistor_69 (.in(15'h4081), .out(out_5), .gate(and_1_out));
  Transistor #(.\type ("n"), .width(15)) transistor_70 (.in(15'h2082), .out(out_16), .gate(and_1_out));
  Transistor #(.\type ("n"), .width(15)) transistor_71 (.in(15'h808), .out(out_17), .gate(and_1_out));
  Transistor #(.\type ("n"), .width(15)) transistor_72 (.in(15'h1004), .out(out_6), .gate(and_1_out));
  Transistor #(.\type ("n"), .width(15)) transistor_73 (.in(15'h2082), .out(out_11), .gate(and_1_out));
  Transistor #(.\type ("n"), .width(15)) transistor_74 (.in(15'h630), .out(out_12), .gate(and_1_out));
  Transistor #(.\type ("n"), .width(15)) transistor_75 (.in(15'h1c0), .out(out_7), .gate(and_1_out));
endmodule

module orange (
  input  [1:0] in_1,
  input  [1:0] in_2,
  output [14:0] out_3,
  output [14:0] out_4,
  output [14:0] out_5,
  output [14:0] out_6,
  output [14:0] out_7,
  output [14:0] out_8,
  output [14:0] out_9,
  output [14:0] out_10,
  output [14:0] out_11,
  output [14:0] out_12,
  output [14:0] out_13,
  output [14:0] out_14,
  output [14:0] out_15,
  output [14:0] out_16,
  output [14:0] out_17
);

  wire and_1_out, controlled_buffer_2_out, decoder_1_out0, decoder_1_out1, decoder_1_out2, decoder_1_out3,
       not_1_out;
  wire [1:0] pull_resistor_1_node;

  DotMatrix #(.matrixcols(15), .matrixrows(15)) dotmatrix_1 (
    .col0(out_14), .col1(out_9), .col2(out_3), .col3(out_15), .col4(out_10), .col5(out_4), .col6(out_13),
    .col7(out_8), .col8(out_5), .col9(out_16), .col10(out_11), .col11(out_6), .col12(out_17), .col13(out_12),
    .col14(out_7));
  Decoder #(.select(2), .enable("false")) decoder_1 (
    .out0(decoder_1_out0), .out1(decoder_1_out1), .out2(decoder_1_out2), .out3(decoder_1_out3),
    .sel(pull_resistor_1_node));
  Pull_Resistor pull_resistor_1 (.node(pull_resistor_1_node));
  assign pull_resistor_1_node = in_1[1] ? in_2 : 2'bz;  // Controlled_Buffer controlled_buffer_1
  and and_1 (and_1_out, in_1[1], in_1[0]);
  assign controlled_buffer_2_out = not_1_out ? decoder_1_out0 : 1'bz;  // Controlled_Buffer controlled_buffer_2
  not not_1 (not_1_out, and_1_out);
  Pull_Resistor pull_resistor_2 (.node(controlled_buffer_2_out));
  Transistor #(.\type ("n"), .width(15)) transistor_1 (.in({15{1'b0}}), .out(out_9), .gate(controlled_buffer_2_out));
  Transistor #(.\type ("n"), .width(15)) transistor_2 (.in({15{1'b0}}), .out(out_14), .gate(controlled_buffer_2_out));
  Transistor #(.\type ("n"), .width(15)) transistor_3 (.in({15{1'b0}}), .out(out_10), .gate(controlled_buffer_2_out));
  Transistor #(.\type ("n"), .width(15)) transistor_4 (.in({15{1'b0}}), .out(out_15), .gate(controlled_buffer_2_out));
  Transistor #(.\type ("n"), .width(15)) transistor_5 (.in({15{1'b0}}), .out(out_3), .gate(controlled_buffer_2_out));
  Transistor #(.\type ("n"), .width(15)) transistor_6 (.in({15{1'b0}}), .out(out_4), .gate(controlled_buffer_2_out));
  Transistor #(.\type ("n"), .width(15)) transistor_7 (.in({15{1'b0}}), .out(out_16), .gate(controlled_buffer_2_out));
  Transistor #(.\type ("n"), .width(15)) transistor_8 (.in({15{1'b0}}), .out(out_13), .gate(controlled_buffer_2_out));
  Transistor #(.\type ("n"), .width(15)) transistor_9 (.in({15{1'b0}}), .out(out_5), .gate(controlled_buffer_2_out));
  Transistor #(.\type ("n"), .width(15)) transistor_10 (.in({15{1'b0}}), .out(out_8), .gate(controlled_buffer_2_out));
  Transistor #(.\type ("n"), .width(15)) transistor_11 (.in({15{1'b0}}), .out(out_6), .gate(controlled_buffer_2_out));
  Transistor #(.\type ("n"), .width(15)) transistor_12 (.in({15{1'b0}}), .out(out_12), .gate(controlled_buffer_2_out));
  Transistor #(.\type ("n"), .width(15)) transistor_13 (.in({15{1'b0}}), .out(out_11), .gate(controlled_buffer_2_out));
  Transistor #(.\type ("n"), .width(15)) transistor_14 (.in({15{1'b0}}), .out(out_17), .gate(controlled_buffer_2_out));
  Transistor #(.\type ("n"), .width(15)) transistor_15 (.in({15{1'b0}}), .out(out_7), .gate(controlled_buffer_2_out));
  Transistor #(.\type ("n"), .width(15)) transistor_16 (.in({15{1'b0}}), .out(out_14), .gate(decoder_1_out1));
  Transistor #(.\type ("n"), .width(15)) transistor_17 (.in(15'h180c), .out(out_9), .gate(decoder_1_out1));
  Transistor #(.\type ("n"), .width(15)) transistor_18 (.in(15'h2412), .out(out_3), .gate(decoder_1_out1));
  Transistor #(.\type ("n"), .width(15)) transistor_19 (.in(15'h2a82), .out(out_4), .gate(decoder_1_out1));
  Transistor #(.\type ("n"), .width(15)) transistor_20 (.in(15'h23d6), .out(out_15), .gate(decoder_1_out1));
  Transistor #(.\type ("n"), .width(15)) transistor_21 (.in(15'h2aa2), .out(out_13), .gate(decoder_1_out1));
  Transistor #(.\type ("n"), .width(15)) transistor_22 (.in(15'h383a), .out(out_10), .gate(decoder_1_out1));
  Transistor #(.\type ("n"), .width(15)) transistor_23 (.in(15'h2a22), .out(out_5), .gate(decoder_1_out1));
  Transistor #(.\type ("n"), .width(15)) transistor_24 (.in(15'h2aa2), .out(out_8), .gate(decoder_1_out1));
  Transistor #(.\type ("n"), .width(15)) transistor_25 (.in(15'h2882), .out(out_11), .gate(decoder_1_out1));
  Transistor #(.\type ("n"), .width(15)) transistor_26 (.in(15'h2aa2), .out(out_16), .gate(decoder_1_out1));
  Transistor #(.\type ("n"), .width(15)) transistor_27 (.in(15'h2c02), .out(out_6), .gate(decoder_1_out1));
  Transistor #(.\type ("n"), .width(15)) transistor_28 (.in(15'h2bc4), .out(out_17), .gate(decoder_1_out1));
  Transistor #(.\type ("n"), .width(15)) transistor_29 (.in(15'h1838), .out(out_12), .gate(decoder_1_out1));
  Transistor #(.\type ("n"), .width(15)) transistor_30 (.in({15{1'b0}}), .out(out_7), .gate(decoder_1_out1));
  Transistor #(.\type ("n"), .width(15)) transistor_31 (.in(15'h80), .out(out_14), .gate(decoder_1_out2));
  Transistor #(.\type ("n"), .width(15)) transistor_32 (.in(15'h140), .out(out_9), .gate(decoder_1_out2));
  Transistor #(.\type ("n"), .width(15)) transistor_33 (.in({15{1'b0}}), .out(out_10), .gate(decoder_1_out2));
  Transistor #(.\type ("n"), .width(15)) transistor_34 (.in(15'h220), .out(out_3), .gate(decoder_1_out2));
  Transistor #(.\type ("n"), .width(15)) transistor_35 (.in(15'h1084), .out(out_4), .gate(decoder_1_out2));
  Transistor #(.\type ("n"), .width(15)) transistor_36 (.in({15{1'b0}}), .out(out_15), .gate(decoder_1_out2));
  Transistor #(.\type ("n"), .width(15)) transistor_37 (.in(15'h21b2), .out(out_13), .gate(decoder_1_out2));
  Transistor #(.\type ("n"), .width(15)) transistor_38 (.in(15'h43e1), .out(out_8), .gate(decoder_1_out2));
  Transistor #(.\type ("n"), .width(15)) transistor_39 (.in(15'h26c2), .out(out_5), .gate(decoder_1_out2));
  Transistor #(.\type ("n"), .width(15)) transistor_40 (.in(15'h1084), .out(out_16), .gate(decoder_1_out2));
  Transistor #(.\type ("n"), .width(15)) transistor_41 (.in(15'h140), .out(out_12), .gate(decoder_1_out2));
  Transistor #(.\type ("n"), .width(15)) transistor_42 (.in({15{1'b0}}), .out(out_6), .gate(decoder_1_out2));
  Transistor #(.\type ("n"), .width(15)) transistor_43 (.in(15'h220), .out(out_17), .gate(decoder_1_out2));
  Transistor #(.\type ("n"), .width(15)) transistor_44 (.in({15{1'b0}}), .out(out_11), .gate(decoder_1_out2));
  Transistor #(.\type ("n"), .width(15)) transistor_45 (.in(15'h80), .out(out_7), .gate(decoder_1_out2));
  Transistor #(.\type ("n"), .width(15)) transistor_46 (.in({15{1'b0}}), .out(out_14), .gate(decoder_1_out3));
  Transistor #(.\type ("n"), .width(15)) transistor_47 (.in(15'h700), .out(out_10), .gate(decoder_1_out3));
  Transistor #(.\type ("n"), .width(15)) transistor_48 (.in(15'h100), .out(out_3), .gate(decoder_1_out3));
  Transistor #(.\type ("n"), .width(15)) transistor_49 (.in(15'h300), .out(out_15), .gate(decoder_1_out3));
  Transistor #(.\type ("n"), .width(15)) transistor_50 (.in({15{1'b0}}), .out(out_9), .gate(decoder_1_out3));
  Transistor #(.\type ("n"), .width(15)) transistor_51 (.in(15'h1ffe), .out(out_5), .gate(decoder_1_out3));
  Transistor #(.\type ("n"), .width(15)) transistor_52 (.in(15'he00), .out(out_4), .gate(decoder_1_out3));
  Transistor #(.\type ("n"), .width(15)) transistor_53 (.in(15'h1ffe), .out(out_13), .gate(decoder_1_out3));
  Transistor #(.\type ("n"), .width(15)) transistor_54 (.in(15'h3ffe), .out(out_8), .gate(decoder_1_out3));
  Transistor #(.\type ("n"), .width(15)) transistor_55 (.in(15'h700), .out(out_11), .gate(decoder_1_out3));
  Transistor #(.\type ("n"), .width(15)) transistor_56 (.in(15'h300), .out(out_6), .gate(decoder_1_out3));
  Transistor #(.\type ("n"), .width(15)) transistor_57 (.in(15'he00), .out(out_16), .gate(decoder_1_out3));
  Transistor #(.\type ("n"), .width(15)) transistor_58 (.in(15'h100), .out(out_17), .gate(decoder_1_out3));
  Transistor #(.\type ("n"), .width(15)) transistor_59 (.in({15{1'b0}}), .out(out_7), .gate(decoder_1_out3));
  Transistor #(.\type ("n"), .width(15)) transistor_60 (.in({15{1'b0}}), .out(out_12), .gate(decoder_1_out3));
  Transistor #(.\type ("n"), .width(15)) transistor_61 (.in(15'h1004), .out(out_15), .gate(and_1_out));
  Transistor #(.\type ("n"), .width(15)) transistor_62 (.in(15'h630), .out(out_9), .gate(and_1_out));
  Transistor #(.\type ("n"), .width(15)) transistor_63 (.in(15'h1c0), .out(out_14), .gate(and_1_out));
  Transistor #(.\type ("n"), .width(15)) transistor_64 (.in(15'h808), .out(out_3), .gate(and_1_out));
  Transistor #(.\type ("n"), .width(15)) transistor_65 (.in(15'h5f81), .out(out_8), .gate(and_1_out));
  Transistor #(.\type ("n"), .width(15)) transistor_66 (.in(15'h2002), .out(out_10), .gate(and_1_out));
  Transistor #(.\type ("n"), .width(15)) transistor_67 (.in(15'h4001), .out(out_13), .gate(and_1_out));
  Transistor #(.\type ("n"), .width(15)) transistor_68 (.in(15'h2002), .out(out_4), .gate(and_1_out));
  Transistor #(.\type ("n"), .width(15)) transistor_69 (.in(15'h2082), .out(out_16), .gate(and_1_out));
  Transistor #(.\type ("n"), .width(15)) transistor_70 (.in(15'h2082), .out(out_11), .gate(and_1_out));
  Transistor #(.\type ("n"), .width(15)) transistor_71 (.in(15'h4081), .out(out_5), .gate(and_1_out));
  Transistor #(.\type ("n"), .width(15)) transistor_72 (.in(15'h1004), .out(out_6), .gate(and_1_out));
  Transistor #(.\type ("n"), .width(15)) transistor_73 (.in(15'h1c0), .out(out_7), .gate(and_1_out));
  Transistor #(.\type ("n"), .width(15)) transistor_74 (.in(15'h808), .out(out_17), .gate(and_1_out));
  Transistor #(.\type ("n"), .width(15)) transistor_75 (.in(15'h630), .out(out_12), .gate(and_1_out));
endmodule

module main (
  input  in_1,
  input  in_2
);

  wire blue, ornge;
  wire [1:0] T;
  wire [14:0] fasa_1_p1, fasa_1_p2, fasa_1_p3, fasa_1_p4, fasa_1_p6, fasa_1_p8, fasa_1_p10, fasa_1_p12,
       fasa_1_p14, fasa_1_p16, fasa_1_p18, fasa_1_p20, fasa_1_p22, fasa_1_p24, fasa_1_p26, fasa_1_p28,
       fasa_1_p30, fasa_1_p32, undriven, undriven_2, undriven_3, undriven_4, undriven_5, undriven_6,
       undriven_7, undriven_8, undriven_9, undriven_10, undriven_11, undriven_12;

  DotMatrix #(.matrixcols(15), .matrixrows(15)) dotmatrix_1 (
    .col0(undriven), .col1(undriven_2), .col2(undriven_3), .col3(undriven_4), .col4(undriven_5),
    .col5(undriven_6), .col6(undriven_7), .col7(undriven_8), .col8(undriven_9), .col9(undriven_10),
    .col10(undriven_11), .col11(undriven_12), .col12(fasa_1_p1), .col13(fasa_1_p2), .col14(fasa_1_p3));
  DotMatrix #(.matrixcols(15), .matrixrows(15)) dotmatrix_2 (
    .col0(fasa_1_p4), .col1(fasa_1_p6), .col2(fasa_1_p8), .col3(fasa_1_p10), .col4(fasa_1_p12),
    .col5(fasa_1_p14), .col6(fasa_1_p16), .col7(fasa_1_p18), .col8(fasa_1_p20), .col9(fasa_1_p22),
    .col10(fasa_1_p24), .col11(fasa_1_p26), .col12(fasa_1_p28), .col13(fasa_1_p30), .col14(fasa_1_p32));
  // Fasa fasa_1: pin names not known; wires that end beside it: fasa_1_p1, fasa_1_p2, fasa_1_p3, fasa_1_p4, fasa_1_p4, fasa_1_p6, fasa_1_p6, fasa_1_p8, fasa_1_p8, fasa_1_p10, fasa_1_p10, fasa_1_p12, fasa_1_p12, fasa_1_p14, fasa_1_p14, fasa_1_p16, fasa_1_p16, fasa_1_p18, fasa_1_p18, fasa_1_p20, fasa_1_p20, fasa_1_p22, fasa_1_p22, fasa_1_p24, fasa_1_p24, fasa_1_p26, fasa_1_p26, fasa_1_p28, fasa_1_p28, fasa_1_p30, fasa_1_p30, fasa_1_p32, T
  Decoder #(.select(2), .enable("false")) decoder_1 (.out1(blue), .out2(ornge), .sel(T));  // open: out0, out3
  // Width width_1: pin names not known
  // height height_1: pin names not known
endmodule

module generator (
  input  in_1,
  input  in_2,
  input  [1:0] Who,
  output err,
  output [15:0] out_5,
  output err_2,
  output out_7
);

  wire _1_b, _1_o, _2_b, _2_o, _3_b, _3_o, _4_b, _4_o, _5_b, _5_o, and_2_out, and_6_out, and_7_out,
       and_10_out, and_11_out, and_12_out, and_13_out, and_14_out, and_16_out, and_17_out, and_18_out,
       and_19_out, and_20_out, and_21_out, and_22_out, and_23_out, and_25_out, and_26_out, and_27_out,
       and_28_out, and_29_out, and_30_out, button_1_out, comparator_1_eq, comparator_4_eq, comparator_6_eq,
       comparator_8_eq, controlled_buffer_4_out, controlled_buffer_5_out, jk, kj, not_1_out, not_2_out,
       not_3_out, not_4_out, or_2_out, or_3_out, or_4_out, or_5_out, or_6_out, or_7_out, or_8_out, or_9_out,
       or_10_out, or_11_out, or_12_out, or_13_out, rst, rst_1, rst_2, rst_3, rst_4, rst_5, rst_6, rst_7,
       rst_8, rst_9, rst_10, Soh_prime, undriven_3;
  wire [1:0] controlled_buffer_2_out, haight_1_out_2, pull_resistor_3_node, weight_1_out_2, xx, yy;
  wire [2:0] h_1b, h_1o, inc_3_out_2, inc_4_out_2, w_1b, w_1o;
  wire [3:0] input_shifter_1_buffer_ptr;
  wire [4:0] comparator_2_eq, numder_2_1_out_5, numder_2_1_out_6, numder_2_1_out_7, numder_2_1_out_9,
       numder_2_1_out_11, numder_2_1_out_12, numder_2_1_out_13, numder_2_2_out_5, numder_2_2_out_6,
       numder_2_2_out_7, numder_2_2_out_9, numder_2_2_out_11, numder_2_2_out_12, numder_2_2_out_13,
       numder_2_3_out_5, numder_2_3_out_6, numder_2_3_out_7, numder_2_3_out_9, numder_2_3_out_11,
       numder_2_3_out_12, numder_2_3_out_13, numder_2_4_out_5, numder_2_4_out_6, numder_2_4_out_7,
       numder_2_4_out_9, numder_2_4_out_11, numder_2_4_out_12, numder_2_4_out_13, numder_2_5_out_5,
       numder_2_5_out_6, numder_2_5_out_7, numder_2_5_out_9, numder_2_5_out_11, numder_2_5_out_12,
       numder_2_5_out_13, numder_2_6_out_5, numder_2_6_out_6, numder_2_6_out_7, numder_2_6_out_9,
       numder_2_6_out_11, numder_2_6_out_12, numder_2_6_out_13, numder_2_7_out_5, numder_2_7_out_6,
       numder_2_7_out_7, numder_2_7_out_9, numder_2_7_out_11, numder_2_7_out_12, numder_2_7_out_13,
       numder_2_8_out_5, numder_2_8_out_6, numder_2_8_out_7, numder_2_8_out_9, numder_2_8_out_11,
       numder_2_8_out_12, numder_2_8_out_13, numder_2_9_out_5, numder_2_9_out_6, numder_2_9_out_7,
       numder_2_9_out_9, numder_2_9_out_11, numder_2_9_out_12, numder_2_9_out_13, numder_2_10_out_5,
       numder_2_10_out_6, numder_2_10_out_7, numder_2_10_out_9, numder_2_10_out_11, numder_2_10_out_12,
       numder_2_10_out_13, numders_1_out_3, numders_1_out_4, numders_1_out_5, numders_1_out_6,
       numders_1_out_7, numders_1_out_8, numders_1_out_9, numders_1_out_10, numders_1_out_11,
       numders_1_out_12, numders_1_out_13;
  wire [5:0] b_exzit_1, b_exzit_2, b_exzit_3, b_exzit_4, b_exzit_5, controlled_buffer_8_out, inc_1_out_2,
       o_exzit_1, o_exzit_2, o_exzit_3, o_exzit_4, o_exzit_5, undriven;
  wire [9:0] undriven_2;
  wire [14:0] haight_1_out_3, haight_1_out_4, haight_1_out_5, haight_1_out_6, haight_1_out_7, haight_1_out_8,
       haight_1_out_9, haight_1_out_10, haight_1_out_11, weight_1_out_3, weight_1_out_4, weight_1_out_5,
       weight_1_out_6, weight_1_out_7, weight_1_out_8, weight_1_out_9, weight_1_out_10, weight_1_out_11;
  wire [15:4] controlled_buffer_1_out;

  input_shifter input_shifter_1 (
    .MOSI(in_2), .CLK(in_1), .Reset(button_1_out), .Data_out(out_5), .buffer_ptr(input_shifter_1_buffer_ptr));
  Button button_1 (.out(button_1_out));
  assign {controlled_buffer_1_out, xx, yy} = comparator_1_eq ? out_5 : 16'bz;  // Controlled_Buffer controlled_buffer_1
  Comparator #(.width(4)) comparator_1 (
    .a(input_shifter_1_buffer_ptr), .b(4'b0101), .eq(comparator_1_eq));  // open: gt, lt
  Pull_Resistor pull_resistor_1 (.node({controlled_buffer_1_out, xx, yy}));
  not not_1 (not_1_out, controlled_buffer_1_out[4]);
  assign controlled_buffer_2_out = not_1_out ? yy : 2'bz;  // Controlled_Buffer controlled_buffer_2
  // Probe on controlled_buffer_2_out
  Pull_Resistor pull_resistor_2 (.node(controlled_buffer_2_out));
  // Probe on pull_resistor_3_node
  Pull_Resistor pull_resistor_3 (.node(pull_resistor_3_node));
  assign pull_resistor_3_node = not_1_out ? xx : 2'bz;  // Controlled_Buffer controlled_buffer_3
  inc inc_1 (.in_1(controlled_buffer_2_out), .out_2(inc_1_out_2[2:0]));
  inc inc_2 (.in_1(pull_resistor_3_node), .out_2(inc_1_out_2[5:3]));
  and and_1 (Soh_prime, controlled_buffer_1_out[4], yy[1], ~xx[1], yy[0], ~xx[0]);  // AND_Gate
  and and_2 (and_2_out, xx[0], controlled_buffer_1_out[4]);
  // OR_Gate or_1 has open pins: in0=inc_1_out_2[0], in1=inc_1_out_2[1], in2=inc_1_out_2[2], out=open
  and and_3 (rst, ~yy[0], ~yy[1], ~xx[0], ~xx[1], controlled_buffer_1_out[4]);  // AND_Gate
  DotMatrix #(.matrixcols(9), .matrixrows(15)) dotmatrix_1 (
    .col0(weight_1_out_3), .col1(weight_1_out_4), .col2(weight_1_out_5), .col3(weight_1_out_6),
    .col4(weight_1_out_7), .col5(weight_1_out_8), .col6(weight_1_out_9), .col7(weight_1_out_10),
    .col8(weight_1_out_11));
  Weight weight_1 (
    .new_task(and_2_out), .out_3(weight_1_out_3), .out_4(weight_1_out_4), .out_5(weight_1_out_5),
    .out_6(weight_1_out_6), .out_7(weight_1_out_7), .out_8(weight_1_out_8), .out_9(weight_1_out_9),
    .out_10(weight_1_out_10), .out_11(weight_1_out_11), .out_2(weight_1_out_2));
  // Probe on inc_1_out_2
  // Probe on weight_1_out_2
  assign controlled_buffer_4_out = Who[0] ? Soh_prime : 1'bz;  // Controlled_Buffer controlled_buffer_4
  assign controlled_buffer_5_out = Who[1] ? Soh_prime : 1'bz;  // Controlled_Buffer controlled_buffer_5
  Comparator #(.width(6)) comparator_2 (.a(o_exzit_1), .b(inc_1_out_2), .eq(comparator_2_eq[0]));  // open: gt, lt
  or or_2 (or_2_out, w_1o[0], w_1o[1], w_1o[2]);
  DotMatrix #(.matrixcols(9), .matrixrows(15)) dotmatrix_2 (
    .col0(haight_1_out_3), .col1(haight_1_out_4), .col2(haight_1_out_5), .col3(haight_1_out_6),
    .col4(haight_1_out_7), .col5(haight_1_out_8), .col6(haight_1_out_9), .col7(haight_1_out_10),
    .col8(haight_1_out_11));
  Haight haight_1 (
    .new_task(and_2_out), .out_3(haight_1_out_3), .out_4(haight_1_out_4), .out_5(haight_1_out_5),
    .out_6(haight_1_out_6), .out_7(haight_1_out_7), .out_8(haight_1_out_8), .out_9(haight_1_out_9),
    .out_10(haight_1_out_10), .out_11(haight_1_out_11), .out_2(haight_1_out_2));
  inc inc_3 (.in_1(weight_1_out_2), .out_2(inc_3_out_2));
  Pull_Resistor pull_resistor_4 (.node(controlled_buffer_4_out));
  Pull_Resistor pull_resistor_5 (.node(controlled_buffer_5_out));
  Comparator #(.width(6)) comparator_3 (.a(b_exzit_1), .b(undriven), .eq(rst_6));  // open: gt, lt
  not not_2 (not_2_out, or_2_out);
  assign w_1o = controlled_buffer_4_out ? inc_3_out_2 : 3'bz;  // Controlled_Buffer controlled_buffer_6
  // Probe on haight_1_out_2
  and and_4 (kj, not_2_out, or_2_out);
  Pull_Resistor pull_resistor_6 (.node(h_1o));
  Pull_Resistor pull_resistor_7 (.node(w_1o));
  inc inc_4 (.in_1(haight_1_out_2), .out_2(inc_4_out_2));
  assign w_1b = controlled_buffer_5_out ? inc_3_out_2 : 3'bz;  // Controlled_Buffer controlled_buffer_7
  assign controlled_buffer_8_out = rst_1 ? o_exzit_1 : 6'bz;  // Controlled_Buffer controlled_buffer_8
  Pull_Resistor pull_resistor_8 (.node(w_1b));
  assign h_1o = controlled_buffer_4_out ? inc_4_out_2 : 3'bz;  // Controlled_Buffer controlled_buffer_9
  assign h_1b = controlled_buffer_5_out ? inc_4_out_2 : 3'bz;  // Controlled_Buffer controlled_buffer_10
  and and_5 (comparator_2_eq[1], ~comparator_2_eq[0], comparator_4_eq);  // AND_Gate
  Comparator #(.width(6)) comparator_4 (.a(o_exzit_2), .b(inc_1_out_2), .eq(comparator_4_eq));  // open: gt, lt
  or or_3 (or_3_out, w_1b[0], w_1b[1], w_1b[2]);
  Pull_Resistor pull_resistor_9 (.node(h_1b));
  Pull_Resistor pull_resistor_10 (.node({rst_5, rst_4, rst_3, rst_2, rst_1}));
  not not_3 (not_3_out, or_3_out);
  and and_6 (and_6_out, kj, ~_1_o);  // AND_Gate
  and and_7 (and_7_out, jk, ~_1_b);  // AND_Gate
  Comparator #(.width(6)) comparator_5 (.a(b_exzit_2), .b(undriven), .eq(rst_7));  // open: gt, lt
  and and_8 (jk, not_3_out, or_3_out);
  DotMatrix #(.matrixcols(7), .matrixrows(5)) dotmatrix_3 (
    .col0(numder_2_1_out_5), .col1(numder_2_1_out_6), .col2(numder_2_1_out_7), .col3(numder_2_1_out_9),
    .col4(numder_2_1_out_11), .col5(numder_2_1_out_12), .col6(numder_2_1_out_13));
  numder_2 numder_2_1 (
    .in_1(w_1o), .out_5(numder_2_1_out_5), .out_6(numder_2_1_out_6), .out_7(numder_2_1_out_7),
    .out_9(numder_2_1_out_9), .out_11(numder_2_1_out_11), .in_2(h_1o), .out_12(numder_2_1_out_12),
    .out_13(numder_2_1_out_13), .out_8(_1_o), .in_3(and_6_out), .rst(or_4_out), .out_10(o_exzit_1));
  or or_4 (or_4_out, rst, rst_1);
  DotMatrix #(.matrixcols(7), .matrixrows(5)) dotmatrix_4 (
    .col0(numder_2_2_out_5), .col1(numder_2_2_out_6), .col2(numder_2_2_out_7), .col3(numder_2_2_out_9),
    .col4(numder_2_2_out_11), .col5(numder_2_2_out_12), .col6(numder_2_2_out_13));
  numder_2 numder_2_2 (
    .in_1(w_1b), .out_5(numder_2_2_out_5), .out_6(numder_2_2_out_6), .out_7(numder_2_2_out_7),
    .out_9(numder_2_2_out_9), .out_11(numder_2_2_out_11), .in_2(h_1b), .out_12(numder_2_2_out_12),
    .out_13(numder_2_2_out_13), .out_8(_1_b), .in_3(and_7_out), .rst(or_5_out), .out_10(b_exzit_1));
  or or_5 (or_5_out, rst, rst_6);
  assign {rst_5, rst_4, rst_3, rst_2, rst_1} = and_14_out ? comparator_2_eq : 5'bz;  // Controlled_Buffer controlled_buffer_11
  not not_4 (not_4_out, in_1);
  and and_9 (comparator_2_eq[2], ~comparator_2_eq[0], ~comparator_4_eq, comparator_6_eq);  // AND_Gate
  Comparator #(.width(6)) comparator_6 (.a(o_exzit_3), .b(inc_1_out_2), .eq(comparator_6_eq));  // open: gt, lt
  and and_10 (and_10_out, _1_o, ~_2_o);  // AND_Gate
  and and_11 (and_11_out, jk, and_12_out);
  and and_12 (and_12_out, _1_b, ~_2_b);  // AND_Gate
  Comparator #(.width(6)) comparator_7 (.a(b_exzit_3), .b(undriven), .eq(rst_8));  // open: gt, lt
  DotMatrix #(.matrixcols(7), .matrixrows(5)) dotmatrix_5 (
    .col0(numder_2_3_out_5), .col1(numder_2_3_out_6), .col2(numder_2_3_out_7), .col3(numder_2_3_out_9),
    .col4(numder_2_3_out_11), .col5(numder_2_3_out_12), .col6(numder_2_3_out_13));
  numder_2 numder_2_3 (
    .in_1(w_1o), .out_5(numder_2_3_out_5), .out_6(numder_2_3_out_6), .out_7(numder_2_3_out_7),
    .out_9(numder_2_3_out_9), .out_11(numder_2_3_out_11), .in_2(h_1o), .out_12(numder_2_3_out_12),
    .out_13(numder_2_3_out_13), .out_8(_2_o), .in_3(and_13_out), .rst(or_6_out), .out_10(o_exzit_2));
  and and_13 (and_13_out, kj, and_10_out);
  or or_6 (or_6_out, rst, rst_2);
  DotMatrix #(.matrixcols(7), .matrixrows(5)) dotmatrix_6 (
    .col0(numder_2_4_out_5), .col1(numder_2_4_out_6), .col2(numder_2_4_out_7), .col3(numder_2_4_out_9),
    .col4(numder_2_4_out_11), .col5(numder_2_4_out_12), .col6(numder_2_4_out_13));
  numder_2 numder_2_4 (
    .in_1(w_1b), .out_5(numder_2_4_out_5), .out_6(numder_2_4_out_6), .out_7(numder_2_4_out_7),
    .out_9(numder_2_4_out_9), .out_11(numder_2_4_out_11), .in_2(h_1b), .out_12(numder_2_4_out_12),
    .out_13(numder_2_4_out_13), .out_8(_2_b), .in_3(and_11_out), .rst(or_7_out), .out_10(b_exzit_2));
  or or_7 (or_7_out, rst, rst_7);
  and and_14 (and_14_out, ~not_4_out, ~in_1);  // AND_Gate
  and and_15 (comparator_2_eq[3], ~comparator_2_eq[0], ~comparator_4_eq, ~comparator_6_eq, comparator_8_eq);  // AND_Gate
  Comparator #(.width(6)) comparator_8 (.a(o_exzit_4), .b(inc_1_out_2), .eq(comparator_8_eq));  // open: gt, lt
  and and_16 (and_16_out, _1_o, _2_o, ~_3_o);  // AND_Gate
  and and_17 (and_17_out, _1_b, _2_b, ~_3_b);  // AND_Gate
  and and_18 (and_18_out, kj, and_16_out);
  or or_8 (or_8_out, rst, rst_3);
  DotMatrix #(.matrixcols(7), .matrixrows(5)) dotmatrix_7 (
    .col0(numder_2_5_out_5), .col1(numder_2_5_out_6), .col2(numder_2_5_out_7), .col3(numder_2_5_out_9),
    .col4(numder_2_5_out_11), .col5(numder_2_5_out_12), .col6(numder_2_5_out_13));
  numder_2 numder_2_5 (
    .in_1(w_1b), .out_5(numder_2_5_out_5), .out_6(numder_2_5_out_6), .out_7(numder_2_5_out_7),
    .out_9(numder_2_5_out_9), .out_11(numder_2_5_out_11), .in_2(h_1b), .out_12(numder_2_5_out_12),
    .out_13(numder_2_5_out_13), .out_8(_3_b), .in_3(and_19_out), .rst(or_9_out), .out_10(b_exzit_3));
  and and_19 (and_19_out, jk, and_17_out);
  or or_9 (or_9_out, rst, rst_8);
  Comparator #(.width(6)) comparator_9 (.a(b_exzit_4), .b(undriven), .eq(rst_9));  // open: gt, lt
  DotMatrix #(.matrixcols(7), .matrixrows(5)) dotmatrix_8 (
    .col0(numder_2_6_out_5), .col1(numder_2_6_out_6), .col2(numder_2_6_out_7), .col3(numder_2_6_out_9),
    .col4(numder_2_6_out_11), .col5(numder_2_6_out_12), .col6(numder_2_6_out_13));
  numder_2 numder_2_6 (
    .in_1(w_1o), .out_5(numder_2_6_out_5), .out_6(numder_2_6_out_6), .out_7(numder_2_6_out_7),
    .out_9(numder_2_6_out_9), .out_11(numder_2_6_out_11), .in_2(h_1o), .out_12(numder_2_6_out_12),
    .out_13(numder_2_6_out_13), .out_8(_3_o), .in_3(and_18_out), .rst(or_8_out), .out_10(o_exzit_3));
  and and_20 (and_20_out, _1_o, _2_o, _3_o, ~_4_o);  // AND_Gate
  and and_21 (and_21_out, _1_b, _2_b, _3_b, ~_4_b);  // AND_Gate
  DotMatrix #(.matrixcols(7), .matrixrows(5)) dotmatrix_9 (
    .col0(numder_2_7_out_5), .col1(numder_2_7_out_6), .col2(numder_2_7_out_7), .col3(numder_2_7_out_9),
    .col4(numder_2_7_out_11), .col5(numder_2_7_out_12), .col6(numder_2_7_out_13));
  numder_2 numder_2_7 (
    .in_1(w_1o), .out_5(numder_2_7_out_5), .out_6(numder_2_7_out_6), .out_7(numder_2_7_out_7),
    .out_9(numder_2_7_out_9), .out_11(numder_2_7_out_11), .in_2(h_1o), .out_12(numder_2_7_out_12),
    .out_13(numder_2_7_out_13), .out_8(_4_o), .in_3(and_22_out), .rst(or_10_out), .out_10(o_exzit_4));
  and and_22 (and_22_out, kj, and_20_out);
  or or_10 (or_10_out, rst, rst_4);
  DotMatrix #(.matrixcols(7), .matrixrows(5)) dotmatrix_10 (
    .col0(numder_2_8_out_5), .col1(numder_2_8_out_6), .col2(numder_2_8_out_7), .col3(numder_2_8_out_9),
    .col4(numder_2_8_out_11), .col5(numder_2_8_out_12), .col6(numder_2_8_out_13));
  numder_2 numder_2_8 (
    .in_1(w_1b), .out_5(numder_2_8_out_5), .out_6(numder_2_8_out_6), .out_7(numder_2_8_out_7),
    .out_9(numder_2_8_out_9), .out_11(numder_2_8_out_11), .in_2(h_1b), .out_12(numder_2_8_out_12),
    .out_13(numder_2_8_out_13), .out_8(_4_b), .in_3(and_23_out), .rst(or_11_out), .out_10(b_exzit_4));
  and and_23 (and_23_out, jk, and_21_out);
  or or_11 (or_11_out, rst, rst_9);
  and and_24 (comparator_2_eq[4], ~comparator_2_eq[0], ~comparator_4_eq, ~comparator_6_eq, ~comparator_8_eq, out_7);  // AND_Gate
  Comparator #(.width(6)) comparator_10 (.a(o_exzit_5), .b(inc_1_out_2), .eq(out_7));  // open: gt, lt
  and and_25 (and_25_out, _1_b, _2_b, _3_b, _4_b, ~_5_b);  // AND_Gate
  Comparator #(.width(6)) comparator_11 (.a(b_exzit_5), .b(undriven), .eq(rst_10));  // open: gt, lt
  and and_26 (and_26_out, _1_o, _2_o, _3_o, _4_o, ~_5_o);  // AND_Gate
  and and_27 (and_27_out, jk, and_25_out);
  or or_12 (or_12_out, rst, rst_10);
  and and_28 (and_28_out, kj, and_26_out);
  or or_13 (or_13_out, rst, rst_5);
  DotMatrix #(.matrixcols(7), .matrixrows(5)) dotmatrix_11 (
    .col0(numder_2_9_out_5), .col1(numder_2_9_out_6), .col2(numder_2_9_out_7), .col3(numder_2_9_out_9),
    .col4(numder_2_9_out_11), .col5(numder_2_9_out_12), .col6(numder_2_9_out_13));
  numder_2 numder_2_9 (
    .in_1(w_1b), .out_5(numder_2_9_out_5), .out_6(numder_2_9_out_6), .out_7(numder_2_9_out_7),
    .out_9(numder_2_9_out_9), .out_11(numder_2_9_out_11), .in_2(h_1b), .out_12(numder_2_9_out_12),
    .out_13(numder_2_9_out_13), .out_8(_5_b), .in_3(and_27_out), .rst(or_12_out), .out_10(b_exzit_5));
  DotMatrix #(.matrixcols(7), .matrixrows(5)) dotmatrix_12 (
    .col0(numder_2_10_out_5), .col1(numder_2_10_out_6), .col2(numder_2_10_out_7), .col3(numder_2_10_out_9),
    .col4(numder_2_10_out_11), .col5(numder_2_10_out_12), .col6(numder_2_10_out_13));
  numder_2 numder_2_10 (
    .in_1(w_1o), .out_5(numder_2_10_out_5), .out_6(numder_2_10_out_6), .out_7(numder_2_10_out_7),
    .out_9(numder_2_10_out_9), .out_11(numder_2_10_out_11), .in_2(h_1o), .out_12(numder_2_10_out_12),
    .out_13(numder_2_10_out_13), .out_8(_5_o), .in_3(and_28_out), .rst(or_13_out), .out_10(o_exzit_5));
  and and_29 (and_29_out, _1_b, _2_b, _3_b, _4_b, _5_b);
  and and_30 (and_30_out, _1_o, _2_o, _3_o, _4_o, _5_o);
  and and_31 (err, kj, and_30_out);
  and and_32 (err_2, kj, and_29_out);
  DotMatrix #(.matrixcols(11), .matrixrows(5)) dotmatrix_13 (
    .col0(numders_1_out_3), .col1(numders_1_out_4), .col2(numders_1_out_5), .col3(numders_1_out_6),
    .col4(numders_1_out_7), .col5(numders_1_out_8), .col6(numders_1_out_9), .col7(numders_1_out_10),
    .col8(numders_1_out_11), .col9(numders_1_out_12), .col10(numders_1_out_13));
  Numders numders_1 (
    .Energy(undriven_2), .in_2(1'b0), .out_3(numders_1_out_3), .out_4(numders_1_out_4),
    .out_5(numders_1_out_5), .out_6(numders_1_out_6), .out_7(numders_1_out_7), .out_8(numders_1_out_8),
    .out_9(numders_1_out_9), .out_10(numders_1_out_10), .out_11(numders_1_out_11), .out_12(numders_1_out_12),
    .out_13(numders_1_out_13));
  Register #(.width(10)) register_1 (.D(undriven_2), .clr(undriven_3));  // open: en, Q, clk
  // Probe on nothing

  // Other names for the same wires on the sheet: clk = in_1; or = Who[0]; blue = Who[1]
endmodule

module Weight (
  input  new_task,
  output [1:0] out_2,
  output [14:0] out_3,
  output [14:0] out_4,
  output [14:0] out_5,
  output [14:0] out_6,
  output [14:0] out_7,
  output [14:0] out_8,
  output [14:0] out_9,
  output [14:0] out_10,
  output [14:0] out_11
);

  wire [2:0] inc_1_out_2;

  Random #(.width(2), .seed(1)) random_1 (.clk(new_task), .out(out_2));  // open: next, clr
  // Probe on inc_1_out_2
  display_controller_inc inc_1 (.in_1(out_2), .out_2(inc_1_out_2));
  DotMatrix #(.matrixcols(9), .matrixrows(15)) dotmatrix_1 (
    .col0(out_3), .col1(out_3), .col2(out_3), .col3(out_6), .col4(out_6), .col5(out_6), .col6(out_9),
    .col7(out_9), .col8(out_9));
  Big_col_1 big_col_1_1 (
    .Zero(new_task), .D(1'b0), .C(inc_1_out_2[2]), .B(inc_1_out_2[1]), .A(inc_1_out_2[0]), .out_7(out_3),
    .Inversion(1'b0));
  Big_col_2 big_col_2_1 (
    .Zero(new_task), .D(1'b0), .C(inc_1_out_2[2]), .B(inc_1_out_2[1]), .A(inc_1_out_2[0]), .out_7(out_6),
    .Inversion(1'b0));
  Big_col_3 big_col_3_1 (
    .Zero(new_task), .D(1'b0), .C(inc_1_out_2[2]), .B(inc_1_out_2[1]), .A(inc_1_out_2[0]), .out_7(out_9),
    .Inversion(1'b0));

  assign out_4 = out_3;
  assign out_5 = out_3;
  assign out_7 = out_6;
  assign out_8 = out_6;
  assign out_10 = out_9;
  assign out_11 = out_9;
endmodule

module Haight (
  input  new_task,
  output [1:0] out_2,
  output [14:0] out_3,
  output [14:0] out_4,
  output [14:0] out_5,
  output [14:0] out_6,
  output [14:0] out_7,
  output [14:0] out_8,
  output [14:0] out_9,
  output [14:0] out_10,
  output [14:0] out_11
);

  wire [2:0] inc_1_out_2;

  Random #(.width(2)) random_1 (.clk(new_task), .out(out_2));  // open: next, clr
  display_controller_inc inc_1 (.in_1(out_2), .out_2(inc_1_out_2));
  // Probe on inc_1_out_2
  DotMatrix #(.matrixcols(9), .matrixrows(15)) dotmatrix_1 (
    .col0(out_3), .col1(out_3), .col2(out_3), .col3(out_6), .col4(out_6), .col5(out_6), .col6(out_9),
    .col7(out_9), .col8(out_9));
  Big_col_1 big_col_1_1 (
    .Zero(new_task), .D(1'b0), .C(inc_1_out_2[2]), .B(inc_1_out_2[1]), .A(inc_1_out_2[0]), .out_7(out_3),
    .Inversion(1'b0));
  Big_col_2 big_col_2_1 (
    .Zero(new_task), .D(1'b0), .C(inc_1_out_2[2]), .B(inc_1_out_2[1]), .A(inc_1_out_2[0]), .out_7(out_6),
    .Inversion(1'b0));
  Big_col_3 big_col_3_1 (
    .Zero(new_task), .D(1'b0), .C(inc_1_out_2[2]), .B(inc_1_out_2[1]), .A(inc_1_out_2[0]), .out_7(out_9),
    .Inversion(1'b0));

  assign out_4 = out_3;
  assign out_5 = out_3;
  assign out_7 = out_6;
  assign out_8 = out_6;
  assign out_10 = out_9;
  assign out_11 = out_9;
endmodule

module numder_2 (
  input  [2:0] in_1,
  input  [2:0] in_2,
  input  in_3,
  input  rst,
  output [4:0] out_5,
  output [4:0] out_6,
  output [4:0] out_7,
  output out_8,
  output [4:0] out_9,
  output [5:0] out_10,
  output [4:0] out_11,
  output [4:0] out_12,
  output [4:0] out_13
);

  wire and_1_out, nor_1_out, nor_2_out;
  wire [4:0] col_1_1_e, col_1_2_e, col_2_1_e, col_2_2_e, col_3_1_e, col_3_2_e;

  // Probe on {in_1, in_2}
  and and_1 (and_1_out, in_3, ~out_8);  // AND_Gate
  Register #(.width(6)) register_1 (.D({in_1, in_2}), .Q(out_10), .clk(and_1_out), .clr(rst));  // open: en
  Comparator #(.width(6), .mode("unsigned")) comparator_1 (.a(out_10), .b({6{1'b0}}), .gt(out_8));  // open: eq, lt
  nor nor_1 (nor_1_out, out_10[3], out_10[4], out_10[5]);
  Col_1 col_1_1 (
    .D(1'b0), .C(out_10[5]), .B(out_10[4]), .A(out_10[3]), .e(col_1_1_e[0]), .d_2(col_1_1_e[1]),
    .c_2(col_1_1_e[2]), .b_2(col_1_1_e[3]), .a_2(col_1_1_e[4]));
  Col_2 col_2_1 (
    .D(1'b0), .C(out_10[5]), .B(out_10[4]), .A(out_10[3]), .e(col_2_1_e[0]), .d_2(col_2_1_e[1]),
    .c_2(col_2_1_e[2]), .b_2(col_2_1_e[3]), .a_2(col_2_1_e[4]));
  Col_3 col_3_1 (
    .D(1'b0), .C(out_10[5]), .B(out_10[4]), .A(out_10[3]), .e(col_3_1_e[0]), .d_2(col_3_1_e[1]),
    .c_2(col_3_1_e[2]), .b_2(col_3_1_e[3]), .a_2(col_3_1_e[4]));
  nor nor_2 (nor_2_out, out_10[0], out_10[1], out_10[2]);
  Transistor #(.\type ("n"), .width(5)) transistor_1 (.in({5{1'b0}}), .out(out_5), .gate(nor_1_out));
  Transistor #(.\type ("n"), .width(5)) transistor_2 (.in({5{1'b0}}), .out(out_6), .gate(nor_1_out));
  Transistor #(.\type ("n"), .width(5)) transistor_3 (.in({5{1'b0}}), .out(out_7), .gate(nor_1_out));
  Col_1 col_1_2 (
    .D(1'b0), .C(out_10[2]), .B(out_10[1]), .A(out_10[0]), .e(col_1_2_e[0]), .d_2(col_1_2_e[1]),
    .c_2(col_1_2_e[2]), .b_2(col_1_2_e[3]), .a_2(col_1_2_e[4]));
  Col_2 col_2_2 (
    .D(1'b0), .C(out_10[2]), .B(out_10[1]), .A(out_10[0]), .e(col_2_2_e[0]), .d_2(col_2_2_e[1]),
    .c_2(col_2_2_e[2]), .b_2(col_2_2_e[3]), .a_2(col_2_2_e[4]));
  Col_3 col_3_2 (
    .D(1'b0), .C(out_10[2]), .B(out_10[1]), .A(out_10[0]), .e(col_3_2_e[0]), .d_2(col_3_2_e[1]),
    .c_2(col_3_2_e[2]), .b_2(col_3_2_e[3]), .a_2(col_3_2_e[4]));
  DotMatrix #(.matrixcols(3), .matrixrows(5)) dotmatrix_1 (.col0(out_5), .col1(out_6), .col2(out_7));
  Transistor #(.width(5)) transistor_4 (.in(col_1_1_e), .out(out_5), .gate(nor_1_out));
  Transistor #(.width(5)) transistor_5 (.in(col_2_1_e), .out(out_6), .gate(nor_1_out));
  Transistor #(.width(5)) transistor_6 (.in(col_3_1_e), .out(out_7), .gate(nor_1_out));
  Transistor #(.\type ("n"), .width(5)) transistor_7 (.in({5{1'b0}}), .out(out_11), .gate(nor_2_out));
  Transistor #(.\type ("n"), .width(5)) transistor_8 (.in({5{1'b0}}), .out(out_12), .gate(nor_2_out));
  Transistor #(.\type ("n"), .width(5)) transistor_9 (.in({5{1'b0}}), .out(out_13), .gate(nor_2_out));
  DotMatrix #(.matrixcols(3), .matrixrows(5)) dotmatrix_2 (.col0(out_11), .col1(out_12), .col2(out_13));
  Transistor #(.width(5)) transistor_10 (.in(col_1_2_e), .out(out_11), .gate(nor_2_out));
  Transistor #(.width(5)) transistor_11 (.in(col_2_2_e), .out(out_12), .gate(nor_2_out));
  Transistor #(.width(5)) transistor_12 (.in(col_3_2_e), .out(out_13), .gate(nor_2_out));

  assign out_9 = {5{1'b0}};
endmodule

module inc (
  input  [1:0] in_1,
  output [2:0] out_2
);

  wire [0:0] and_1_out;

  assign {out_2[2], and_1_out[0]} = {and_1_out[0], 1'b1} & in_1;  // AND_Gate and_1, 2 bits wide
  assign out_2[1:0] = in_1 ^ {and_1_out[0], 1'b1};  // XOR_Gate xor_1, 2 bits wide
endmodule
